// Logisim project design_cpu_logisim.circ as structural Verilog: 20 circuits, main circuit main
module main (
  input  a,
  input  b,
  output o
);

  wire not_1_out;

  not not_1 (not_1_out, b);
  or or_1 (o, not_1_out, a);
endmodule

module CPU_MEM_1 (
  input  i,
  input  s,
  output o
);

  wire nand_1_out, nand_2_out, nand_4_out;

  nand nand_1 (nand_1_out, i, s);
  nand nand_2 (nand_2_out, nand_1_out, s);
  nand nand_3 (o, nand_1_out, nand_4_out);
  nand nand_4 (nand_4_out, o, nand_2_out);
endmodule

module CPU_MEM_8 (
  input  [7:0] i,
  input  s,
  output [7:0] o
);

  CPU_MEM_1 cpu_mem_1_1 (.i(i[0]), .s(s), .o(o[0]));
  CPU_MEM_1 cpu_mem_1_2 (.i(i[1]), .s(s), .o(o[1]));
  CPU_MEM_1 cpu_mem_1_3 (.i(i[2]), .s(s), .o(o[2]));
  CPU_MEM_1 cpu_mem_1_4 (.i(i[3]), .s(s), .o(o[3]));
  CPU_MEM_1 cpu_mem_1_5 (.i(i[4]), .s(s), .o(o[4]));
  CPU_MEM_1 cpu_mem_1_6 (.i(i[5]), .s(s), .o(o[5]));
  CPU_MEM_1 cpu_mem_1_7 (.i(i[6]), .s(s), .o(o[6]));
  CPU_MEM_1 cpu_mem_1_8 (.i(i[7]), .s(s), .o(o[7]));
endmodule

module CPU_ENABLE_8 (
  input  [7:0] i,
  input  e,
  output [7:0] o
);

  wire and_1_out, and_2_out, and_3_out, and_4_out, and_5_out, and_6_out, and_7_out, and_8_out;

  and and_1 (and_1_out, i[0], e);
  and and_2 (and_2_out, i[1], e);
  and and_3 (and_3_out, i[2], e);
  and and_4 (and_4_out, i[3], e);
  and and_5 (and_5_out, i[4], e);
  and and_6 (and_6_out, i[5], e);
  and and_7 (and_7_out, i[6], e);
  and and_8 (and_8_out, i[7], e);
  assign o[0] = e ? and_1_out : 1'bz;  // Controlled_Buffer controlled_buffer_1
  assign o[1] = e ? and_2_out : 1'bz;  // Controlled_Buffer controlled_buffer_2
  assign o[2] = e ? and_3_out : 1'bz;  // Controlled_Buffer controlled_buffer_3
  assign o[3] = e ? and_4_out : 1'bz;  // Controlled_Buffer controlled_buffer_4
  assign o[4] = e ? and_5_out : 1'bz;  // Controlled_Buffer controlled_buffer_5
  assign o[5] = e ? and_6_out : 1'bz;  // Controlled_Buffer controlled_buffer_6
  assign o[6] = e ? and_7_out : 1'bz;  // Controlled_Buffer controlled_buffer_7
  assign o[7] = e ? and_8_out : 1'bz;  // Controlled_Buffer controlled_buffer_8
endmodule

module CPU_REG_8 (
  input  [7:0] i,
  input  s,
  input  e,
  output [7:0] r,
  output [7:0] o
);

  wire [7:0] cpu_enable_8_1_o;

  CPU_MEM_8 cpu_mem_8_1 (.i(i), .s(s), .o(r));
  CPU_ENABLE_8 cpu_enable_8_1 (.o(cpu_enable_8_1_o));  // open: i, e
  assign o = e ? cpu_enable_8_1_o : 8'bz;  // Controlled_Buffer controlled_buffer_1
endmodule

module CPU_DECODER_3x8 (
  input  a,
  input  b,
  input  c,
  output o1,
  output o2,
  output o3,
  output o4,
  output o5,
  output o6,
  output o7,
  output o8
);

  wire not_1_out, not_2_out, not_3_out;

  not not_1 (not_1_out, a);
  not not_2 (not_2_out, b);
  not not_3 (not_3_out, c);
  and and_1 (o1, not_1_out, not_2_out, not_3_out);
  and and_2 (o2, not_1_out, not_2_out, c);
  and and_3 (o3, not_1_out, b, not_3_out);
  and and_4 (o4, not_1_out, b, c);
  and and_5 (o5, a, not_2_out, not_3_out);
  and and_6 (o6, a, not_2_out, c);
  and and_7 (o7, a, b, not_3_out);
  and and_8 (o8, a, b, c);
endmodule

module CPU_DECODER_4x16 (
  input  [3:0] i,
  output o1,
  output o2,
  output o3,
  output o4,
  output o5,
  output o6,
  output o7,
  output o8,
  output o9,
  output o10,
  output o11,
  output o12,
  output o13,
  output o14,
  output o15,
  output o16
);

  wire not_1_out, not_2_out, not_3_out, not_4_out;

  not not_1 (not_1_out, i[3]);
  not not_2 (not_2_out, i[2]);
  not not_3 (not_3_out, i[1]);
  not not_4 (not_4_out, i[0]);
  and and_1 (o1, not_1_out, not_2_out, not_3_out, not_4_out);
  and and_2 (o2, not_1_out, not_2_out, not_3_out, i[0]);
  and and_3 (o3, not_1_out, not_2_out, i[1], not_4_out);
  and and_4 (o4, not_1_out, not_2_out, i[1], i[0]);
  and and_5 (o5, not_1_out, i[2], not_3_out, not_4_out);
  and and_6 (o6, not_1_out, i[2], not_3_out, i[0]);
  and and_7 (o7, not_1_out, i[2], i[1], not_4_out);
  and and_8 (o8, not_1_out, i[2], i[1], i[0]);
  and and_9 (o9, i[3], not_2_out, not_3_out, not_4_out);
  and and_10 (o10, i[3], not_2_out, not_3_out, i[0]);
  and and_11 (o11, i[3], not_2_out, i[1], not_4_out);
  and and_12 (o12, i[3], not_2_out, i[1], i[0]);
  and and_13 (o13, i[3], i[2], not_3_out, not_4_out);
  and and_14 (o14, i[3], i[2], not_3_out, i[0]);
  and and_15 (o15, i[3], i[2], i[1], not_4_out);
  and and_16 (o16, i[3], i[2], i[1], i[0]);
endmodule

module CPU_REG_BYTE (
  input  reset,
  input  [7:0] i,
  input  h,
  input  v,
  input  s,
  input  e,
  output [7:0] op,
  output [7:0] o
);

  wire and_1_out, and_2_out, and_3_out, or_1_out;
  wire [7:0] cpu_reg_8_1_o;

  and and_1 (and_1_out, h, v);
  and and_2 (and_2_out, and_1_out, s);
  and and_3 (and_3_out, and_1_out, e);
  or or_1 (or_1_out, reset, and_2_out);
  CPU_REG_8 cpu_reg_8_1 (.i(i), .s(or_1_out), .e(and_3_out), .r(op), .o(cpu_reg_8_1_o));
  assign o = and_3_out ? cpu_reg_8_1_o : 8'bz;  // Controlled_Buffer controlled_buffer_1
endmodule

module CPU_RAM_256 (
  input  [7:0] i,
  input  sa,
  input  [7:0] adress,
  input  s,
  input  e,
  input  reset,
  output [7:0] o,
  output [7:0] out_8,
  output [7:0] out_9,
  output [7:0] out_10,
  output [7:0] out_11,
  output [7:0] out_12,
  output [7:0] out_13,
  output [7:0] out_14,
  output [7:0] out_15,
  output [7:0] out_16,
  output [7:0] out_17,
  output [7:0] out_18,
  output [7:0] out_19,
  output [7:0] out_20,
  output [7:0] out_21,
  output [7:0] out_22,
  output [7:0] out_23,
  output [7:0] out_24,
  output [7:0] out_25,
  output [7:0] out_26,
  output [7:0] out_27,
  output [7:0] out_28,
  output [7:0] out_29,
  output [7:0] out_30,
  output [7:0] out_31,
  output [7:0] out_32,
  output [7:0] out_33,
  output [7:0] out_34,
  output [7:0] out_35,
  output [7:0] out_36,
  output [7:0] out_37,
  output [7:0] out_38,
  output [7:0] out_39,
  output [7:0] out_40,
  output [7:0] out_41,
  output [7:0] out_42,
  output [7:0] out_43,
  output [7:0] out_44,
  output [7:0] out_45,
  output [7:0] out_46,
  output [7:0] out_47,
  output [7:0] out_48,
  output [7:0] out_49,
  output [7:0] out_50,
  output [7:0] out_51,
  output [7:0] out_52,
  output [7:0] out_53,
  output [7:0] out_54,
  output [7:0] out_55,
  output [7:0] out_56,
  output [7:0] out_57,
  output [7:0] out_58,
  output [7:0] out_59,
  output [7:0] out_60,
  output [7:0] out_61,
  output [7:0] out_62,
  output [7:0] out_63,
  output [7:0] out_64,
  output [7:0] out_65,
  output [7:0] out_66,
  output [7:0] out_67,
  output [7:0] out_68,
  output [7:0] out_69,
  output [7:0] out_70,
  output [7:0] out_71,
  output [7:0] out_72,
  output [7:0] out_73,
  output [7:0] out_74,
  output [7:0] out_75,
  output [7:0] out_76,
  output [7:0] out_77,
  output [7:0] out_78,
  output [7:0] out_79,
  output [7:0] out_80,
  output [7:0] out_81,
  output [7:0] out_82,
  output [7:0] out_83,
  output [7:0] out_84,
  output [7:0] out_85,
  output [7:0] out_86,
  output [7:0] out_87,
  output [7:0] out_88,
  output [7:0] out_89,
  output [7:0] out_90,
  output [7:0] out_91,
  output [7:0] out_92,
  output [7:0] out_93,
  output [7:0] out_94,
  output [7:0] out_95,
  output [7:0] out_96,
  output [7:0] out_97,
  output [7:0] out_98,
  output [7:0] out_99,
  output [7:0] out_100,
  output [7:0] out_101,
  output [7:0] out_102,
  output [7:0] out_103,
  output [7:0] out_104,
  output [7:0] out_105,
  output [7:0] out_106,
  output [7:0] out_107,
  output [7:0] out_108,
  output [7:0] out_109,
  output [7:0] out_110,
  output [7:0] out_111,
  output [7:0] out_112,
  output [7:0] out_113,
  output [7:0] out_114,
  output [7:0] out_115,
  output [7:0] out_116,
  output [7:0] out_117,
  output [7:0] out_118,
  output [7:0] out_119,
  output [7:0] out_120,
  output [7:0] out_121,
  output [7:0] out_122,
  output [7:0] out_123,
  output [7:0] out_124,
  output [7:0] out_125,
  output [7:0] out_126,
  output [7:0] out_127,
  output [7:0] out_128,
  output [7:0] out_129,
  output [7:0] out_130,
  output [7:0] out_131,
  output [7:0] out_132,
  output [7:0] out_133,
  output [7:0] out_134,
  output [7:0] out_135,
  output [7:0] out_136,
  output [7:0] out_137,
  output [7:0] out_138,
  output [7:0] out_139,
  output [7:0] out_140,
  output [7:0] out_141,
  output [7:0] out_142,
  output [7:0] out_143,
  output [7:0] out_144,
  output [7:0] out_145,
  output [7:0] out_146,
  output [7:0] out_147,
  output [7:0] out_148,
  output [7:0] out_149,
  output [7:0] out_150,
  output [7:0] out_151,
  output [7:0] out_152,
  output [7:0] out_153,
  output [7:0] out_154,
  output [7:0] out_155,
  output [7:0] out_156,
  output [7:0] out_157,
  output [7:0] out_158,
  output [7:0] out_159,
  output [7:0] out_160,
  output [7:0] out_161,
  output [7:0] out_162,
  output [7:0] out_163,
  output [7:0] out_164,
  output [7:0] out_165,
  output [7:0] out_166,
  output [7:0] out_167,
  output [7:0] out_168,
  output [7:0] out_169,
  output [7:0] out_170,
  output [7:0] out_171,
  output [7:0] out_172,
  output [7:0] out_173,
  output [7:0] out_174,
  output [7:0] out_175,
  output [7:0] out_176,
  output [7:0] out_177,
  output [7:0] out_178,
  output [7:0] out_179,
  output [7:0] out_180,
  output [7:0] out_181,
  output [7:0] out_182,
  output [7:0] out_183,
  output [7:0] out_184,
  output [7:0] out_185,
  output [7:0] out_186,
  output [7:0] out_187,
  output [7:0] out_188,
  output [7:0] out_189,
  output [7:0] out_190,
  output [7:0] out_191,
  output [7:0] out_192,
  output [7:0] out_193,
  output [7:0] out_194,
  output [7:0] out_195,
  output [7:0] out_196,
  output [7:0] out_197,
  output [7:0] out_198,
  output [7:0] out_199,
  output [7:0] out_200,
  output [7:0] out_201,
  output [7:0] out_202,
  output [7:0] out_203,
  output [7:0] out_204,
  output [7:0] out_205,
  output [7:0] out_206,
  output [7:0] out_207,
  output [7:0] out_208,
  output [7:0] out_209,
  output [7:0] out_210,
  output [7:0] out_211,
  output [7:0] out_212,
  output [7:0] out_213,
  output [7:0] out_214,
  output [7:0] out_215,
  output [7:0] out_216,
  output [7:0] out_217,
  output [7:0] out_218,
  output [7:0] out_219,
  output [7:0] out_220,
  output [7:0] out_221,
  output [7:0] out_222,
  output [7:0] out_223,
  output [7:0] out_224,
  output [7:0] out_225,
  output [7:0] out_226,
  output [7:0] out_227,
  output [7:0] out_228,
  output [7:0] out_229,
  output [7:0] out_230,
  output [7:0] out_231,
  output [7:0] out_232,
  output [7:0] out_233,
  output [7:0] out_234,
  output [7:0] out_235,
  output [7:0] out_236,
  output [7:0] out_237,
  output [7:0] out_238,
  output [7:0] out_239,
  output [7:0] out_240,
  output [7:0] out_241,
  output [7:0] out_242,
  output [7:0] out_243,
  output [7:0] out_244,
  output [7:0] out_245,
  output [7:0] out_246,
  output [7:0] out_247,
  output [7:0] out_248,
  output [7:0] out_249,
  output [7:0] out_250,
  output [7:0] out_251,
  output [7:0] out_252,
  output [7:0] out_253,
  output [7:0] out_254,
  output [7:0] out_255,
  output [7:0] out_256,
  output [7:0] out_257,
  output [7:0] out_258,
  output [7:0] out_259,
  output [7:0] out_260,
  output [7:0] out_261,
  output [7:0] out_262,
  output [7:0] out_263
);

  wire cpu_decoder_4x16_1_o1, cpu_decoder_4x16_1_o2, cpu_decoder_4x16_1_o3, cpu_decoder_4x16_1_o4,
       cpu_decoder_4x16_1_o5, cpu_decoder_4x16_1_o6, cpu_decoder_4x16_1_o7, cpu_decoder_4x16_1_o8,
       cpu_decoder_4x16_1_o9, cpu_decoder_4x16_1_o10, cpu_decoder_4x16_1_o11, cpu_decoder_4x16_1_o12,
       cpu_decoder_4x16_1_o13, cpu_decoder_4x16_1_o14, cpu_decoder_4x16_1_o15, cpu_decoder_4x16_1_o16,
       cpu_decoder_4x16_2_o1, cpu_decoder_4x16_2_o2, cpu_decoder_4x16_2_o3, cpu_decoder_4x16_2_o4,
       cpu_decoder_4x16_2_o5, cpu_decoder_4x16_2_o6, cpu_decoder_4x16_2_o7, cpu_decoder_4x16_2_o8,
       cpu_decoder_4x16_2_o9, cpu_decoder_4x16_2_o10, cpu_decoder_4x16_2_o11, cpu_decoder_4x16_2_o12,
       cpu_decoder_4x16_2_o13, cpu_decoder_4x16_2_o14, cpu_decoder_4x16_2_o15, cpu_decoder_4x16_2_o16;
  wire [7:0] cpu_mem_8_1_o, cpu_reg_byte_1_o;

  CPU_MEM_8 cpu_mem_8_1 (.i(adress), .s(sa), .o(cpu_mem_8_1_o));
  CPU_DECODER_4x16 cpu_decoder_4x16_1 (
    .i(cpu_mem_8_1_o[7:4]), .o1(cpu_decoder_4x16_1_o1), .o2(cpu_decoder_4x16_1_o2),
    .o3(cpu_decoder_4x16_1_o3), .o4(cpu_decoder_4x16_1_o4), .o5(cpu_decoder_4x16_1_o5),
    .o6(cpu_decoder_4x16_1_o6), .o7(cpu_decoder_4x16_1_o7), .o8(cpu_decoder_4x16_1_o8),
    .o9(cpu_decoder_4x16_1_o9), .o10(cpu_decoder_4x16_1_o10), .o11(cpu_decoder_4x16_1_o11),
    .o12(cpu_decoder_4x16_1_o12), .o13(cpu_decoder_4x16_1_o13), .o14(cpu_decoder_4x16_1_o14),
    .o15(cpu_decoder_4x16_1_o15), .o16(cpu_decoder_4x16_1_o16));
  assign o = e ? cpu_reg_byte_1_o : 8'bz;  // Controlled_Buffer controlled_buffer_1
  CPU_REG_BYTE cpu_reg_byte_1 (
    .i(i), .h(cpu_decoder_4x16_1_o1), .v(cpu_decoder_4x16_2_o16), .s(s), .e(e), .reset(reset), .op(out_8),
    .o(cpu_reg_byte_1_o));
  CPU_REG_BYTE cpu_reg_byte_2 (
    .i(i), .h(cpu_decoder_4x16_1_o2), .v(cpu_decoder_4x16_2_o16), .s(s), .e(e), .reset(reset), .op(out_24),
    .o(cpu_reg_byte_1_o));
  CPU_REG_BYTE cpu_reg_byte_3 (
    .i(i), .h(cpu_decoder_4x16_1_o3), .v(cpu_decoder_4x16_2_o16), .s(s), .e(e), .reset(reset), .op(out_40),
    .o(cpu_reg_byte_1_o));
  CPU_REG_BYTE cpu_reg_byte_4 (
    .i(i), .h(cpu_decoder_4x16_1_o4), .v(cpu_decoder_4x16_2_o16), .s(s), .e(e), .reset(reset), .op(out_56),
    .o(cpu_reg_byte_1_o));
  CPU_REG_BYTE cpu_reg_byte_5 (
    .i(i), .h(cpu_decoder_4x16_1_o5), .v(cpu_decoder_4x16_2_o16), .s(s), .e(e), .reset(reset), .op(out_72),
    .o(cpu_reg_byte_1_o));
  CPU_REG_BYTE cpu_reg_byte_6 (
    .i(i), .h(cpu_decoder_4x16_1_o6), .v(cpu_decoder_4x16_2_o16), .s(s), .e(e), .reset(reset), .op(out_88),
    .o(cpu_reg_byte_1_o));
  CPU_REG_BYTE cpu_reg_byte_7 (
    .i(i), .h(cpu_decoder_4x16_1_o7), .v(cpu_decoder_4x16_2_o16), .s(s), .e(e), .reset(reset), .op(out_104),
    .o(cpu_reg_byte_1_o));
  CPU_REG_BYTE cpu_reg_byte_8 (
    .i(i), .h(cpu_decoder_4x16_1_o8), .v(cpu_decoder_4x16_2_o16), .s(s), .e(e), .reset(reset), .op(out_120),
    .o(cpu_reg_byte_1_o));
  CPU_REG_BYTE cpu_reg_byte_9 (
    .i(i), .h(cpu_decoder_4x16_1_o9), .v(cpu_decoder_4x16_2_o16), .s(s), .e(e), .reset(reset), .op(out_136),
    .o(cpu_reg_byte_1_o));
  CPU_REG_BYTE cpu_reg_byte_10 (
    .i(i), .h(cpu_decoder_4x16_1_o10), .v(cpu_decoder_4x16_2_o16), .s(s), .e(e), .reset(reset), .op(out_152),
    .o(cpu_reg_byte_1_o));
  CPU_REG_BYTE cpu_reg_byte_11 (
    .i(i), .h(cpu_decoder_4x16_1_o11), .v(cpu_decoder_4x16_2_o16), .s(s), .e(e), .reset(reset), .op(out_168),
    .o(cpu_reg_byte_1_o));
  CPU_REG_BYTE cpu_reg_byte_12 (
    .i(i), .h(cpu_decoder_4x16_1_o12), .v(cpu_decoder_4x16_2_o16), .s(s), .e(e), .reset(reset), .op(out_184),
    .o(cpu_reg_byte_1_o));
  CPU_REG_BYTE cpu_reg_byte_13 (
    .i(i), .h(cpu_decoder_4x16_1_o13), .v(cpu_decoder_4x16_2_o16), .s(s), .e(e), .reset(reset), .op(out_200),
    .o(cpu_reg_byte_1_o));
  CPU_REG_BYTE cpu_reg_byte_14 (
    .i(i), .h(cpu_decoder_4x16_1_o14), .v(cpu_decoder_4x16_2_o16), .s(s), .e(e), .reset(reset), .op(out_216),
    .o(cpu_reg_byte_1_o));
  CPU_REG_BYTE cpu_reg_byte_15 (
    .i(i), .h(cpu_decoder_4x16_1_o15), .v(cpu_decoder_4x16_2_o16), .s(s), .e(e), .reset(reset), .op(out_232),
    .o(cpu_reg_byte_1_o));
  CPU_REG_BYTE cpu_reg_byte_16 (
    .i(i), .h(cpu_decoder_4x16_1_o16), .v(cpu_decoder_4x16_2_o16), .s(s), .e(e), .reset(reset), .op(out_248),
    .o(cpu_reg_byte_1_o));
  CPU_DECODER_4x16 cpu_decoder_4x16_2 (
    .i(cpu_mem_8_1_o[3:0]), .o1(cpu_decoder_4x16_2_o1), .o2(cpu_decoder_4x16_2_o2),
    .o3(cpu_decoder_4x16_2_o3), .o4(cpu_decoder_4x16_2_o4), .o5(cpu_decoder_4x16_2_o5),
    .o6(cpu_decoder_4x16_2_o6), .o7(cpu_decoder_4x16_2_o7), .o8(cpu_decoder_4x16_2_o8),
    .o9(cpu_decoder_4x16_2_o9), .o10(cpu_decoder_4x16_2_o10), .o11(cpu_decoder_4x16_2_o11),
    .o12(cpu_decoder_4x16_2_o12), .o13(cpu_decoder_4x16_2_o13), .o14(cpu_decoder_4x16_2_o14),
    .o15(cpu_decoder_4x16_2_o15), .o16(cpu_decoder_4x16_2_o16));
  CPU_REG_BYTE cpu_reg_byte_17 (
    .i(i), .h(cpu_decoder_4x16_1_o1), .v(cpu_decoder_4x16_2_o15), .s(s), .e(e), .reset(reset), .op(out_9),
    .o(cpu_reg_byte_1_o));
  CPU_REG_BYTE cpu_reg_byte_18 (
    .i(i), .h(cpu_decoder_4x16_1_o2), .v(cpu_decoder_4x16_2_o15), .s(s), .e(e), .reset(reset), .op(out_25),
    .o(cpu_reg_byte_1_o));
  CPU_REG_BYTE cpu_reg_byte_19 (
    .i(i), .h(cpu_decoder_4x16_1_o3), .v(cpu_decoder_4x16_2_o15), .s(s), .e(e), .reset(reset), .op(out_41),
    .o(cpu_reg_byte_1_o));
  CPU_REG_BYTE cpu_reg_byte_20 (
    .i(i), .h(cpu_decoder_4x16_1_o4), .v(cpu_decoder_4x16_2_o15), .s(s), .e(e), .reset(reset), .op(out_57),
    .o(cpu_reg_byte_1_o));
  CPU_REG_BYTE cpu_reg_byte_21 (
    .i(i), .h(cpu_decoder_4x16_1_o5), .v(cpu_decoder_4x16_2_o15), .s(s), .e(e), .reset(reset), .op(out_73),
    .o(cpu_reg_byte_1_o));
  CPU_REG_BYTE cpu_reg_byte_22 (
    .i(i), .h(cpu_decoder_4x16_1_o6), .v(cpu_decoder_4x16_2_o15), .s(s), .e(e), .reset(reset), .op(out_89),
    .o(cpu_reg_byte_1_o));
  CPU_REG_BYTE cpu_reg_byte_23 (
    .i(i), .h(cpu_decoder_4x16_1_o7), .v(cpu_decoder_4x16_2_o15), .s(s), .e(e), .reset(reset), .op(out_105),
    .o(cpu_reg_byte_1_o));
  CPU_REG_BYTE cpu_reg_byte_24 (
    .i(i), .h(cpu_decoder_4x16_1_o8), .v(cpu_decoder_4x16_2_o15), .s(s), .e(e), .reset(reset), .op(out_121),
    .o(cpu_reg_byte_1_o));
  CPU_REG_BYTE cpu_reg_byte_25 (
    .i(i), .h(cpu_decoder_4x16_1_o9), .v(cpu_decoder_4x16_2_o15), .s(s), .e(e), .reset(reset), .op(out_137),
    .o(cpu_reg_byte_1_o));
  CPU_REG_BYTE cpu_reg_byte_26 (
    .i(i), .h(cpu_decoder_4x16_1_o10), .v(cpu_decoder_4x16_2_o15), .s(s), .e(e), .reset(reset), .op(out_153),
    .o(cpu_reg_byte_1_o));
  CPU_REG_BYTE cpu_reg_byte_27 (
    .i(i), .h(cpu_decoder_4x16_1_o11), .v(cpu_decoder_4x16_2_o15), .s(s), .e(e), .reset(reset), .op(out_169),
    .o(cpu_reg_byte_1_o));
  CPU_REG_BYTE cpu_reg_byte_28 (
    .i(i), .h(cpu_decoder_4x16_1_o12), .v(cpu_decoder_4x16_2_o15), .s(s), .e(e), .reset(reset), .op(out_185),
    .o(cpu_reg_byte_1_o));
  CPU_REG_BYTE cpu_reg_byte_29 (
    .i(i), .h(cpu_decoder_4x16_1_o13), .v(cpu_decoder_4x16_2_o15), .s(s), .e(e), .reset(reset), .op(out_201),
    .o(cpu_reg_byte_1_o));
  CPU_REG_BYTE cpu_reg_byte_30 (
    .i(i), .h(cpu_decoder_4x16_1_o14), .v(cpu_decoder_4x16_2_o15), .s(s), .e(e), .reset(reset), .op(out_217),
    .o(cpu_reg_byte_1_o));
  CPU_REG_BYTE cpu_reg_byte_31 (
    .i(i), .h(cpu_decoder_4x16_1_o15), .v(cpu_decoder_4x16_2_o15), .s(s), .e(e), .reset(reset), .op(out_233),
    .o(cpu_reg_byte_1_o));
  CPU_REG_BYTE cpu_reg_byte_32 (
    .i(i), .h(cpu_decoder_4x16_1_o16), .v(cpu_decoder_4x16_2_o15), .s(s), .e(e), .reset(reset), .op(out_249),
    .o(cpu_reg_byte_1_o));
  CPU_REG_BYTE cpu_reg_byte_33 (
    .i(i), .h(cpu_decoder_4x16_1_o1), .v(cpu_decoder_4x16_2_o14), .s(s), .e(e), .reset(reset), .op(out_10),
    .o(cpu_reg_byte_1_o));
  CPU_REG_BYTE cpu_reg_byte_34 (
    .i(i), .h(cpu_decoder_4x16_1_o2), .v(cpu_decoder_4x16_2_o14), .s(s), .e(e), .reset(reset), .op(out_26),
    .o(cpu_reg_byte_1_o));
  CPU_REG_BYTE cpu_reg_byte_35 (
    .i(i), .h(cpu_decoder_4x16_1_o3), .v(cpu_decoder_4x16_2_o14), .s(s), .e(e), .reset(reset), .op(out_42),
    .o(cpu_reg_byte_1_o));
  CPU_REG_BYTE cpu_reg_byte_36 (
    .i(i), .h(cpu_decoder_4x16_1_o4), .v(cpu_decoder_4x16_2_o14), .s(s), .e(e), .reset(reset), .op(out_58),
    .o(cpu_reg_byte_1_o));
  CPU_REG_BYTE cpu_reg_byte_37 (
    .i(i), .h(cpu_decoder_4x16_1_o5), .v(cpu_decoder_4x16_2_o14), .s(s), .e(e), .reset(reset), .op(out_74),
    .o(cpu_reg_byte_1_o));
  CPU_REG_BYTE cpu_reg_byte_38 (
    .i(i), .h(cpu_decoder_4x16_1_o6), .v(cpu_decoder_4x16_2_o14), .s(s), .e(e), .reset(reset), .op(out_90),
    .o(cpu_reg_byte_1_o));
  CPU_REG_BYTE cpu_reg_byte_39 (
    .i(i), .h(cpu_decoder_4x16_1_o7), .v(cpu_decoder_4x16_2_o14), .s(s), .e(e), .reset(reset), .op(out_106),
    .o(cpu_reg_byte_1_o));
  CPU_REG_BYTE cpu_reg_byte_40 (
    .i(i), .h(cpu_decoder_4x16_1_o8), .v(cpu_decoder_4x16_2_o14), .s(s), .e(e), .reset(reset), .op(out_122),
    .o(cpu_reg_byte_1_o));
  CPU_REG_BYTE cpu_reg_byte_41 (
    .i(i), .h(cpu_decoder_4x16_1_o9), .v(cpu_decoder_4x16_2_o14), .s(s), .e(e), .reset(reset), .op(out_138),
    .o(cpu_reg_byte_1_o));
  CPU_REG_BYTE cpu_reg_byte_42 (
    .i(i), .h(cpu_decoder_4x16_1_o10), .v(cpu_decoder_4x16_2_o14), .s(s), .e(e), .reset(reset), .op(out_154),
    .o(cpu_reg_byte_1_o));
  CPU_REG_BYTE cpu_reg_byte_43 (
    .i(i), .h(cpu_decoder_4x16_1_o11), .v(cpu_decoder_4x16_2_o14), .s(s), .e(e), .reset(reset), .op(out_170),
    .o(cpu_reg_byte_1_o));
  CPU_REG_BYTE cpu_reg_byte_44 (
    .i(i), .h(cpu_decoder_4x16_1_o12), .v(cpu_decoder_4x16_2_o14), .s(s), .e(e), .reset(reset), .op(out_186),
    .o(cpu_reg_byte_1_o));
  CPU_REG_BYTE cpu_reg_byte_45 (
    .i(i), .h(cpu_decoder_4x16_1_o13), .v(cpu_decoder_4x16_2_o14), .s(s), .e(e), .reset(reset), .op(out_202),
    .o(cpu_reg_byte_1_o));
  CPU_REG_BYTE cpu_reg_byte_46 (
    .i(i), .h(cpu_decoder_4x16_1_o14), .v(cpu_decoder_4x16_2_o14), .s(s), .e(e), .reset(reset), .op(out_218),
    .o(cpu_reg_byte_1_o));
  CPU_REG_BYTE cpu_reg_byte_47 (
    .i(i), .h(cpu_decoder_4x16_1_o15), .v(cpu_decoder_4x16_2_o14), .s(s), .e(e), .reset(reset), .op(out_234),
    .o(cpu_reg_byte_1_o));
  CPU_REG_BYTE cpu_reg_byte_48 (
    .i(i), .h(cpu_decoder_4x16_1_o16), .v(cpu_decoder_4x16_2_o14), .s(s), .e(e), .reset(reset), .op(out_250),
    .o(cpu_reg_byte_1_o));
  CPU_REG_BYTE cpu_reg_byte_49 (
    .i(i), .h(cpu_decoder_4x16_1_o1), .v(cpu_decoder_4x16_2_o13), .s(s), .e(e), .reset(reset), .op(out_11),
    .o(cpu_reg_byte_1_o));
  CPU_REG_BYTE cpu_reg_byte_50 (
    .i(i), .h(cpu_decoder_4x16_1_o2), .v(cpu_decoder_4x16_2_o13), .s(s), .e(e), .reset(reset), .op(out_27),
    .o(cpu_reg_byte_1_o));
  CPU_REG_BYTE cpu_reg_byte_51 (
    .i(i), .h(cpu_decoder_4x16_1_o3), .v(cpu_decoder_4x16_2_o13), .s(s), .e(e), .reset(reset), .op(out_43),
    .o(cpu_reg_byte_1_o));
  CPU_REG_BYTE cpu_reg_byte_52 (
    .i(i), .h(cpu_decoder_4x16_1_o4), .v(cpu_decoder_4x16_2_o13), .s(s), .e(e), .reset(reset), .op(out_59),
    .o(cpu_reg_byte_1_o));
  CPU_REG_BYTE cpu_reg_byte_53 (
    .i(i), .h(cpu_decoder_4x16_1_o5), .v(cpu_decoder_4x16_2_o13), .s(s), .e(e), .reset(reset), .op(out_75),
    .o(cpu_reg_byte_1_o));
  CPU_REG_BYTE cpu_reg_byte_54 (
    .i(i), .h(cpu_decoder_4x16_1_o6), .v(cpu_decoder_4x16_2_o13), .s(s), .e(e), .reset(reset), .op(out_91),
    .o(cpu_reg_byte_1_o));
  CPU_REG_BYTE cpu_reg_byte_55 (
    .i(i), .h(cpu_decoder_4x16_1_o7), .v(cpu_decoder_4x16_2_o13), .s(s), .e(e), .reset(reset), .op(out_107),
    .o(cpu_reg_byte_1_o));
  CPU_REG_BYTE cpu_reg_byte_56 (
    .i(i), .h(cpu_decoder_4x16_1_o8), .v(cpu_decoder_4x16_2_o13), .s(s), .e(e), .reset(reset), .op(out_123),
    .o(cpu_reg_byte_1_o));
  CPU_REG_BYTE cpu_reg_byte_57 (
    .i(i), .h(cpu_decoder_4x16_1_o9), .v(cpu_decoder_4x16_2_o13), .s(s), .e(e), .reset(reset), .op(out_139),
    .o(cpu_reg_byte_1_o));
  CPU_REG_BYTE cpu_reg_byte_58 (
    .i(i), .h(cpu_decoder_4x16_1_o10), .v(cpu_decoder_4x16_2_o13), .s(s), .e(e), .reset(reset), .op(out_155),
    .o(cpu_reg_byte_1_o));
  CPU_REG_BYTE cpu_reg_byte_59 (
    .i(i), .h(cpu_decoder_4x16_1_o11), .v(cpu_decoder_4x16_2_o13), .s(s), .e(e), .reset(reset), .op(out_171),
    .o(cpu_reg_byte_1_o));
  CPU_REG_BYTE cpu_reg_byte_60 (
    .i(i), .h(cpu_decoder_4x16_1_o12), .v(cpu_decoder_4x16_2_o13), .s(s), .e(e), .reset(reset), .op(out_187),
    .o(cpu_reg_byte_1_o));
  CPU_REG_BYTE cpu_reg_byte_61 (
    .i(i), .h(cpu_decoder_4x16_1_o13), .v(cpu_decoder_4x16_2_o13), .s(s), .e(e), .reset(reset), .op(out_203),
    .o(cpu_reg_byte_1_o));
  CPU_REG_BYTE cpu_reg_byte_62 (
    .i(i), .h(cpu_decoder_4x16_1_o14), .v(cpu_decoder_4x16_2_o13), .s(s), .e(e), .reset(reset), .op(out_219),
    .o(cpu_reg_byte_1_o));
  CPU_REG_BYTE cpu_reg_byte_63 (
    .i(i), .h(cpu_decoder_4x16_1_o15), .v(cpu_decoder_4x16_2_o13), .s(s), .e(e), .reset(reset), .op(out_235),
    .o(cpu_reg_byte_1_o));
  CPU_REG_BYTE cpu_reg_byte_64 (
    .i(i), .h(cpu_decoder_4x16_1_o16), .v(cpu_decoder_4x16_2_o13), .s(s), .e(e), .reset(reset), .op(out_251),
    .o(cpu_reg_byte_1_o));
  CPU_REG_BYTE cpu_reg_byte_65 (
    .i(i), .h(cpu_decoder_4x16_1_o1), .v(cpu_decoder_4x16_2_o12), .s(s), .e(e), .reset(reset), .op(out_12),
    .o(cpu_reg_byte_1_o));
  CPU_REG_BYTE cpu_reg_byte_66 (
    .i(i), .h(cpu_decoder_4x16_1_o2), .v(cpu_decoder_4x16_2_o12), .s(s), .e(e), .reset(reset), .op(out_28),
    .o(cpu_reg_byte_1_o));
  CPU_REG_BYTE cpu_reg_byte_67 (
    .i(i), .h(cpu_decoder_4x16_1_o3), .v(cpu_decoder_4x16_2_o12), .s(s), .e(e), .reset(reset), .op(out_44),
    .o(cpu_reg_byte_1_o));
  CPU_REG_BYTE cpu_reg_byte_68 (
    .i(i), .h(cpu_decoder_4x16_1_o4), .v(cpu_decoder_4x16_2_o12), .s(s), .e(e), .reset(reset), .op(out_60),
    .o(cpu_reg_byte_1_o));
  CPU_REG_BYTE cpu_reg_byte_69 (
    .i(i), .h(cpu_decoder_4x16_1_o5), .v(cpu_decoder_4x16_2_o12), .s(s), .e(e), .reset(reset), .op(out_76),
    .o(cpu_reg_byte_1_o));
  CPU_REG_BYTE cpu_reg_byte_70 (
    .i(i), .h(cpu_decoder_4x16_1_o6), .v(cpu_decoder_4x16_2_o12), .s(s), .e(e), .reset(reset), .op(out_92),
    .o(cpu_reg_byte_1_o));
  CPU_REG_BYTE cpu_reg_byte_71 (
    .i(i), .h(cpu_decoder_4x16_1_o7), .v(cpu_decoder_4x16_2_o12), .s(s), .e(e), .reset(reset), .op(out_108),
    .o(cpu_reg_byte_1_o));
  CPU_REG_BYTE cpu_reg_byte_72 (
    .i(i), .h(cpu_decoder_4x16_1_o8), .v(cpu_decoder_4x16_2_o12), .s(s), .e(e), .reset(reset), .op(out_124),
    .o(cpu_reg_byte_1_o));
  CPU_REG_BYTE cpu_reg_byte_73 (
    .i(i), .h(cpu_decoder_4x16_1_o9), .v(cpu_decoder_4x16_2_o12), .s(s), .e(e), .reset(reset), .op(out_140),
    .o(cpu_reg_byte_1_o));
  CPU_REG_BYTE cpu_reg_byte_74 (
    .i(i), .h(cpu_decoder_4x16_1_o10), .v(cpu_decoder_4x16_2_o12), .s(s), .e(e), .reset(reset), .op(out_156),
    .o(cpu_reg_byte_1_o));
  CPU_REG_BYTE cpu_reg_byte_75 (
    .i(i), .h(cpu_decoder_4x16_1_o11), .v(cpu_decoder_4x16_2_o12), .s(s), .e(e), .reset(reset), .op(out_172),
    .o(cpu_reg_byte_1_o));
  CPU_REG_BYTE cpu_reg_byte_76 (
    .i(i), .h(cpu_decoder_4x16_1_o12), .v(cpu_decoder_4x16_2_o12), .s(s), .e(e), .reset(reset), .op(out_188),
    .o(cpu_reg_byte_1_o));
  CPU_REG_BYTE cpu_reg_byte_77 (
    .i(i), .h(cpu_decoder_4x16_1_o13), .v(cpu_decoder_4x16_2_o12), .s(s), .e(e), .reset(reset), .op(out_204),
    .o(cpu_reg_byte_1_o));
  CPU_REG_BYTE cpu_reg_byte_78 (
    .i(i), .h(cpu_decoder_4x16_1_o14), .v(cpu_decoder_4x16_2_o12), .s(s), .e(e), .reset(reset), .op(out_220),
    .o(cpu_reg_byte_1_o));
  CPU_REG_BYTE cpu_reg_byte_79 (
    .i(i), .h(cpu_decoder_4x16_1_o15), .v(cpu_decoder_4x16_2_o12), .s(s), .e(e), .reset(reset), .op(out_236),
    .o(cpu_reg_byte_1_o));
  CPU_REG_BYTE cpu_reg_byte_80 (
    .i(i), .h(cpu_decoder_4x16_1_o16), .v(cpu_decoder_4x16_2_o12), .s(s), .e(e), .reset(reset), .op(out_252),
    .o(cpu_reg_byte_1_o));
  CPU_REG_BYTE cpu_reg_byte_81 (
    .i(i), .h(cpu_decoder_4x16_1_o1), .v(cpu_decoder_4x16_2_o11), .s(s), .e(e), .reset(reset), .op(out_13),
    .o(cpu_reg_byte_1_o));
  CPU_REG_BYTE cpu_reg_byte_82 (
    .i(i), .h(cpu_decoder_4x16_1_o2), .v(cpu_decoder_4x16_2_o11), .s(s), .e(e), .reset(reset), .op(out_29),
    .o(cpu_reg_byte_1_o));
  CPU_REG_BYTE cpu_reg_byte_83 (
    .i(i), .h(cpu_decoder_4x16_1_o3), .v(cpu_decoder_4x16_2_o11), .s(s), .e(e), .reset(reset), .op(out_45),
    .o(cpu_reg_byte_1_o));
  CPU_REG_BYTE cpu_reg_byte_84 (
    .i(i), .h(cpu_decoder_4x16_1_o4), .v(cpu_decoder_4x16_2_o11), .s(s), .e(e), .reset(reset), .op(out_61),
    .o(cpu_reg_byte_1_o));
  CPU_REG_BYTE cpu_reg_byte_85 (
    .i(i), .h(cpu_decoder_4x16_1_o5), .v(cpu_decoder_4x16_2_o11), .s(s), .e(e), .reset(reset), .op(out_77),
    .o(cpu_reg_byte_1_o));
  CPU_REG_BYTE cpu_reg_byte_86 (
    .i(i), .h(cpu_decoder_4x16_1_o6), .v(cpu_decoder_4x16_2_o11), .s(s), .e(e), .reset(reset), .op(out_93),
    .o(cpu_reg_byte_1_o));
  CPU_REG_BYTE cpu_reg_byte_87 (
    .i(i), .h(cpu_decoder_4x16_1_o7), .v(cpu_decoder_4x16_2_o11), .s(s), .e(e), .reset(reset), .op(out_109),
    .o(cpu_reg_byte_1_o));
  CPU_REG_BYTE cpu_reg_byte_88 (
    .i(i), .h(cpu_decoder_4x16_1_o8), .v(cpu_decoder_4x16_2_o11), .s(s), .e(e), .reset(reset), .op(out_125),
    .o(cpu_reg_byte_1_o));
  CPU_REG_BYTE cpu_reg_byte_89 (
    .i(i), .h(cpu_decoder_4x16_1_o9), .v(cpu_decoder_4x16_2_o11), .s(s), .e(e), .reset(reset), .op(out_141),
    .o(cpu_reg_byte_1_o));
  CPU_REG_BYTE cpu_reg_byte_90 (
    .i(i), .h(cpu_decoder_4x16_1_o10), .v(cpu_decoder_4x16_2_o11), .s(s), .e(e), .reset(reset), .op(out_157),
    .o(cpu_reg_byte_1_o));
  CPU_REG_BYTE cpu_reg_byte_91 (
    .i(i), .h(cpu_decoder_4x16_1_o11), .v(cpu_decoder_4x16_2_o11), .s(s), .e(e), .reset(reset), .op(out_173),
    .o(cpu_reg_byte_1_o));
  CPU_REG_BYTE cpu_reg_byte_92 (
    .i(i), .h(cpu_decoder_4x16_1_o12), .v(cpu_decoder_4x16_2_o11), .s(s), .e(e), .reset(reset), .op(out_189),
    .o(cpu_reg_byte_1_o));
  CPU_REG_BYTE cpu_reg_byte_93 (
    .i(i), .h(cpu_decoder_4x16_1_o13), .v(cpu_decoder_4x16_2_o11), .s(s), .e(e), .reset(reset), .op(out_205),
    .o(cpu_reg_byte_1_o));
  CPU_REG_BYTE cpu_reg_byte_94 (
    .i(i), .h(cpu_decoder_4x16_1_o14), .v(cpu_decoder_4x16_2_o11), .s(s), .e(e), .reset(reset), .op(out_221),
    .o(cpu_reg_byte_1_o));
  CPU_REG_BYTE cpu_reg_byte_95 (
    .i(i), .h(cpu_decoder_4x16_1_o15), .v(cpu_decoder_4x16_2_o11), .s(s), .e(e), .reset(reset), .op(out_237),
    .o(cpu_reg_byte_1_o));
  CPU_REG_BYTE cpu_reg_byte_96 (
    .i(i), .h(cpu_decoder_4x16_1_o16), .v(cpu_decoder_4x16_2_o11), .s(s), .e(e), .reset(reset), .op(out_253),
    .o(cpu_reg_byte_1_o));
  CPU_REG_BYTE cpu_reg_byte_97 (
    .i(i), .h(cpu_decoder_4x16_1_o1), .v(cpu_decoder_4x16_2_o10), .s(s), .e(e), .reset(reset), .op(out_14),
    .o(cpu_reg_byte_1_o));
  CPU_REG_BYTE cpu_reg_byte_98 (
    .i(i), .h(cpu_decoder_4x16_1_o2), .v(cpu_decoder_4x16_2_o10), .s(s), .e(e), .reset(reset), .op(out_30),
    .o(cpu_reg_byte_1_o));
  CPU_REG_BYTE cpu_reg_byte_99 (
    .i(i), .h(cpu_decoder_4x16_1_o3), .v(cpu_decoder_4x16_2_o10), .s(s), .e(e), .reset(reset), .op(out_46),
    .o(cpu_reg_byte_1_o));
  CPU_REG_BYTE cpu_reg_byte_100 (
    .i(i), .h(cpu_decoder_4x16_1_o4), .v(cpu_decoder_4x16_2_o10), .s(s), .e(e), .reset(reset), .op(out_62),
    .o(cpu_reg_byte_1_o));
  CPU_REG_BYTE cpu_reg_byte_101 (
    .i(i), .h(cpu_decoder_4x16_1_o5), .v(cpu_decoder_4x16_2_o10), .s(s), .e(e), .reset(reset), .op(out_78),
    .o(cpu_reg_byte_1_o));
  CPU_REG_BYTE cpu_reg_byte_102 (
    .i(i), .h(cpu_decoder_4x16_1_o6), .v(cpu_decoder_4x16_2_o10), .s(s), .e(e), .reset(reset), .op(out_94),
    .o(cpu_reg_byte_1_o));
  CPU_REG_BYTE cpu_reg_byte_103 (
    .i(i), .h(cpu_decoder_4x16_1_o7), .v(cpu_decoder_4x16_2_o10), .s(s), .e(e), .reset(reset), .op(out_110),
    .o(cpu_reg_byte_1_o));
  CPU_REG_BYTE cpu_reg_byte_104 (
    .i(i), .h(cpu_decoder_4x16_1_o8), .v(cpu_decoder_4x16_2_o10), .s(s), .e(e), .reset(reset), .op(out_126),
    .o(cpu_reg_byte_1_o));
  CPU_REG_BYTE cpu_reg_byte_105 (
    .i(i), .h(cpu_decoder_4x16_1_o9), .v(cpu_decoder_4x16_2_o10), .s(s), .e(e), .reset(reset), .op(out_142),
    .o(cpu_reg_byte_1_o));
  CPU_REG_BYTE cpu_reg_byte_106 (
    .i(i), .h(cpu_decoder_4x16_1_o10), .v(cpu_decoder_4x16_2_o10), .s(s), .e(e), .reset(reset), .op(out_158),
    .o(cpu_reg_byte_1_o));
  CPU_REG_BYTE cpu_reg_byte_107 (
    .i(i), .h(cpu_decoder_4x16_1_o11), .v(cpu_decoder_4x16_2_o10), .s(s), .e(e), .reset(reset), .op(out_174),
    .o(cpu_reg_byte_1_o));
  CPU_REG_BYTE cpu_reg_byte_108 (
    .i(i), .h(cpu_decoder_4x16_1_o12), .v(cpu_decoder_4x16_2_o10), .s(s), .e(e), .reset(reset), .op(out_190),
    .o(cpu_reg_byte_1_o));
  CPU_REG_BYTE cpu_reg_byte_109 (
    .i(i), .h(cpu_decoder_4x16_1_o13), .v(cpu_decoder_4x16_2_o10), .s(s), .e(e), .reset(reset), .op(out_206),
    .o(cpu_reg_byte_1_o));
  CPU_REG_BYTE cpu_reg_byte_110 (
    .i(i), .h(cpu_decoder_4x16_1_o14), .v(cpu_decoder_4x16_2_o10), .s(s), .e(e), .reset(reset), .op(out_222),
    .o(cpu_reg_byte_1_o));
  CPU_REG_BYTE cpu_reg_byte_111 (
    .i(i), .h(cpu_decoder_4x16_1_o15), .v(cpu_decoder_4x16_2_o10), .s(s), .e(e), .reset(reset), .op(out_238),
    .o(cpu_reg_byte_1_o));
  CPU_REG_BYTE cpu_reg_byte_112 (
    .i(i), .h(cpu_decoder_4x16_1_o16), .v(cpu_decoder_4x16_2_o10), .s(s), .e(e), .reset(reset), .op(out_254),
    .o(cpu_reg_byte_1_o));
  CPU_REG_BYTE cpu_reg_byte_113 (
    .i(i), .h(cpu_decoder_4x16_1_o1), .v(cpu_decoder_4x16_2_o9), .s(s), .e(e), .reset(reset), .op(out_15),
    .o(cpu_reg_byte_1_o));
  CPU_REG_BYTE cpu_reg_byte_114 (
    .i(i), .h(cpu_decoder_4x16_1_o2), .v(cpu_decoder_4x16_2_o9), .s(s), .e(e), .reset(reset), .op(out_31),
    .o(cpu_reg_byte_1_o));
  CPU_REG_BYTE cpu_reg_byte_115 (
    .i(i), .h(cpu_decoder_4x16_1_o3), .v(cpu_decoder_4x16_2_o9), .s(s), .e(e), .reset(reset), .op(out_47),
    .o(cpu_reg_byte_1_o));
  CPU_REG_BYTE cpu_reg_byte_116 (
    .i(i), .h(cpu_decoder_4x16_1_o4), .v(cpu_decoder_4x16_2_o9), .s(s), .e(e), .reset(reset), .op(out_63),
    .o(cpu_reg_byte_1_o));
  CPU_REG_BYTE cpu_reg_byte_117 (
    .i(i), .h(cpu_decoder_4x16_1_o5), .v(cpu_decoder_4x16_2_o9), .s(s), .e(e), .reset(reset), .op(out_79),
    .o(cpu_reg_byte_1_o));
  CPU_REG_BYTE cpu_reg_byte_118 (
    .i(i), .h(cpu_decoder_4x16_1_o6), .v(cpu_decoder_4x16_2_o9), .s(s), .e(e), .reset(reset), .op(out_95),
    .o(cpu_reg_byte_1_o));
  CPU_REG_BYTE cpu_reg_byte_119 (
    .i(i), .h(cpu_decoder_4x16_1_o7), .v(cpu_decoder_4x16_2_o9), .s(s), .e(e), .reset(reset), .op(out_111),
    .o(cpu_reg_byte_1_o));
  CPU_REG_BYTE cpu_reg_byte_120 (
    .i(i), .h(cpu_decoder_4x16_1_o8), .v(cpu_decoder_4x16_2_o9), .s(s), .e(e), .reset(reset), .op(out_127),
    .o(cpu_reg_byte_1_o));
  CPU_REG_BYTE cpu_reg_byte_121 (
    .i(i), .h(cpu_decoder_4x16_1_o9), .v(cpu_decoder_4x16_2_o9), .s(s), .e(e), .reset(reset), .op(out_143),
    .o(cpu_reg_byte_1_o));
  CPU_REG_BYTE cpu_reg_byte_122 (
    .i(i), .h(cpu_decoder_4x16_1_o10), .v(cpu_decoder_4x16_2_o9), .s(s), .e(e), .reset(reset), .op(out_159),
    .o(cpu_reg_byte_1_o));
  CPU_REG_BYTE cpu_reg_byte_123 (
    .i(i), .h(cpu_decoder_4x16_1_o11), .v(cpu_decoder_4x16_2_o9), .s(s), .e(e), .reset(reset), .op(out_175),
    .o(cpu_reg_byte_1_o));
  CPU_REG_BYTE cpu_reg_byte_124 (
    .i(i), .h(cpu_decoder_4x16_1_o12), .v(cpu_decoder_4x16_2_o9), .s(s), .e(e), .reset(reset), .op(out_191),
    .o(cpu_reg_byte_1_o));
  CPU_REG_BYTE cpu_reg_byte_125 (
    .i(i), .h(cpu_decoder_4x16_1_o13), .v(cpu_decoder_4x16_2_o9), .s(s), .e(e), .reset(reset), .op(out_207),
    .o(cpu_reg_byte_1_o));
  CPU_REG_BYTE cpu_reg_byte_126 (
    .i(i), .h(cpu_decoder_4x16_1_o14), .v(cpu_decoder_4x16_2_o9), .s(s), .e(e), .reset(reset), .op(out_223),
    .o(cpu_reg_byte_1_o));
  CPU_REG_BYTE cpu_reg_byte_127 (
    .i(i), .h(cpu_decoder_4x16_1_o15), .v(cpu_decoder_4x16_2_o9), .s(s), .e(e), .reset(reset), .op(out_239),
    .o(cpu_reg_byte_1_o));
  CPU_REG_BYTE cpu_reg_byte_128 (
    .i(i), .h(cpu_decoder_4x16_1_o16), .v(cpu_decoder_4x16_2_o9), .s(s), .e(e), .reset(reset), .op(out_255),
    .o(cpu_reg_byte_1_o));
  CPU_REG_BYTE cpu_reg_byte_129 (
    .i(i), .h(cpu_decoder_4x16_1_o1), .v(cpu_decoder_4x16_2_o8), .s(s), .e(e), .reset(reset), .op(out_16),
    .o(cpu_reg_byte_1_o));
  CPU_REG_BYTE cpu_reg_byte_130 (
    .i(i), .h(cpu_decoder_4x16_1_o2), .v(cpu_decoder_4x16_2_o8), .s(s), .e(e), .reset(reset), .op(out_32),
    .o(cpu_reg_byte_1_o));
  CPU_REG_BYTE cpu_reg_byte_131 (
    .i(i), .h(cpu_decoder_4x16_1_o3), .v(cpu_decoder_4x16_2_o8), .s(s), .e(e), .reset(reset), .op(out_48),
    .o(cpu_reg_byte_1_o));
  CPU_REG_BYTE cpu_reg_byte_132 (
    .i(i), .h(cpu_decoder_4x16_1_o4), .v(cpu_decoder_4x16_2_o8), .s(s), .e(e), .reset(reset), .op(out_64),
    .o(cpu_reg_byte_1_o));
  CPU_REG_BYTE cpu_reg_byte_133 (
    .i(i), .h(cpu_decoder_4x16_1_o5), .v(cpu_decoder_4x16_2_o8), .s(s), .e(e), .reset(reset), .op(out_80),
    .o(cpu_reg_byte_1_o));
  CPU_REG_BYTE cpu_reg_byte_134 (
    .i(i), .h(cpu_decoder_4x16_1_o6), .v(cpu_decoder_4x16_2_o8), .s(s), .e(e), .reset(reset), .op(out_96),
    .o(cpu_reg_byte_1_o));
  CPU_REG_BYTE cpu_reg_byte_135 (
    .i(i), .h(cpu_decoder_4x16_1_o7), .v(cpu_decoder_4x16_2_o8), .s(s), .e(e), .reset(reset), .op(out_112),
    .o(cpu_reg_byte_1_o));
  CPU_REG_BYTE cpu_reg_byte_136 (
    .i(i), .h(cpu_decoder_4x16_1_o8), .v(cpu_decoder_4x16_2_o8), .s(s), .e(e), .reset(reset), .op(out_128),
    .o(cpu_reg_byte_1_o));
  CPU_REG_BYTE cpu_reg_byte_137 (
    .i(i), .h(cpu_decoder_4x16_1_o9), .v(cpu_decoder_4x16_2_o8), .s(s), .e(e), .reset(reset), .op(out_144),
    .o(cpu_reg_byte_1_o));
  CPU_REG_BYTE cpu_reg_byte_138 (
    .i(i), .h(cpu_decoder_4x16_1_o10), .v(cpu_decoder_4x16_2_o8), .s(s), .e(e), .reset(reset), .op(out_160),
    .o(cpu_reg_byte_1_o));
  CPU_REG_BYTE cpu_reg_byte_139 (
    .i(i), .h(cpu_decoder_4x16_1_o11), .v(cpu_decoder_4x16_2_o8), .s(s), .e(e), .reset(reset), .op(out_176),
    .o(cpu_reg_byte_1_o));
  CPU_REG_BYTE cpu_reg_byte_140 (
    .i(i), .h(cpu_decoder_4x16_1_o12), .v(cpu_decoder_4x16_2_o8), .s(s), .e(e), .reset(reset), .op(out_192),
    .o(cpu_reg_byte_1_o));
  CPU_REG_BYTE cpu_reg_byte_141 (
    .i(i), .h(cpu_decoder_4x16_1_o13), .v(cpu_decoder_4x16_2_o8), .s(s), .e(e), .reset(reset), .op(out_208),
    .o(cpu_reg_byte_1_o));
  CPU_REG_BYTE cpu_reg_byte_142 (
    .i(i), .h(cpu_decoder_4x16_1_o14), .v(cpu_decoder_4x16_2_o8), .s(s), .e(e), .reset(reset), .op(out_224),
    .o(cpu_reg_byte_1_o));
  CPU_REG_BYTE cpu_reg_byte_143 (
    .i(i), .h(cpu_decoder_4x16_1_o15), .v(cpu_decoder_4x16_2_o8), .s(s), .e(e), .reset(reset), .op(out_240),
    .o(cpu_reg_byte_1_o));
  CPU_REG_BYTE cpu_reg_byte_144 (
    .i(i), .h(cpu_decoder_4x16_1_o16), .v(cpu_decoder_4x16_2_o8), .s(s), .e(e), .reset(reset), .op(out_256),
    .o(cpu_reg_byte_1_o));
  CPU_REG_BYTE cpu_reg_byte_145 (
    .i(i), .h(cpu_decoder_4x16_1_o1), .v(cpu_decoder_4x16_2_o7), .s(s), .e(e), .reset(reset), .op(out_17),
    .o(cpu_reg_byte_1_o));
  CPU_REG_BYTE cpu_reg_byte_146 (
    .i(i), .h(cpu_decoder_4x16_1_o2), .v(cpu_decoder_4x16_2_o7), .s(s), .e(e), .reset(reset), .op(out_33),
    .o(cpu_reg_byte_1_o));
  CPU_REG_BYTE cpu_reg_byte_147 (
    .i(i), .h(cpu_decoder_4x16_1_o3), .v(cpu_decoder_4x16_2_o7), .s(s), .e(e), .reset(reset), .op(out_49),
    .o(cpu_reg_byte_1_o));
  CPU_REG_BYTE cpu_reg_byte_148 (
    .i(i), .h(cpu_decoder_4x16_1_o4), .v(cpu_decoder_4x16_2_o7), .s(s), .e(e), .reset(reset), .op(out_65),
    .o(cpu_reg_byte_1_o));
  CPU_REG_BYTE cpu_reg_byte_149 (
    .i(i), .h(cpu_decoder_4x16_1_o5), .v(cpu_decoder_4x16_2_o7), .s(s), .e(e), .reset(reset), .op(out_81),
    .o(cpu_reg_byte_1_o));
  CPU_REG_BYTE cpu_reg_byte_150 (
    .i(i), .h(cpu_decoder_4x16_1_o6), .v(cpu_decoder_4x16_2_o7), .s(s), .e(e), .reset(reset), .op(out_97),
    .o(cpu_reg_byte_1_o));
  CPU_REG_BYTE cpu_reg_byte_151 (
    .i(i), .h(cpu_decoder_4x16_1_o7), .v(cpu_decoder_4x16_2_o7), .s(s), .e(e), .reset(reset), .op(out_113),
    .o(cpu_reg_byte_1_o));
  CPU_REG_BYTE cpu_reg_byte_152 (
    .i(i), .h(cpu_decoder_4x16_1_o8), .v(cpu_decoder_4x16_2_o7), .s(s), .e(e), .reset(reset), .op(out_129),
    .o(cpu_reg_byte_1_o));
  CPU_REG_BYTE cpu_reg_byte_153 (
    .i(i), .h(cpu_decoder_4x16_1_o9), .v(cpu_decoder_4x16_2_o7), .s(s), .e(e), .reset(reset), .op(out_145),
    .o(cpu_reg_byte_1_o));
  CPU_REG_BYTE cpu_reg_byte_154 (
    .i(i), .h(cpu_decoder_4x16_1_o10), .v(cpu_decoder_4x16_2_o7), .s(s), .e(e), .reset(reset), .op(out_161),
    .o(cpu_reg_byte_1_o));
  CPU_REG_BYTE cpu_reg_byte_155 (
    .i(i), .h(cpu_decoder_4x16_1_o11), .v(cpu_decoder_4x16_2_o7), .s(s), .e(e), .reset(reset), .op(out_177),
    .o(cpu_reg_byte_1_o));
  CPU_REG_BYTE cpu_reg_byte_156 (
    .i(i), .h(cpu_decoder_4x16_1_o12), .v(cpu_decoder_4x16_2_o7), .s(s), .e(e), .reset(reset), .op(out_193),
    .o(cpu_reg_byte_1_o));
  CPU_REG_BYTE cpu_reg_byte_157 (
    .i(i), .h(cpu_decoder_4x16_1_o13), .v(cpu_decoder_4x16_2_o7), .s(s), .e(e), .reset(reset), .op(out_209),
    .o(cpu_reg_byte_1_o));
  CPU_REG_BYTE cpu_reg_byte_158 (
    .i(i), .h(cpu_decoder_4x16_1_o14), .v(cpu_decoder_4x16_2_o7), .s(s), .e(e), .reset(reset), .op(out_225),
    .o(cpu_reg_byte_1_o));
  CPU_REG_BYTE cpu_reg_byte_159 (
    .i(i), .h(cpu_decoder_4x16_1_o15), .v(cpu_decoder_4x16_2_o7), .s(s), .e(e), .reset(reset), .op(out_241),
    .o(cpu_reg_byte_1_o));
  CPU_REG_BYTE cpu_reg_byte_160 (
    .i(i), .h(cpu_decoder_4x16_1_o16), .v(cpu_decoder_4x16_2_o7), .s(s), .e(e), .reset(reset), .op(out_257),
    .o(cpu_reg_byte_1_o));
  CPU_REG_BYTE cpu_reg_byte_161 (
    .i(i), .h(cpu_decoder_4x16_1_o1), .v(cpu_decoder_4x16_2_o6), .s(s), .e(e), .reset(reset), .op(out_18),
    .o(cpu_reg_byte_1_o));
  CPU_REG_BYTE cpu_reg_byte_162 (
    .i(i), .h(cpu_decoder_4x16_1_o2), .v(cpu_decoder_4x16_2_o6), .s(s), .e(e), .reset(reset), .op(out_34),
    .o(cpu_reg_byte_1_o));
  CPU_REG_BYTE cpu_reg_byte_163 (
    .i(i), .h(cpu_decoder_4x16_1_o3), .v(cpu_decoder_4x16_2_o6), .s(s), .e(e), .reset(reset), .op(out_50),
    .o(cpu_reg_byte_1_o));
  CPU_REG_BYTE cpu_reg_byte_164 (
    .i(i), .h(cpu_decoder_4x16_1_o4), .v(cpu_decoder_4x16_2_o6), .s(s), .e(e), .reset(reset), .op(out_66),
    .o(cpu_reg_byte_1_o));
  CPU_REG_BYTE cpu_reg_byte_165 (
    .i(i), .h(cpu_decoder_4x16_1_o5), .v(cpu_decoder_4x16_2_o6), .s(s), .e(e), .reset(reset), .op(out_82),
    .o(cpu_reg_byte_1_o));
  CPU_REG_BYTE cpu_reg_byte_166 (
    .i(i), .h(cpu_decoder_4x16_1_o6), .v(cpu_decoder_4x16_2_o6), .s(s), .e(e), .reset(reset), .op(out_98),
    .o(cpu_reg_byte_1_o));
  CPU_REG_BYTE cpu_reg_byte_167 (
    .i(i), .h(cpu_decoder_4x16_1_o7), .v(cpu_decoder_4x16_2_o6), .s(s), .e(e), .reset(reset), .op(out_114),
    .o(cpu_reg_byte_1_o));
  CPU_REG_BYTE cpu_reg_byte_168 (
    .i(i), .h(cpu_decoder_4x16_1_o8), .v(cpu_decoder_4x16_2_o6), .s(s), .e(e), .reset(reset), .op(out_130),
    .o(cpu_reg_byte_1_o));
  CPU_REG_BYTE cpu_reg_byte_169 (
    .i(i), .h(cpu_decoder_4x16_1_o9), .v(cpu_decoder_4x16_2_o6), .s(s), .e(e), .reset(reset), .op(out_146),
    .o(cpu_reg_byte_1_o));
  CPU_REG_BYTE cpu_reg_byte_170 (
    .i(i), .h(cpu_decoder_4x16_1_o10), .v(cpu_decoder_4x16_2_o6), .s(s), .e(e), .reset(reset), .op(out_162),
    .o(cpu_reg_byte_1_o));
  CPU_REG_BYTE cpu_reg_byte_171 (
    .i(i), .h(cpu_decoder_4x16_1_o11), .v(cpu_decoder_4x16_2_o6), .s(s), .e(e), .reset(reset), .op(out_178),
    .o(cpu_reg_byte_1_o));
  CPU_REG_BYTE cpu_reg_byte_172 (
    .i(i), .h(cpu_decoder_4x16_1_o12), .v(cpu_decoder_4x16_2_o6), .s(s), .e(e), .reset(reset), .op(out_194),
    .o(cpu_reg_byte_1_o));
  CPU_REG_BYTE cpu_reg_byte_173 (
    .i(i), .h(cpu_decoder_4x16_1_o13), .v(cpu_decoder_4x16_2_o6), .s(s), .e(e), .reset(reset), .op(out_210),
    .o(cpu_reg_byte_1_o));
  CPU_REG_BYTE cpu_reg_byte_174 (
    .i(i), .h(cpu_decoder_4x16_1_o14), .v(cpu_decoder_4x16_2_o6), .s(s), .e(e), .reset(reset), .op(out_226),
    .o(cpu_reg_byte_1_o));
  CPU_REG_BYTE cpu_reg_byte_175 (
    .i(i), .h(cpu_decoder_4x16_1_o15), .v(cpu_decoder_4x16_2_o6), .s(s), .e(e), .reset(reset), .op(out_242),
    .o(cpu_reg_byte_1_o));
  CPU_REG_BYTE cpu_reg_byte_176 (
    .i(i), .h(cpu_decoder_4x16_1_o16), .v(cpu_decoder_4x16_2_o6), .s(s), .e(e), .reset(reset), .op(out_258),
    .o(cpu_reg_byte_1_o));
  CPU_REG_BYTE cpu_reg_byte_177 (
    .i(i), .h(cpu_decoder_4x16_1_o1), .v(cpu_decoder_4x16_2_o5), .s(s), .e(e), .reset(reset), .op(out_19),
    .o(cpu_reg_byte_1_o));
  CPU_REG_BYTE cpu_reg_byte_178 (
    .i(i), .h(cpu_decoder_4x16_1_o2), .v(cpu_decoder_4x16_2_o5), .s(s), .e(e), .reset(reset), .op(out_35),
    .o(cpu_reg_byte_1_o));
  CPU_REG_BYTE cpu_reg_byte_179 (
    .i(i), .h(cpu_decoder_4x16_1_o3), .v(cpu_decoder_4x16_2_o5), .s(s), .e(e), .reset(reset), .op(out_51),
    .o(cpu_reg_byte_1_o));
  CPU_REG_BYTE cpu_reg_byte_180 (
    .i(i), .h(cpu_decoder_4x16_1_o4), .v(cpu_decoder_4x16_2_o5), .s(s), .e(e), .reset(reset), .op(out_67),
    .o(cpu_reg_byte_1_o));
  CPU_REG_BYTE cpu_reg_byte_181 (
    .i(i), .h(cpu_decoder_4x16_1_o5), .v(cpu_decoder_4x16_2_o5), .s(s), .e(e), .reset(reset), .op(out_83),
    .o(cpu_reg_byte_1_o));
  CPU_REG_BYTE cpu_reg_byte_182 (
    .i(i), .h(cpu_decoder_4x16_1_o6), .v(cpu_decoder_4x16_2_o5), .s(s), .e(e), .reset(reset), .op(out_99),
    .o(cpu_reg_byte_1_o));
  CPU_REG_BYTE cpu_reg_byte_183 (
    .i(i), .h(cpu_decoder_4x16_1_o7), .v(cpu_decoder_4x16_2_o5), .s(s), .e(e), .reset(reset), .op(out_115),
    .o(cpu_reg_byte_1_o));
  CPU_REG_BYTE cpu_reg_byte_184 (
    .i(i), .h(cpu_decoder_4x16_1_o8), .v(cpu_decoder_4x16_2_o5), .s(s), .e(e), .reset(reset), .op(out_131),
    .o(cpu_reg_byte_1_o));
  CPU_REG_BYTE cpu_reg_byte_185 (
    .i(i), .h(cpu_decoder_4x16_1_o9), .v(cpu_decoder_4x16_2_o5), .s(s), .e(e), .reset(reset), .op(out_147),
    .o(cpu_reg_byte_1_o));
  CPU_REG_BYTE cpu_reg_byte_186 (
    .i(i), .h(cpu_decoder_4x16_1_o10), .v(cpu_decoder_4x16_2_o5), .s(s), .e(e), .reset(reset), .op(out_163),
    .o(cpu_reg_byte_1_o));
  CPU_REG_BYTE cpu_reg_byte_187 (
    .i(i), .h(cpu_decoder_4x16_1_o11), .v(cpu_decoder_4x16_2_o5), .s(s), .e(e), .reset(reset), .op(out_179),
    .o(cpu_reg_byte_1_o));
  CPU_REG_BYTE cpu_reg_byte_188 (
    .i(i), .h(cpu_decoder_4x16_1_o12), .v(cpu_decoder_4x16_2_o5), .s(s), .e(e), .reset(reset), .op(out_195),
    .o(cpu_reg_byte_1_o));
  CPU_REG_BYTE cpu_reg_byte_189 (
    .i(i), .h(cpu_decoder_4x16_1_o13), .v(cpu_decoder_4x16_2_o5), .s(s), .e(e), .reset(reset), .op(out_211),
    .o(cpu_reg_byte_1_o));
  CPU_REG_BYTE cpu_reg_byte_190 (
    .i(i), .h(cpu_decoder_4x16_1_o14), .v(cpu_decoder_4x16_2_o5), .s(s), .e(e), .reset(reset), .op(out_227),
    .o(cpu_reg_byte_1_o));
  CPU_REG_BYTE cpu_reg_byte_191 (
    .i(i), .h(cpu_decoder_4x16_1_o15), .v(cpu_decoder_4x16_2_o5), .s(s), .e(e), .reset(reset), .op(out_243),
    .o(cpu_reg_byte_1_o));
  CPU_REG_BYTE cpu_reg_byte_192 (
    .i(i), .h(cpu_decoder_4x16_1_o16), .v(cpu_decoder_4x16_2_o5), .s(s), .e(e), .reset(reset), .op(out_259),
    .o(cpu_reg_byte_1_o));
  CPU_REG_BYTE cpu_reg_byte_193 (
    .i(i), .h(cpu_decoder_4x16_1_o1), .v(cpu_decoder_4x16_2_o4), .s(s), .e(e), .reset(reset), .op(out_20),
    .o(cpu_reg_byte_1_o));
  CPU_REG_BYTE cpu_reg_byte_194 (
    .i(i), .h(cpu_decoder_4x16_1_o2), .v(cpu_decoder_4x16_2_o4), .s(s), .e(e), .reset(reset), .op(out_36),
    .o(cpu_reg_byte_1_o));
  CPU_REG_BYTE cpu_reg_byte_195 (
    .i(i), .h(cpu_decoder_4x16_1_o3), .v(cpu_decoder_4x16_2_o4), .s(s), .e(e), .reset(reset), .op(out_52),
    .o(cpu_reg_byte_1_o));
  CPU_REG_BYTE cpu_reg_byte_196 (
    .i(i), .h(cpu_decoder_4x16_1_o4), .v(cpu_decoder_4x16_2_o4), .s(s), .e(e), .reset(reset), .op(out_68),
    .o(cpu_reg_byte_1_o));
  CPU_REG_BYTE cpu_reg_byte_197 (
    .i(i), .h(cpu_decoder_4x16_1_o5), .v(cpu_decoder_4x16_2_o4), .s(s), .e(e), .reset(reset), .op(out_84),
    .o(cpu_reg_byte_1_o));
  CPU_REG_BYTE cpu_reg_byte_198 (
    .i(i), .h(cpu_decoder_4x16_1_o6), .v(cpu_decoder_4x16_2_o4), .s(s), .e(e), .reset(reset), .op(out_100),
    .o(cpu_reg_byte_1_o));
  CPU_REG_BYTE cpu_reg_byte_199 (
    .i(i), .h(cpu_decoder_4x16_1_o7), .v(cpu_decoder_4x16_2_o4), .s(s), .e(e), .reset(reset), .op(out_116),
    .o(cpu_reg_byte_1_o));
  CPU_REG_BYTE cpu_reg_byte_200 (
    .i(i), .h(cpu_decoder_4x16_1_o8), .v(cpu_decoder_4x16_2_o4), .s(s), .e(e), .reset(reset), .op(out_132),
    .o(cpu_reg_byte_1_o));
  CPU_REG_BYTE cpu_reg_byte_201 (
    .i(i), .h(cpu_decoder_4x16_1_o9), .v(cpu_decoder_4x16_2_o4), .s(s), .e(e), .reset(reset), .op(out_148),
    .o(cpu_reg_byte_1_o));
  CPU_REG_BYTE cpu_reg_byte_202 (
    .i(i), .h(cpu_decoder_4x16_1_o10), .v(cpu_decoder_4x16_2_o4), .s(s), .e(e), .reset(reset), .op(out_164),
    .o(cpu_reg_byte_1_o));
  CPU_REG_BYTE cpu_reg_byte_203 (
    .i(i), .h(cpu_decoder_4x16_1_o11), .v(cpu_decoder_4x16_2_o4), .s(s), .e(e), .reset(reset), .op(out_180),
    .o(cpu_reg_byte_1_o));
  CPU_REG_BYTE cpu_reg_byte_204 (
    .i(i), .h(cpu_decoder_4x16_1_o12), .v(cpu_decoder_4x16_2_o4), .s(s), .e(e), .reset(reset), .op(out_196),
    .o(cpu_reg_byte_1_o));
  CPU_REG_BYTE cpu_reg_byte_205 (
    .i(i), .h(cpu_decoder_4x16_1_o13), .v(cpu_decoder_4x16_2_o4), .s(s), .e(e), .reset(reset), .op(out_212),
    .o(cpu_reg_byte_1_o));
  CPU_REG_BYTE cpu_reg_byte_206 (
    .i(i), .h(cpu_decoder_4x16_1_o14), .v(cpu_decoder_4x16_2_o4), .s(s), .e(e), .reset(reset), .op(out_228),
    .o(cpu_reg_byte_1_o));
  CPU_REG_BYTE cpu_reg_byte_207 (
    .i(i), .h(cpu_decoder_4x16_1_o15), .v(cpu_decoder_4x16_2_o4), .s(s), .e(e), .reset(reset), .op(out_244),
    .o(cpu_reg_byte_1_o));
  CPU_REG_BYTE cpu_reg_byte_208 (
    .i(i), .h(cpu_decoder_4x16_1_o16), .v(cpu_decoder_4x16_2_o4), .s(s), .e(e), .reset(reset), .op(out_260),
    .o(cpu_reg_byte_1_o));
  CPU_REG_BYTE cpu_reg_byte_209 (
    .i(i), .h(cpu_decoder_4x16_1_o1), .v(cpu_decoder_4x16_2_o3), .s(s), .e(e), .reset(reset), .op(out_21),
    .o(cpu_reg_byte_1_o));
  CPU_REG_BYTE cpu_reg_byte_210 (
    .i(i), .h(cpu_decoder_4x16_1_o2), .v(cpu_decoder_4x16_2_o3), .s(s), .e(e), .reset(reset), .op(out_37),
    .o(cpu_reg_byte_1_o));
  CPU_REG_BYTE cpu_reg_byte_211 (
    .i(i), .h(cpu_decoder_4x16_1_o3), .v(cpu_decoder_4x16_2_o3), .s(s), .e(e), .reset(reset), .op(out_53),
    .o(cpu_reg_byte_1_o));
  CPU_REG_BYTE cpu_reg_byte_212 (
    .i(i), .h(cpu_decoder_4x16_1_o4), .v(cpu_decoder_4x16_2_o3), .s(s), .e(e), .reset(reset), .op(out_69),
    .o(cpu_reg_byte_1_o));
  CPU_REG_BYTE cpu_reg_byte_213 (
    .i(i), .h(cpu_decoder_4x16_1_o5), .v(cpu_decoder_4x16_2_o3), .s(s), .e(e), .reset(reset), .op(out_85),
    .o(cpu_reg_byte_1_o));
  CPU_REG_BYTE cpu_reg_byte_214 (
    .i(i), .h(cpu_decoder_4x16_1_o6), .v(cpu_decoder_4x16_2_o3), .s(s), .e(e), .reset(reset), .op(out_101),
    .o(cpu_reg_byte_1_o));
  CPU_REG_BYTE cpu_reg_byte_215 (
    .i(i), .h(cpu_decoder_4x16_1_o7), .v(cpu_decoder_4x16_2_o3), .s(s), .e(e), .reset(reset), .op(out_117),
    .o(cpu_reg_byte_1_o));
  CPU_REG_BYTE cpu_reg_byte_216 (
    .i(i), .h(cpu_decoder_4x16_1_o8), .v(cpu_decoder_4x16_2_o3), .s(s), .e(e), .reset(reset), .op(out_133),
    .o(cpu_reg_byte_1_o));
  CPU_REG_BYTE cpu_reg_byte_217 (
    .i(i), .h(cpu_decoder_4x16_1_o9), .v(cpu_decoder_4x16_2_o3), .s(s), .e(e), .reset(reset), .op(out_149),
    .o(cpu_reg_byte_1_o));
  CPU_REG_BYTE cpu_reg_byte_218 (
    .i(i), .h(cpu_decoder_4x16_1_o10), .v(cpu_decoder_4x16_2_o3), .s(s), .e(e), .reset(reset), .op(out_165),
    .o(cpu_reg_byte_1_o));
  CPU_REG_BYTE cpu_reg_byte_219 (
    .i(i), .h(cpu_decoder_4x16_1_o11), .v(cpu_decoder_4x16_2_o3), .s(s), .e(e), .reset(reset), .op(out_181),
    .o(cpu_reg_byte_1_o));
  CPU_REG_BYTE cpu_reg_byte_220 (
    .i(i), .h(cpu_decoder_4x16_1_o12), .v(cpu_decoder_4x16_2_o3), .s(s), .e(e), .reset(reset), .op(out_197),
    .o(cpu_reg_byte_1_o));
  CPU_REG_BYTE cpu_reg_byte_221 (
    .i(i), .h(cpu_decoder_4x16_1_o13), .v(cpu_decoder_4x16_2_o3), .s(s), .e(e), .reset(reset), .op(out_213),
    .o(cpu_reg_byte_1_o));
  CPU_REG_BYTE cpu_reg_byte_222 (
    .i(i), .h(cpu_decoder_4x16_1_o14), .v(cpu_decoder_4x16_2_o3), .s(s), .e(e), .reset(reset), .op(out_229),
    .o(cpu_reg_byte_1_o));
  CPU_REG_BYTE cpu_reg_byte_223 (
    .i(i), .h(cpu_decoder_4x16_1_o15), .v(cpu_decoder_4x16_2_o3), .s(s), .e(e), .reset(reset), .op(out_245),
    .o(cpu_reg_byte_1_o));
  CPU_REG_BYTE cpu_reg_byte_224 (
    .i(i), .h(cpu_decoder_4x16_1_o16), .v(cpu_decoder_4x16_2_o3), .s(s), .e(e), .reset(reset), .op(out_261),
    .o(cpu_reg_byte_1_o));
  CPU_REG_BYTE cpu_reg_byte_225 (
    .i(i), .h(cpu_decoder_4x16_1_o1), .v(cpu_decoder_4x16_2_o2), .s(s), .e(e), .reset(reset), .op(out_22),
    .o(cpu_reg_byte_1_o));
  CPU_REG_BYTE cpu_reg_byte_226 (
    .i(i), .h(cpu_decoder_4x16_1_o2), .v(cpu_decoder_4x16_2_o2), .s(s), .e(e), .reset(reset), .op(out_38),
    .o(cpu_reg_byte_1_o));
  CPU_REG_BYTE cpu_reg_byte_227 (
    .i(i), .h(cpu_decoder_4x16_1_o3), .v(cpu_decoder_4x16_2_o2), .s(s), .e(e), .reset(reset), .op(out_54),
    .o(cpu_reg_byte_1_o));
  CPU_REG_BYTE cpu_reg_byte_228 (
    .i(i), .h(cpu_decoder_4x16_1_o4), .v(cpu_decoder_4x16_2_o2), .s(s), .e(e), .reset(reset), .op(out_70),
    .o(cpu_reg_byte_1_o));
  CPU_REG_BYTE cpu_reg_byte_229 (
    .i(i), .h(cpu_decoder_4x16_1_o5), .v(cpu_decoder_4x16_2_o2), .s(s), .e(e), .reset(reset), .op(out_86),
    .o(cpu_reg_byte_1_o));
  CPU_REG_BYTE cpu_reg_byte_230 (
    .i(i), .h(cpu_decoder_4x16_1_o6), .v(cpu_decoder_4x16_2_o2), .s(s), .e(e), .reset(reset), .op(out_102),
    .o(cpu_reg_byte_1_o));
  CPU_REG_BYTE cpu_reg_byte_231 (
    .i(i), .h(cpu_decoder_4x16_1_o7), .v(cpu_decoder_4x16_2_o2), .s(s), .e(e), .reset(reset), .op(out_118),
    .o(cpu_reg_byte_1_o));
  CPU_REG_BYTE cpu_reg_byte_232 (
    .i(i), .h(cpu_decoder_4x16_1_o8), .v(cpu_decoder_4x16_2_o2), .s(s), .e(e), .reset(reset), .op(out_134),
    .o(cpu_reg_byte_1_o));
  CPU_REG_BYTE cpu_reg_byte_233 (
    .i(i), .h(cpu_decoder_4x16_1_o9), .v(cpu_decoder_4x16_2_o2), .s(s), .e(e), .reset(reset), .op(out_150),
    .o(cpu_reg_byte_1_o));
  CPU_REG_BYTE cpu_reg_byte_234 (
    .i(i), .h(cpu_decoder_4x16_1_o10), .v(cpu_decoder_4x16_2_o2), .s(s), .e(e), .reset(reset), .op(out_166),
    .o(cpu_reg_byte_1_o));
  CPU_REG_BYTE cpu_reg_byte_235 (
    .i(i), .h(cpu_decoder_4x16_1_o11), .v(cpu_decoder_4x16_2_o2), .s(s), .e(e), .reset(reset), .op(out_182),
    .o(cpu_reg_byte_1_o));
  CPU_REG_BYTE cpu_reg_byte_236 (
    .i(i), .h(cpu_decoder_4x16_1_o12), .v(cpu_decoder_4x16_2_o2), .s(s), .e(e), .reset(reset), .op(out_198),
    .o(cpu_reg_byte_1_o));
  CPU_REG_BYTE cpu_reg_byte_237 (
    .i(i), .h(cpu_decoder_4x16_1_o13), .v(cpu_decoder_4x16_2_o2), .s(s), .e(e), .reset(reset), .op(out_214),
    .o(cpu_reg_byte_1_o));
  CPU_REG_BYTE cpu_reg_byte_238 (
    .i(i), .h(cpu_decoder_4x16_1_o14), .v(cpu_decoder_4x16_2_o2), .s(s), .e(e), .reset(reset), .op(out_230),
    .o(cpu_reg_byte_1_o));
  CPU_REG_BYTE cpu_reg_byte_239 (
    .i(i), .h(cpu_decoder_4x16_1_o15), .v(cpu_decoder_4x16_2_o2), .s(s), .e(e), .reset(reset), .op(out_246),
    .o(cpu_reg_byte_1_o));
  CPU_REG_BYTE cpu_reg_byte_240 (
    .i(i), .h(cpu_decoder_4x16_1_o16), .v(cpu_decoder_4x16_2_o2), .s(s), .e(e), .reset(reset), .op(out_262),
    .o(cpu_reg_byte_1_o));
  CPU_REG_BYTE cpu_reg_byte_241 (
    .i(i), .h(cpu_decoder_4x16_1_o1), .v(cpu_decoder_4x16_2_o1), .s(s), .e(e), .reset(reset), .op(out_23),
    .o(cpu_reg_byte_1_o));
  CPU_REG_BYTE cpu_reg_byte_242 (
    .i(i), .h(cpu_decoder_4x16_1_o2), .v(cpu_decoder_4x16_2_o1), .s(s), .e(e), .reset(reset), .op(out_39),
    .o(cpu_reg_byte_1_o));
  CPU_REG_BYTE cpu_reg_byte_243 (
    .i(i), .h(cpu_decoder_4x16_1_o3), .v(cpu_decoder_4x16_2_o1), .s(s), .e(e), .reset(reset), .op(out_55),
    .o(cpu_reg_byte_1_o));
  CPU_REG_BYTE cpu_reg_byte_244 (
    .i(i), .h(cpu_decoder_4x16_1_o4), .v(cpu_decoder_4x16_2_o1), .s(s), .e(e), .reset(reset), .op(out_71),
    .o(cpu_reg_byte_1_o));
  CPU_REG_BYTE cpu_reg_byte_245 (
    .i(i), .h(cpu_decoder_4x16_1_o5), .v(cpu_decoder_4x16_2_o1), .s(s), .e(e), .reset(reset), .op(out_87),
    .o(cpu_reg_byte_1_o));
  CPU_REG_BYTE cpu_reg_byte_246 (
    .i(i), .h(cpu_decoder_4x16_1_o6), .v(cpu_decoder_4x16_2_o1), .s(s), .e(e), .reset(reset), .op(out_103),
    .o(cpu_reg_byte_1_o));
  CPU_REG_BYTE cpu_reg_byte_247 (
    .i(i), .h(cpu_decoder_4x16_1_o7), .v(cpu_decoder_4x16_2_o1), .s(s), .e(e), .reset(reset), .op(out_119),
    .o(cpu_reg_byte_1_o));
  CPU_REG_BYTE cpu_reg_byte_248 (
    .i(i), .h(cpu_decoder_4x16_1_o8), .v(cpu_decoder_4x16_2_o1), .s(s), .e(e), .reset(reset), .op(out_135),
    .o(cpu_reg_byte_1_o));
  CPU_REG_BYTE cpu_reg_byte_249 (
    .i(i), .h(cpu_decoder_4x16_1_o9), .v(cpu_decoder_4x16_2_o1), .s(s), .e(e), .reset(reset), .op(out_151),
    .o(cpu_reg_byte_1_o));
  CPU_REG_BYTE cpu_reg_byte_250 (
    .i(i), .h(cpu_decoder_4x16_1_o10), .v(cpu_decoder_4x16_2_o1), .s(s), .e(e), .reset(reset), .op(out_167),
    .o(cpu_reg_byte_1_o));
  CPU_REG_BYTE cpu_reg_byte_251 (
    .i(i), .h(cpu_decoder_4x16_1_o11), .v(cpu_decoder_4x16_2_o1), .s(s), .e(e), .reset(reset), .op(out_183),
    .o(cpu_reg_byte_1_o));
  CPU_REG_BYTE cpu_reg_byte_252 (
    .i(i), .h(cpu_decoder_4x16_1_o12), .v(cpu_decoder_4x16_2_o1), .s(s), .e(e), .reset(reset), .op(out_199),
    .o(cpu_reg_byte_1_o));
  CPU_REG_BYTE cpu_reg_byte_253 (
    .i(i), .h(cpu_decoder_4x16_1_o13), .v(cpu_decoder_4x16_2_o1), .s(s), .e(e), .reset(reset), .op(out_215),
    .o(cpu_reg_byte_1_o));
  CPU_REG_BYTE cpu_reg_byte_254 (
    .i(i), .h(cpu_decoder_4x16_1_o14), .v(cpu_decoder_4x16_2_o1), .s(s), .e(e), .reset(reset), .op(out_231),
    .o(cpu_reg_byte_1_o));
  CPU_REG_BYTE cpu_reg_byte_255 (
    .i(i), .h(cpu_decoder_4x16_1_o15), .v(cpu_decoder_4x16_2_o1), .s(s), .e(e), .reset(reset), .op(out_247),
    .o(cpu_reg_byte_1_o));
  CPU_REG_BYTE cpu_reg_byte_256 (
    .i(i), .h(cpu_decoder_4x16_1_o16), .v(cpu_decoder_4x16_2_o1), .s(s), .e(e), .reset(reset), .op(out_263),
    .o(cpu_reg_byte_1_o));
endmodule

module CPU_RAM_32 (
  input  [7:0] i,
  input  sa,
  input  [7:0] adress,
  input  s,
  input  e,
  input  reset,
  output [7:0] o,
  output [7:0] out_8,
  output [7:0] out_9,
  output [7:0] out_10,
  output [7:0] out_11,
  output [7:0] out_12,
  output [7:0] out_13,
  output [7:0] out_14,
  output [7:0] out_15,
  output [7:0] out_16,
  output [7:0] out_17,
  output [7:0] out_18,
  output [7:0] out_19,
  output [7:0] out_20,
  output [7:0] out_21,
  output [7:0] out_22,
  output [7:0] out_23,
  output [7:0] out_24,
  output [7:0] out_25,
  output [7:0] out_26,
  output [7:0] out_27,
  output [7:0] out_28,
  output [7:0] out_29,
  output [7:0] out_30,
  output [7:0] out_31,
  output [7:0] out_32,
  output [7:0] out_33,
  output [7:0] out_34,
  output [7:0] out_35,
  output [7:0] out_36,
  output [7:0] out_37,
  output [7:0] out_38,
  output [7:0] out_39
);

  wire cpu_decoder_4x16_1_o1, cpu_decoder_4x16_1_o2, cpu_decoder_4x16_1_o3, cpu_decoder_4x16_1_o4,
       cpu_decoder_4x16_1_o5, cpu_decoder_4x16_1_o6, cpu_decoder_4x16_1_o7, cpu_decoder_4x16_1_o8,
       cpu_decoder_4x16_1_o9, cpu_decoder_4x16_1_o10, cpu_decoder_4x16_1_o11, cpu_decoder_4x16_1_o12,
       cpu_decoder_4x16_1_o13, cpu_decoder_4x16_1_o14, cpu_decoder_4x16_1_o15, cpu_decoder_4x16_1_o16,
       cpu_decoder_4x16_2_o1, cpu_decoder_4x16_2_o2, cpu_decoder_4x16_2_o3, cpu_decoder_4x16_2_o4,
       cpu_decoder_4x16_2_o5, cpu_decoder_4x16_2_o6, cpu_decoder_4x16_2_o7, cpu_decoder_4x16_2_o8,
       cpu_decoder_4x16_2_o9, cpu_decoder_4x16_2_o10, cpu_decoder_4x16_2_o11, cpu_decoder_4x16_2_o12,
       cpu_decoder_4x16_2_o13, cpu_decoder_4x16_2_o14, cpu_decoder_4x16_2_o15, cpu_decoder_4x16_2_o16;
  wire [7:0] cpu_mem_8_1_o, cpu_reg_byte_1_o;

  CPU_MEM_8 cpu_mem_8_1 (.i(adress), .s(sa), .o(cpu_mem_8_1_o));
  CPU_DECODER_4x16 cpu_decoder_4x16_1 (
    .i(cpu_mem_8_1_o[7:4]), .o1(cpu_decoder_4x16_1_o1), .o2(cpu_decoder_4x16_1_o2),
    .o3(cpu_decoder_4x16_1_o3), .o4(cpu_decoder_4x16_1_o4), .o5(cpu_decoder_4x16_1_o5),
    .o6(cpu_decoder_4x16_1_o6), .o7(cpu_decoder_4x16_1_o7), .o8(cpu_decoder_4x16_1_o8),
    .o9(cpu_decoder_4x16_1_o9), .o10(cpu_decoder_4x16_1_o10), .o11(cpu_decoder_4x16_1_o11),
    .o12(cpu_decoder_4x16_1_o12), .o13(cpu_decoder_4x16_1_o13), .o14(cpu_decoder_4x16_1_o14),
    .o15(cpu_decoder_4x16_1_o15), .o16(cpu_decoder_4x16_1_o16));
  assign o = e ? cpu_reg_byte_1_o : 8'bz;  // Controlled_Buffer controlled_buffer_1
  CPU_REG_BYTE cpu_reg_byte_1 (
    .i(i), .h(cpu_decoder_4x16_1_o1), .v(cpu_decoder_4x16_2_o16), .s(s), .e(e), .reset(reset), .op(out_8),
    .o(cpu_reg_byte_1_o));
  CPU_REG_BYTE cpu_reg_byte_2 (
    .i(i), .h(cpu_decoder_4x16_1_o2), .v(cpu_decoder_4x16_2_o16), .s(s), .e(e), .reset(reset), .op(out_24),
    .o(cpu_reg_byte_1_o));
  CPU_DECODER_4x16 cpu_decoder_4x16_2 (
    .i(cpu_mem_8_1_o[3:0]), .o1(cpu_decoder_4x16_2_o1), .o2(cpu_decoder_4x16_2_o2),
    .o3(cpu_decoder_4x16_2_o3), .o4(cpu_decoder_4x16_2_o4), .o5(cpu_decoder_4x16_2_o5),
    .o6(cpu_decoder_4x16_2_o6), .o7(cpu_decoder_4x16_2_o7), .o8(cpu_decoder_4x16_2_o8),
    .o9(cpu_decoder_4x16_2_o9), .o10(cpu_decoder_4x16_2_o10), .o11(cpu_decoder_4x16_2_o11),
    .o12(cpu_decoder_4x16_2_o12), .o13(cpu_decoder_4x16_2_o13), .o14(cpu_decoder_4x16_2_o14),
    .o15(cpu_decoder_4x16_2_o15), .o16(cpu_decoder_4x16_2_o16));
  CPU_REG_BYTE cpu_reg_byte_3 (
    .i(i), .h(cpu_decoder_4x16_1_o1), .v(cpu_decoder_4x16_2_o15), .s(s), .e(e), .reset(reset), .op(out_9),
    .o(cpu_reg_byte_1_o));
  CPU_REG_BYTE cpu_reg_byte_4 (
    .i(i), .h(cpu_decoder_4x16_1_o2), .v(cpu_decoder_4x16_2_o15), .s(s), .e(e), .reset(reset), .op(out_25),
    .o(cpu_reg_byte_1_o));
  CPU_REG_BYTE cpu_reg_byte_5 (
    .i(i), .h(cpu_decoder_4x16_1_o1), .v(cpu_decoder_4x16_2_o14), .s(s), .e(e), .reset(reset), .op(out_10),
    .o(cpu_reg_byte_1_o));
  CPU_REG_BYTE cpu_reg_byte_6 (
    .i(i), .h(cpu_decoder_4x16_1_o2), .v(cpu_decoder_4x16_2_o14), .s(s), .e(e), .reset(reset), .op(out_26),
    .o(cpu_reg_byte_1_o));
  CPU_REG_BYTE cpu_reg_byte_7 (
    .i(i), .h(cpu_decoder_4x16_1_o1), .v(cpu_decoder_4x16_2_o13), .s(s), .e(e), .reset(reset), .op(out_11),
    .o(cpu_reg_byte_1_o));
  CPU_REG_BYTE cpu_reg_byte_8 (
    .i(i), .h(cpu_decoder_4x16_1_o2), .v(cpu_decoder_4x16_2_o13), .s(s), .e(e), .reset(reset), .op(out_27),
    .o(cpu_reg_byte_1_o));
  CPU_REG_BYTE cpu_reg_byte_9 (
    .i(i), .h(cpu_decoder_4x16_1_o1), .v(cpu_decoder_4x16_2_o12), .s(s), .e(e), .reset(reset), .op(out_12),
    .o(cpu_reg_byte_1_o));
  CPU_REG_BYTE cpu_reg_byte_10 (
    .i(i), .h(cpu_decoder_4x16_1_o2), .v(cpu_decoder_4x16_2_o12), .s(s), .e(e), .reset(reset), .op(out_28),
    .o(cpu_reg_byte_1_o));
  CPU_REG_BYTE cpu_reg_byte_11 (
    .i(i), .h(cpu_decoder_4x16_1_o1), .v(cpu_decoder_4x16_2_o11), .s(s), .e(e), .reset(reset), .op(out_13),
    .o(cpu_reg_byte_1_o));
  CPU_REG_BYTE cpu_reg_byte_12 (
    .i(i), .h(cpu_decoder_4x16_1_o2), .v(cpu_decoder_4x16_2_o11), .s(s), .e(e), .reset(reset), .op(out_29),
    .o(cpu_reg_byte_1_o));
  CPU_REG_BYTE cpu_reg_byte_13 (
    .i(i), .h(cpu_decoder_4x16_1_o1), .v(cpu_decoder_4x16_2_o10), .s(s), .e(e), .reset(reset), .op(out_14),
    .o(cpu_reg_byte_1_o));
  CPU_REG_BYTE cpu_reg_byte_14 (
    .i(i), .h(cpu_decoder_4x16_1_o2), .v(cpu_decoder_4x16_2_o10), .s(s), .e(e), .reset(reset), .op(out_30),
    .o(cpu_reg_byte_1_o));
  CPU_REG_BYTE cpu_reg_byte_15 (
    .i(i), .h(cpu_decoder_4x16_1_o1), .v(cpu_decoder_4x16_2_o9), .s(s), .e(e), .reset(reset), .op(out_15),
    .o(cpu_reg_byte_1_o));
  CPU_REG_BYTE cpu_reg_byte_16 (
    .i(i), .h(cpu_decoder_4x16_1_o2), .v(cpu_decoder_4x16_2_o9), .s(s), .e(e), .reset(reset), .op(out_31),
    .o(cpu_reg_byte_1_o));
  CPU_REG_BYTE cpu_reg_byte_17 (
    .i(i), .h(cpu_decoder_4x16_1_o1), .v(cpu_decoder_4x16_2_o8), .s(s), .e(e), .reset(reset), .op(out_16),
    .o(cpu_reg_byte_1_o));
  CPU_REG_BYTE cpu_reg_byte_18 (
    .i(i), .h(cpu_decoder_4x16_1_o2), .v(cpu_decoder_4x16_2_o8), .s(s), .e(e), .reset(reset), .op(out_32),
    .o(cpu_reg_byte_1_o));
  CPU_REG_BYTE cpu_reg_byte_19 (
    .i(i), .h(cpu_decoder_4x16_1_o1), .v(cpu_decoder_4x16_2_o7), .s(s), .e(e), .reset(reset), .op(out_17),
    .o(cpu_reg_byte_1_o));
  CPU_REG_BYTE cpu_reg_byte_20 (
    .i(i), .h(cpu_decoder_4x16_1_o2), .v(cpu_decoder_4x16_2_o7), .s(s), .e(e), .reset(reset), .op(out_33),
    .o(cpu_reg_byte_1_o));
  CPU_REG_BYTE cpu_reg_byte_21 (
    .i(i), .h(cpu_decoder_4x16_1_o1), .v(cpu_decoder_4x16_2_o6), .s(s), .e(e), .reset(reset), .op(out_18),
    .o(cpu_reg_byte_1_o));
  CPU_REG_BYTE cpu_reg_byte_22 (
    .i(i), .h(cpu_decoder_4x16_1_o2), .v(cpu_decoder_4x16_2_o6), .s(s), .e(e), .reset(reset), .op(out_34),
    .o(cpu_reg_byte_1_o));
  CPU_REG_BYTE cpu_reg_byte_23 (
    .i(i), .h(cpu_decoder_4x16_1_o1), .v(cpu_decoder_4x16_2_o5), .s(s), .e(e), .reset(reset), .op(out_19),
    .o(cpu_reg_byte_1_o));
  CPU_REG_BYTE cpu_reg_byte_24 (
    .i(i), .h(cpu_decoder_4x16_1_o2), .v(cpu_decoder_4x16_2_o5), .s(s), .e(e), .reset(reset), .op(out_35),
    .o(cpu_reg_byte_1_o));
  CPU_REG_BYTE cpu_reg_byte_25 (
    .i(i), .h(cpu_decoder_4x16_1_o1), .v(cpu_decoder_4x16_2_o4), .s(s), .e(e), .reset(reset), .op(out_20),
    .o(cpu_reg_byte_1_o));
  CPU_REG_BYTE cpu_reg_byte_26 (
    .i(i), .h(cpu_decoder_4x16_1_o2), .v(cpu_decoder_4x16_2_o4), .s(s), .e(e), .reset(reset), .op(out_36),
    .o(cpu_reg_byte_1_o));
  CPU_REG_BYTE cpu_reg_byte_27 (
    .i(i), .h(cpu_decoder_4x16_1_o1), .v(cpu_decoder_4x16_2_o3), .s(s), .e(e), .reset(reset), .op(out_21),
    .o(cpu_reg_byte_1_o));
  CPU_REG_BYTE cpu_reg_byte_28 (
    .i(i), .h(cpu_decoder_4x16_1_o2), .v(cpu_decoder_4x16_2_o3), .s(s), .e(e), .reset(reset), .op(out_37),
    .o(cpu_reg_byte_1_o));
  CPU_REG_BYTE cpu_reg_byte_29 (
    .i(i), .h(cpu_decoder_4x16_1_o1), .v(cpu_decoder_4x16_2_o2), .s(s), .e(e), .reset(reset), .op(out_22),
    .o(cpu_reg_byte_1_o));
  CPU_REG_BYTE cpu_reg_byte_30 (
    .i(i), .h(cpu_decoder_4x16_1_o2), .v(cpu_decoder_4x16_2_o2), .s(s), .e(e), .reset(reset), .op(out_38),
    .o(cpu_reg_byte_1_o));
  CPU_REG_BYTE cpu_reg_byte_31 (
    .i(i), .h(cpu_decoder_4x16_1_o1), .v(cpu_decoder_4x16_2_o1), .s(s), .e(e), .reset(reset), .op(out_23),
    .o(cpu_reg_byte_1_o));
  CPU_REG_BYTE cpu_reg_byte_32 (
    .i(i), .h(cpu_decoder_4x16_1_o2), .v(cpu_decoder_4x16_2_o1), .s(s), .e(e), .reset(reset), .op(out_39),
    .o(cpu_reg_byte_1_o));
endmodule

module ALU_ADDER (
  input  a,
  input  b,
  input  carry_in,
  output sum,
  output carry_out
);

  wire and_1_out, and_2_out, and_3_out, and_4_out, and_5_out, and_6_out, and_7_out, not_1_out, not_2_out,
       not_3_out;

  not not_1 (not_1_out, a);
  not not_2 (not_2_out, b);
  not not_3 (not_3_out, carry_in);
  and and_1 (and_1_out, not_1_out, not_2_out, carry_in);
  and and_2 (and_2_out, not_1_out, b, not_3_out);
  and and_3 (and_3_out, a, not_2_out, not_3_out);
  and and_4 (and_4_out, a, b, carry_in);
  and and_5 (and_5_out, b, carry_in);
  and and_6 (and_6_out, a, carry_in);
  and and_7 (and_7_out, a, b);
  or or_1 (sum, and_1_out, and_2_out, and_3_out, and_4_out);
  or or_2 (carry_out, and_5_out, and_6_out, and_7_out);
endmodule

module ALU_ADDER_8 (
  input  [7:0] a,
  input  carry_in,
  input  [7:0] b,
  output [7:0] sum,
  output carry_out
);

  wire alu_adder_1_carry_out, alu_adder_2_carry_out, alu_adder_3_carry_out, alu_adder_4_carry_out,
       alu_adder_5_carry_out, alu_adder_6_carry_out, alu_adder_7_carry_out;

  ALU_ADDER alu_adder_1 (.carry_in(carry_in), .a(a[0]), .b(b[0]), .sum(sum[0]), .carry_out(alu_adder_1_carry_out));
  ALU_ADDER alu_adder_2 (
    .carry_in(alu_adder_1_carry_out), .a(a[1]), .b(b[1]), .sum(sum[1]), .carry_out(alu_adder_2_carry_out));
  ALU_ADDER alu_adder_3 (
    .carry_in(alu_adder_2_carry_out), .a(a[2]), .b(b[2]), .sum(sum[2]), .carry_out(alu_adder_3_carry_out));
  ALU_ADDER alu_adder_4 (
    .carry_in(alu_adder_3_carry_out), .a(a[3]), .b(b[3]), .sum(sum[3]), .carry_out(alu_adder_4_carry_out));
  ALU_ADDER alu_adder_5 (
    .carry_in(alu_adder_4_carry_out), .a(a[4]), .b(b[4]), .sum(sum[4]), .carry_out(alu_adder_5_carry_out));
  ALU_ADDER alu_adder_6 (
    .carry_in(alu_adder_5_carry_out), .a(a[5]), .b(b[5]), .sum(sum[5]), .carry_out(alu_adder_6_carry_out));
  ALU_ADDER alu_adder_7 (
    .carry_in(alu_adder_6_carry_out), .a(a[6]), .b(b[6]), .sum(sum[6]), .carry_out(alu_adder_7_carry_out));
  ALU_ADDER alu_adder_8 (.carry_in(alu_adder_7_carry_out), .a(a[7]), .b(b[7]), .sum(sum[7]), .carry_out(carry_out));
endmodule

module ALU_SHIFT_L (
  input  shift_in,
  input  [7:0] i,
  output [7:0] o,
  output shift_out
);


  assign o = {i[6:0], shift_in};
  assign shift_out = i[7];
endmodule

module ALU_SHIFT_R (
  input  [7:0] i,
  input  shift_in,
  output shift_out,
  output [7:0] o
);


  assign o = {shift_in, i[7:1]};
  assign shift_out = i[0];
endmodule

module ALU_NOT (
  input  [7:0] i,
  output [7:0] not_8
);

  not not_1 (not_8[0], i[0]);
  not not_2 (not_8[1], i[1]);
  not not_3 (not_8[2], i[2]);
  not not_4 (not_8[3], i[3]);
  not not_5 (not_8[4], i[4]);
  not not_6 (not_8[5], i[5]);
  not not_7 (not_8[6], i[6]);
  not u_not_8 (not_8[7], i[7]);
endmodule

module ALU_AND (
  input  [7:0] a,
  input  [7:0] b,
  output [7:0] and_8
);

  and and_1 (and_8[0], a[0], b[0]);
  and and_2 (and_8[1], a[1], b[1]);
  and and_3 (and_8[2], a[2], b[2]);
  and and_4 (and_8[3], a[3], b[3]);
  and and_5 (and_8[4], a[4], b[4]);
  and and_6 (and_8[5], a[5], b[5]);
  and and_7 (and_8[6], a[6], b[6]);
  and u_and_8 (and_8[7], a[7], b[7]);
endmodule

module ALU_OR (
  input  [7:0] a,
  input  [7:0] b,
  output [7:0] or_8
);

  or or_1 (or_8[0], a[0], b[0]);
  or or_2 (or_8[1], a[1], b[1]);
  or or_3 (or_8[2], a[2], b[2]);
  or or_4 (or_8[3], a[3], b[3]);
  or or_5 (or_8[4], a[4], b[4]);
  or or_6 (or_8[5], a[5], b[5]);
  or or_7 (or_8[6], a[6], b[6]);
  or u_or_8 (or_8[7], a[7], b[7]);
endmodule

module ALU_XOR_LE (
  input  [7:0] a,
  input  [7:0] b,
  output larger,
  output equal,
  output [7:0] xor_8
);

  Comparator #(.mode("unsigned")) comparator_1 (.a(a), .b(b), .gt(larger), .eq(equal));  // open: lt
  xor xor_1 (xor_8[0], a[0], b[0]);
  xor xor_2 (xor_8[1], a[1], b[1]);
  xor xor_3 (xor_8[2], a[2], b[2]);
  xor xor_4 (xor_8[3], a[3], b[3]);
  xor xor_5 (xor_8[4], a[4], b[4]);
  xor xor_6 (xor_8[5], a[5], b[5]);
  xor xor_7 (xor_8[6], a[6], b[6]);
  xor u_xor_8 (xor_8[7], a[7], b[7]);
endmodule

module ALU_ZERO (
  input  [7:0] i,
  output o
);

  wire or_1_out;

  or or_1 (or_1_out, i[0], i[1], i[2], i[3], i[4], i[5], i[6], i[7]);
  not not_1 (o, or_1_out);
endmodule

module CPU_ALU (
  input  [7:0] a,
  input  [7:0] b,
  input  carry_in,
  input  c1,
  input  c2,
  input  c3,
  output larger,
  output equal,
  output zero,
  output [7:0] o,
  output carry_out
);

  wire alu_adder_8_1_carry_out, alu_shift_l_1_shift_out, alu_shift_r_1_shift_out, cpu_decoder_3x8_1_o1,
       cpu_decoder_3x8_1_o2, cpu_decoder_3x8_1_o3, cpu_decoder_3x8_1_o4, cpu_decoder_3x8_1_o5,
       cpu_decoder_3x8_1_o6, cpu_decoder_3x8_1_o7;
  wire [7:0] alu_adder_8_1_sum, alu_and_1_and_8, alu_not_1_not_8, alu_or_1_or_8, alu_shift_l_1_o,
       alu_shift_r_1_o, alu_xor_le_1_xor_8;

  ALU_XOR_LE alu_xor_le_1 (.a(a), .b(b), .larger(larger), .equal(equal), .xor_8(alu_xor_le_1_xor_8));
  ALU_OR alu_or_1 (.a(a), .b(b), .or_8(alu_or_1_or_8));
  ALU_AND alu_and_1 (.a(a), .b(b), .and_8(alu_and_1_and_8));
  ALU_NOT alu_not_1 (.i(a), .not_8(alu_not_1_not_8));
  ALU_SHIFT_L alu_shift_l_1 (.shift_in(carry_in), .i(a), .o(alu_shift_l_1_o), .shift_out(alu_shift_l_1_shift_out));
  ALU_SHIFT_R alu_shift_r_1 (.i(a), .shift_in(carry_in), .shift_out(alu_shift_r_1_shift_out), .o(alu_shift_r_1_o));
  ALU_ADDER_8 alu_adder_8_1 (
    .a(a), .carry_in(carry_in), .b(b), .sum(alu_adder_8_1_sum), .carry_out(alu_adder_8_1_carry_out));
  CPU_DECODER_3x8 cpu_decoder_3x8_1 (
    .a(c1), .b(c2), .c(c3), .o1(cpu_decoder_3x8_1_o1), .o2(cpu_decoder_3x8_1_o2), .o3(cpu_decoder_3x8_1_o3),
    .o4(cpu_decoder_3x8_1_o4), .o5(cpu_decoder_3x8_1_o5), .o6(cpu_decoder_3x8_1_o6), .o7(cpu_decoder_3x8_1_o7));  // open: o8
  assign carry_out = cpu_decoder_3x8_1_o3 ? alu_shift_l_1_shift_out : 1'bz;  // Controlled_Buffer controlled_buffer_1
  assign carry_out = cpu_decoder_3x8_1_o2 ? alu_shift_r_1_shift_out : 1'bz;  // Controlled_Buffer controlled_buffer_2
  assign carry_out = cpu_decoder_3x8_1_o1 ? alu_adder_8_1_carry_out : 1'bz;  // Controlled_Buffer controlled_buffer_3
  CPU_ENABLE_8 cpu_enable_8_1 (.i(alu_xor_le_1_xor_8), .e(cpu_decoder_3x8_1_o7), .o(o));
  CPU_ENABLE_8 cpu_enable_8_2 (.i(alu_or_1_or_8), .e(cpu_decoder_3x8_1_o6), .o(o));
  CPU_ENABLE_8 cpu_enable_8_3 (.i(alu_and_1_and_8), .e(cpu_decoder_3x8_1_o5), .o(o));
  CPU_ENABLE_8 cpu_enable_8_4 (.i(alu_not_1_not_8), .e(cpu_decoder_3x8_1_o4), .o(o));
  CPU_ENABLE_8 cpu_enable_8_5 (.i(alu_shift_l_1_o), .e(cpu_decoder_3x8_1_o3), .o(o));
  CPU_ENABLE_8 cpu_enable_8_6 (.i(alu_shift_r_1_o), .e(cpu_decoder_3x8_1_o2), .o(o));
  CPU_ENABLE_8 cpu_enable_8_7 (.i(alu_adder_8_1_sum), .e(cpu_decoder_3x8_1_o1), .o(o));
  ALU_ZERO alu_zero_1 (.i(o), .o(zero));
endmodule
