// Logisim project my_design_cpu.circ as structural Verilog: 56 circuits, main circuit USER PANEL
module main (
  input  r,
  input  [15:0] data_in,
  input  cntrl_s,
  input  en,
  input  [3:0] id,
  input  [3:0] in_addr,
  input  ul,
  output [15:0] rgb,
  output [7:0] Y,
  output [7:0] X
);

  wire and_1_out, and_2_out, and_3_out, and_4_out, and_5_out, and_6_out, and_7_out, d_ff_1_q, d_ff_1_qn,
       d_ff_2_q, d_ff_2_qn, d_ff_3_q, not_1_out, not_2_out;
  wire [3:0] xnor_1_out;
  wire [15:0] cpu_register_16_1_reg, cpu_register_16_2__0, cpu_register_16_2_reg, divider_1_out,
       divider_1_rem;

  Pull_Resistor pull_resistor_1 (.node(en));
  assign xnor_1_out = ~(id ^ in_addr);  // XNOR_Gate xnor_1, 4 bits wide
  and and_1 (and_1_out, xnor_1_out[0], xnor_1_out[1], xnor_1_out[2], xnor_1_out[3]);
  Pull_Resistor pull_resistor_2 (.node(and_1_out));
  and and_2 (and_2_out, en, and_1_out);
  Pull_Resistor pull_resistor_3 (.node(and_2_out));
  and and_3 (and_3_out, cntrl_s, d_ff_3_q);
  D_Flip_Flop d_ff_1 (.clk(and_3_out), .D(d_ff_1_qn), .Q(d_ff_1_q), .Qn(d_ff_1_qn));  // open: preset, reset
  D_Flip_Flop d_ff_2 (.clk(and_2_out), .D(d_ff_2_qn), .Q(d_ff_2_q), .Qn(d_ff_2_qn));  // open: preset, reset
  // Probe on cpu_register_16_1_reg
  not not_1 (not_1_out, ul);
  D_Flip_Flop d_ff_3 (.clk(d_ff_2_q), .D(not_1_out), .Q(d_ff_3_q), .reset(ul));  // open: Qn, preset
  and and_4 (and_4_out, d_ff_1_q, d_ff_3_q);
  not not_2 (not_2_out, d_ff_3_q);
  CPU_REGISTER_16 cpu_register_16_1 (
    .REG(cpu_register_16_1_reg), ._0(rgb), .i(data_in), .r(r), .s(and_4_out), .e(and_5_out));
  and and_5 (and_5_out, not_2_out, d_ff_2_qn);
  and and_6 (and_6_out, d_ff_1_qn, d_ff_3_q);
  // Probe on cpu_register_16_2_reg
  CPU_REGISTER_16 cpu_register_16_2 (
    .REG(cpu_register_16_2_reg), ._0(cpu_register_16_2__0), .i(data_in), .r(r), .s(and_6_out), .e(and_7_out));
  and and_7 (and_7_out, not_2_out, d_ff_2_qn);
  Divider #(.mode("unsigned"), .width(16)) divider_1 (
    .a(cpu_register_16_2__0), .b(16'h100), .out(divider_1_out), .rem(divider_1_rem));  // open: upper
  Bit_Extender #(.in_width(16), .out_width(8), .\type ("zero")) bit_extender_1 (.in(divider_1_out), .out(Y));
  Bit_Extender #(.in_width(16), .out_width(8), .\type ("zero")) bit_extender_2 (.in(divider_1_rem), .out(X));

  // Notes on the sheet:
  //   Colour
  //   x , y
endmodule

module USER_PANEL (
  input  W
);

  wire CLKE, CLKIN, CLKL, CLKS, DIS_CLK, END, KB, KYB_CLK, r;
  wire [5:0] FLAGS;
  wire [7:0] IN1, OUT1, X1, Y1;
  wire [15:0] FPU, IAR, IN2, IN3, INDEX, IR, OUT2, OUT3, R0, R1, R2, R3, R4, R5, R6_TEMP, SP;

  TTY #(.asciiwidth(8), .rows(16), .trigger("falling")) tty_1 (.data(OUT1[6:0]), .clk(CLKS), .we(DIS_CLK), .clr(r));
  Keyboard #(.asciiwidth(8), .trigger("falling")) keyboard_1 (
    .clk(CLKS), .re(KYB_CLK), .clr(r), .avail(KB), .data(IN1[6:0]));
  Hex_Digit_Display hex_digit_display_1 (.value(R0[15:12]));  // open: dp
  Hex_Digit_Display hex_digit_display_2 (.value(R0[11:8]));  // open: dp
  Hex_Digit_Display hex_digit_display_3 (.value(SP[15:12]));  // open: dp
  Hex_Digit_Display hex_digit_display_4 (.value(SP[11:8]));  // open: dp
  Hex_Digit_Display hex_digit_display_5 (.value(R0[7:4]));  // open: dp
  Hex_Digit_Display hex_digit_display_6 (.value(R0[3:0]));  // open: dp
  Hex_Digit_Display hex_digit_display_7 (.value(SP[7:4]));  // open: dp
  Hex_Digit_Display hex_digit_display_8 (.value(SP[3:0]));  // open: dp
  Hex_Digit_Display hex_digit_display_9 (.value(R1[15:12]));  // open: dp
  Hex_Digit_Display hex_digit_display_10 (.value(INDEX[15:12]));  // open: dp
  // RGB_Video #(.height(256), .width(256)) rgb_video_1: pin names not known; wires that end beside it: r, CLKIN, 1'b1, X1, Y1, OUT2
  Hex_Digit_Display hex_digit_display_11 (.value(R1[11:8]));  // open: dp
  Hex_Digit_Display hex_digit_display_12 (.value(R1[7:4]));  // open: dp
  Hex_Digit_Display hex_digit_display_13 (.value(INDEX[11:8]));  // open: dp
  Hex_Digit_Display hex_digit_display_14 (.value(INDEX[7:4]));  // open: dp
  Hex_Digit_Display hex_digit_display_15 (.value(R1[3:0]));  // open: dp
  Hex_Digit_Display hex_digit_display_16 (.value(INDEX[3:0]));  // open: dp
  Hex_Digit_Display hex_digit_display_17 (.value(R2[15:12]));  // open: dp
  Hex_Digit_Display hex_digit_display_18 (.value(R2[11:8]));  // open: dp
  Hex_Digit_Display hex_digit_display_19 (.value(FPU[15:12]));  // open: dp
  Hex_Digit_Display hex_digit_display_20 (.value(FPU[11:8]));  // open: dp
  Hex_Digit_Display hex_digit_display_21 (.value(R2[7:4]));  // open: dp
  Hex_Digit_Display hex_digit_display_22 (.value(R2[3:0]));  // open: dp
  Hex_Digit_Display hex_digit_display_23 (.value(FPU[7:4]));  // open: dp
  Hex_Digit_Display hex_digit_display_24 (.value(FPU[3:0]));  // open: dp
  Hex_Digit_Display hex_digit_display_25 (.value(R3[15:12]));  // open: dp
  Hex_Digit_Display hex_digit_display_26 (.value(IAR[15:12]));  // open: dp
  Hex_Digit_Display hex_digit_display_27 (.value(R3[11:8]));  // open: dp
  Hex_Digit_Display hex_digit_display_28 (.value(R3[7:4]));  // open: dp
  Hex_Digit_Display hex_digit_display_29 (.value(IAR[11:8]));  // open: dp
  Hex_Digit_Display hex_digit_display_30 (.value(IAR[7:4]));  // open: dp
  Hex_Digit_Display hex_digit_display_31 (.value(R3[3:0]));  // open: dp
  Hex_Digit_Display hex_digit_display_32 (.value(IR[15:12]));  // open: dp
  Hex_Digit_Display hex_digit_display_33 (.value(IAR[3:0]));  // open: dp
  Hex_Digit_Display hex_digit_display_34 (.value(R4[15:12]));  // open: dp
  Hex_Digit_Display hex_digit_display_35 (.value(R4[11:8]));  // open: dp
  Hex_Digit_Display hex_digit_display_36 (.value(IR[11:8]));  // open: dp
  Hex_Digit_Display hex_digit_display_37 (.value(IR[7:4]));  // open: dp
  CPU_MOTHERBOARD cpu_motherboard_1 (
    .CLKS(CLKS), .R0(R0), .R1(R1), .R2(R2), .R3(R3), .IR(IR), .IAR(IAR), .SP(SP), .OUT1(OUT1), .OUT3_3(Y1),
    .KYB_CLK(KYB_CLK), .OUT2(OUT2), .OUT3(OUT3), .OUT3_2(X1), .CLKL(CLKL), .CLKE(CLKE), .END(END),
    .FLAGS(FLAGS), .DIS_CLK(DIS_CLK), .INDEX(INDEX), .FPU(FPU), .R4(R4), .R5(R5), .R6_TEMP(R6_TEMP),
    .IN2(IN2), .IN3(IN3), .W(W), .CLK_IN(CLKIN), .r(r), .IN1(IN1));  // open: STOP
  Hex_Digit_Display hex_digit_display_38 (.value(R4[7:4]));  // open: dp
  Hex_Digit_Display hex_digit_display_39 (.value(R4[3:0]));  // open: dp
  Hex_Digit_Display hex_digit_display_40 (.value(IR[3:0]));  // open: dp
  Hex_Digit_Display hex_digit_display_41 (.value(R5[15:12]));  // open: dp
  Hex_Digit_Display hex_digit_display_42 (.value(R6_TEMP[15:12]));  // open: dp
  LED led_1 (.in(FLAGS[5]));
  Hex_Digit_Display hex_digit_display_43 (.value(R5[11:8]));  // open: dp
  Hex_Digit_Display hex_digit_display_44 (.value(R5[7:4]));  // open: dp
  Hex_Digit_Display hex_digit_display_45 (.value(R6_TEMP[11:8]));  // open: dp
  Hex_Digit_Display hex_digit_display_46 (.value(R6_TEMP[7:4]));  // open: dp
  LED led_2 (.in(FLAGS[4]));
  LED led_3 (.in(FLAGS[3]));
  Hex_Digit_Display hex_digit_display_47 (.value(R5[3:0]));  // open: dp
  Hex_Digit_Display hex_digit_display_48 (.value(R6_TEMP[3:0]));  // open: dp
  LED led_4 (.in(FLAGS[2]));
  LED led_5 (.in(FLAGS[1]));
  Button RESET (.out(r));
  LED #(.active("false")) led_6 (.in(END));
  Clock CLK (.out(CLKIN));
  LED led_7 (.in(FLAGS[0]));
  // Pins of 7 and 8 bits meet at OUT1
  // Pins of 7 and 8 bits meet at IN1

  // Notes on the sheet:
  //   RO
  //   SP
  //   DISPLAY
  //   KEYBOARD
  //   R1
  //   INDEX
  //   R2
  //   FPU
  //   GRAPHICS
  //   REGISTERS
  //   R3
  //   IAR
  //   R4
  //   IR
  //   COMPUTER
  //   Ci
  //   N
  //   R5
  //   R6 _TEMP
  //   FLAGS
  //   Co
  //   A>B
  //   0
  //   1
  //   0
  //   A=B
  //   Z
  //   CONTROL
endmodule

module CPU_MEM_1 (
  input  in_1,
  input  in_2,
  input  r,
  output out_4
);

  wire controlled_buffer_1_out, nand_1_out, nand_2_out, nand_4_out, not_1_out, or_1_out;

  assign controlled_buffer_1_out = r ? 1'b0 : 1'bz;  // Controlled_Buffer controlled_buffer_1
  assign controlled_buffer_1_out = not_1_out ? in_1 : 1'bz;  // Controlled_Buffer controlled_buffer_2
  not not_1 (not_1_out, r);
  or or_1 (or_1_out, in_2, r);
  nand nand_1 (nand_1_out, controlled_buffer_1_out, or_1_out);
  nand nand_2 (nand_2_out, nand_1_out, or_1_out);
  nand nand_3 (out_4, nand_1_out, nand_4_out);
  nand nand_4 (nand_4_out, out_4, nand_2_out);
endmodule

module CPU_MEM_16 (
  input  [15:0] in_1,
  input  r,
  input  s,
  output [15:0] out_4
);

  CPU_MEM_1 cpu_mem_1_1 (.out_4(out_4[0]), .in_1(in_1[0]), .in_2(s), .r(r));
  CPU_MEM_1 cpu_mem_1_2 (.out_4(out_4[1]), .in_1(in_1[1]), .in_2(s), .r(r));
  CPU_MEM_1 cpu_mem_1_3 (.out_4(out_4[2]), .in_1(in_1[2]), .in_2(s), .r(r));
  CPU_MEM_1 cpu_mem_1_4 (.out_4(out_4[3]), .in_1(in_1[3]), .in_2(s), .r(r));
  CPU_MEM_1 cpu_mem_1_5 (.out_4(out_4[4]), .in_1(in_1[4]), .in_2(s), .r(r));
  CPU_MEM_1 cpu_mem_1_6 (.out_4(out_4[5]), .in_1(in_1[5]), .in_2(s), .r(r));
  CPU_MEM_1 cpu_mem_1_7 (.out_4(out_4[6]), .in_1(in_1[6]), .in_2(s), .r(r));
  CPU_MEM_1 cpu_mem_1_8 (.out_4(out_4[7]), .in_1(in_1[7]), .in_2(s), .r(r));
  CPU_MEM_1 cpu_mem_1_9 (.out_4(out_4[8]), .in_1(in_1[8]), .in_2(s), .r(r));
  CPU_MEM_1 cpu_mem_1_10 (.out_4(out_4[9]), .in_1(in_1[9]), .in_2(s), .r(r));
  CPU_MEM_1 cpu_mem_1_11 (.out_4(out_4[10]), .in_1(in_1[10]), .in_2(s), .r(r));
  CPU_MEM_1 cpu_mem_1_12 (.out_4(out_4[11]), .in_1(in_1[11]), .in_2(s), .r(r));
  CPU_MEM_1 cpu_mem_1_13 (.out_4(out_4[12]), .in_1(in_1[12]), .in_2(s), .r(r));
  CPU_MEM_1 cpu_mem_1_14 (.out_4(out_4[13]), .in_1(in_1[13]), .in_2(s), .r(r));
  CPU_MEM_1 cpu_mem_1_15 (.out_4(out_4[14]), .in_1(in_1[14]), .in_2(s), .r(r));
  CPU_MEM_1 cpu_mem_1_16 (.out_4(out_4[15]), .in_1(in_1[15]), .in_2(s), .r(r));
endmodule

module CPU_ENABLE_16 (
  input  [15:0] in_1,
  input  in_2,
  output [15:0] out_3
);

  wire and_1_out, and_2_out, and_3_out, and_4_out, and_5_out, and_6_out, and_7_out, and_8_out, and_9_out,
       and_10_out, and_11_out, and_12_out, and_13_out, and_14_out, and_15_out, and_16_out;

  and and_1 (and_1_out, in_1[0], in_2);
  and and_2 (and_2_out, in_1[1], in_2);
  and and_3 (and_3_out, in_1[2], in_2);
  and and_4 (and_4_out, in_1[3], in_2);
  and and_5 (and_5_out, in_1[4], in_2);
  and and_6 (and_6_out, in_1[5], in_2);
  and and_7 (and_7_out, in_1[6], in_2);
  and and_8 (and_8_out, in_1[7], in_2);
  and and_9 (and_9_out, in_1[8], in_2);
  and and_10 (and_10_out, in_1[9], in_2);
  and and_11 (and_11_out, in_1[10], in_2);
  and and_12 (and_12_out, in_1[11], in_2);
  and and_13 (and_13_out, in_1[12], in_2);
  and and_14 (and_14_out, in_1[13], in_2);
  and and_15 (and_15_out, in_1[14], in_2);
  and and_16 (and_16_out, in_1[15], in_2);
  assign out_3[0] = in_2 ? and_1_out : 1'bz;  // Controlled_Buffer controlled_buffer_1
  assign out_3[1] = in_2 ? and_2_out : 1'bz;  // Controlled_Buffer controlled_buffer_2
  assign out_3[2] = in_2 ? and_3_out : 1'bz;  // Controlled_Buffer controlled_buffer_3
  assign out_3[3] = in_2 ? and_4_out : 1'bz;  // Controlled_Buffer controlled_buffer_4
  assign out_3[4] = in_2 ? and_5_out : 1'bz;  // Controlled_Buffer controlled_buffer_5
  assign out_3[5] = in_2 ? and_6_out : 1'bz;  // Controlled_Buffer controlled_buffer_6
  assign out_3[6] = in_2 ? and_7_out : 1'bz;  // Controlled_Buffer controlled_buffer_7
  assign out_3[7] = in_2 ? and_8_out : 1'bz;  // Controlled_Buffer controlled_buffer_8
  assign out_3[8] = in_2 ? and_9_out : 1'bz;  // Controlled_Buffer controlled_buffer_9
  assign out_3[9] = in_2 ? and_10_out : 1'bz;  // Controlled_Buffer controlled_buffer_10
  assign out_3[10] = in_2 ? and_11_out : 1'bz;  // Controlled_Buffer controlled_buffer_11
  assign out_3[11] = in_2 ? and_12_out : 1'bz;  // Controlled_Buffer controlled_buffer_12
  assign out_3[12] = in_2 ? and_13_out : 1'bz;  // Controlled_Buffer controlled_buffer_13
  assign out_3[13] = in_2 ? and_14_out : 1'bz;  // Controlled_Buffer controlled_buffer_14
  assign out_3[14] = in_2 ? and_15_out : 1'bz;  // Controlled_Buffer controlled_buffer_15
  assign out_3[15] = in_2 ? and_16_out : 1'bz;  // Controlled_Buffer controlled_buffer_16
endmodule

module CPU_REGISTER_16 (
  input  [15:0] i,
  input  r,
  input  s,
  input  e,
  output [15:0] REG,
  output [15:0] _0
);

  wire [15:0] cpu_enable_16_1_out_3;

  CPU_MEM_16 cpu_mem_16_1 (.out_4(REG), .in_1(i), .r(r), .s(s));
  CPU_ENABLE_16 cpu_enable_16_1 (.out_3(cpu_enable_16_1_out_3), .in_1(REG), .in_2(e));
  assign _0 = e ? cpu_enable_16_1_out_3 : 16'bz;  // Controlled_Buffer controlled_buffer_1
endmodule

module CPU_DECODER_4x16 (
  input  [3:0] in_1,
  output L,
  output out_3,
  output out_4,
  output out_5,
  output out_6,
  output out_7,
  output out_8,
  output out_9,
  output out_10,
  output out_11,
  output out_12,
  output out_13,
  output out_14,
  output out_15,
  output out_16,
  output M
);

  wire not_1_out, not_2_out, not_3_out, not_4_out;

  not not_1 (not_1_out, in_1[0]);
  not not_2 (not_2_out, in_1[1]);
  not not_3 (not_3_out, in_1[2]);
  not not_4 (not_4_out, in_1[3]);
  and and_1 (L, not_4_out, not_3_out, not_2_out, not_1_out);
  and and_2 (out_3, not_4_out, not_3_out, not_2_out, in_1[0]);
  and and_3 (out_4, not_4_out, not_3_out, in_1[1], not_1_out);
  and and_4 (out_5, not_4_out, not_3_out, in_1[1], in_1[0]);
  and and_5 (out_6, not_4_out, in_1[2], not_2_out, not_1_out);
  and and_6 (out_7, not_4_out, in_1[2], not_2_out, in_1[0]);
  and and_7 (out_8, not_4_out, in_1[2], in_1[1], not_1_out);
  and and_8 (out_9, not_4_out, in_1[2], in_1[1], in_1[0]);
  and and_9 (out_10, in_1[3], not_3_out, not_2_out, not_1_out);
  and and_10 (out_11, in_1[3], not_3_out, not_2_out, in_1[0]);
  and and_11 (out_12, in_1[3], not_3_out, in_1[1], not_1_out);
  and and_12 (out_13, in_1[3], not_3_out, in_1[1], in_1[0]);
  and and_13 (out_14, in_1[3], in_1[2], not_2_out, not_1_out);
  and and_14 (out_15, in_1[3], in_1[2], not_2_out, in_1[0]);
  and and_15 (out_16, in_1[3], in_1[2], in_1[1], not_1_out);
  and and_16 (M, in_1[3], in_1[2], in_1[1], in_1[0]);
endmodule

module CPU_REG_BYTE (
  input  [7:0] i,
  input  r,
  input  h,
  input  v,
  input  s,
  input  e,
  output [7:0] o,
  output [7:0] op
);

  wire and_1_out, and_2_out, and_3_out;
  wire [7:0] cpu_register_16_1_p6;

  and and_1 (and_1_out, h, v);
  and and_2 (and_2_out, and_1_out, s);
  and and_3 (and_3_out, and_1_out, e);
  // CPU_REGISTER_16 cpu_register_16_1: pin names not known; wires that end beside it: op, i, r, and_2_out, and_3_out, cpu_register_16_1_p6
  assign o = and_3_out ? cpu_register_16_1_p6 : 8'bz;  // Controlled_Buffer controlled_buffer_1
endmodule

module CPU_RAM_256 (
  input  r,
  input  [7:0] i,
  input  sa,
  input  [7:0] address,
  input  s,
  input  e,
  output [7:0] o,
  output [7:0] _15,
  output [7:0] _14,
  output [7:0] _13,
  output [7:0] _12,
  output [7:0] _11,
  output [7:0] _10,
  output [7:0] _9,
  output [7:0] _8,
  output [7:0] _7,
  output [7:0] _6,
  output [7:0] _5,
  output [7:0] _4,
  output [7:0] _21,
  output [7:0] _2,
  output [7:0] _1,
  output [7:0] _0,
  output [7:0] _31,
  output [7:0] _30,
  output [7:0] _29,
  output [7:0] _28,
  output [7:0] _27,
  output [7:0] _26,
  output [7:0] _25,
  output [7:0] _24,
  output [7:0] _23,
  output [7:0] _22,
  output [7:0] _21_2,
  output [7:0] _20,
  output [7:0] _19,
  output [7:0] _18,
  output [7:0] _17,
  output [7:0] _16,
  output [7:0] _47,
  output [7:0] _46,
  output [7:0] _45,
  output [7:0] _44,
  output [7:0] _43,
  output [7:0] _42,
  output [7:0] _41,
  output [7:0] _40,
  output [7:0] _39,
  output [7:0] _38,
  output [7:0] _37,
  output [7:0] _36,
  output [7:0] _35,
  output [7:0] _34,
  output [7:0] _33,
  output [7:0] _32,
  output [7:0] _63,
  output [7:0] _62,
  output [7:0] _61,
  output [7:0] _60,
  output [7:0] _59,
  output [7:0] _58,
  output [7:0] _57,
  output [7:0] _56,
  output [7:0] _55,
  output [7:0] _54,
  output [7:0] _53,
  output [7:0] _52,
  output [7:0] _51,
  output [7:0] _50,
  output [7:0] _49,
  output [7:0] _48,
  output [7:0] _79,
  output [7:0] _78,
  output [7:0] _77,
  output [7:0] _76,
  output [7:0] _75,
  output [7:0] _74,
  output [7:0] _73,
  output [7:0] _72,
  output [7:0] _71,
  output [7:0] _70,
  output [7:0] _69,
  output [7:0] _68,
  output [7:0] _67,
  output [7:0] _66,
  output [7:0] _65,
  output [7:0] _64,
  output [7:0] _95,
  output [7:0] _94,
  output [7:0] _93,
  output [7:0] _92,
  output [7:0] _91,
  output [7:0] _90,
  output [7:0] _89,
  output [7:0] _88,
  output [7:0] _87,
  output [7:0] _86,
  output [7:0] _85,
  output [7:0] _84,
  output [7:0] _83,
  output [7:0] _82,
  output [7:0] _81,
  output [7:0] _80,
  output [7:0] _111,
  output [7:0] _110,
  output [7:0] _109,
  output [7:0] _108,
  output [7:0] _107,
  output [7:0] _106,
  output [7:0] _105,
  output [7:0] _104,
  output [7:0] _103,
  output [7:0] _102,
  output [7:0] _101,
  output [7:0] _100,
  output [7:0] _99,
  output [7:0] _98,
  output [7:0] _97,
  output [7:0] _96,
  output [7:0] _127,
  output [7:0] _126,
  output [7:0] _125,
  output [7:0] _124,
  output [7:0] _123,
  output [7:0] _122,
  output [7:0] _121,
  output [7:0] _120,
  output [7:0] _119,
  output [7:0] _118,
  output [7:0] _117,
  output [7:0] _116,
  output [7:0] _115,
  output [7:0] _114,
  output [7:0] _113,
  output [7:0] _112,
  output [7:0] _143,
  output [7:0] _142,
  output [7:0] _141,
  output [7:0] _140,
  output [7:0] _139,
  output [7:0] _138,
  output [7:0] _137,
  output [7:0] _136,
  output [7:0] _135,
  output [7:0] _134,
  output [7:0] _133,
  output [7:0] _132,
  output [7:0] _131,
  output [7:0] _130,
  output [7:0] _129,
  output [7:0] _128,
  output [7:0] _159,
  output [7:0] _158,
  output [7:0] _157,
  output [7:0] _156,
  output [7:0] _155,
  output [7:0] _154,
  output [7:0] _153,
  output [7:0] _152,
  output [7:0] _151,
  output [7:0] _150,
  output [7:0] _149,
  output [7:0] _148,
  output [7:0] _147,
  output [7:0] _146,
  output [7:0] _145,
  output [7:0] _144,
  output [7:0] _175,
  output [7:0] _174,
  output [7:0] _173,
  output [7:0] _172,
  output [7:0] _171,
  output [7:0] _170,
  output [7:0] _169,
  output [7:0] _168,
  output [7:0] _167,
  output [7:0] _166,
  output [7:0] _165,
  output [7:0] _164,
  output [7:0] _163,
  output [7:0] _162,
  output [7:0] _161,
  output [7:0] _160,
  output [7:0] _191,
  output [7:0] _190,
  output [7:0] _189,
  output [7:0] _188,
  output [7:0] _187,
  output [7:0] _186,
  output [7:0] _185,
  output [7:0] _184,
  output [7:0] _183,
  output [7:0] _182,
  output [7:0] _181,
  output [7:0] _180,
  output [7:0] _179,
  output [7:0] _178,
  output [7:0] _177,
  output [7:0] _176,
  output [7:0] _207,
  output [7:0] _206,
  output [7:0] _205,
  output [7:0] _204,
  output [7:0] _203,
  output [7:0] _202,
  output [7:0] _201,
  output [7:0] _200,
  output [7:0] _199,
  output [7:0] _198,
  output [7:0] _197,
  output [7:0] _196,
  output [7:0] _195,
  output [7:0] _194,
  output [7:0] _193,
  output [7:0] _192,
  output [7:0] _223,
  output [7:0] _222,
  output [7:0] _221,
  output [7:0] _220,
  output [7:0] _219,
  output [7:0] _218,
  output [7:0] _217,
  output [7:0] _216,
  output [7:0] _215,
  output [7:0] _214,
  output [7:0] _213,
  output [7:0] _212,
  output [7:0] _211,
  output [7:0] _210,
  output [7:0] _209,
  output [7:0] _208,
  output [7:0] _239,
  output [7:0] _238,
  output [7:0] _237,
  output [7:0] _236,
  output [7:0] _235,
  output [7:0] _234,
  output [7:0] _233,
  output [7:0] _232,
  output [7:0] _231,
  output [7:0] _230,
  output [7:0] _229,
  output [7:0] _228,
  output [7:0] _227,
  output [7:0] _226,
  output [7:0] _225,
  output [7:0] _224,
  output [7:0] _255,
  output [7:0] _254,
  output [7:0] _253,
  output [7:0] _252,
  output [7:0] _251,
  output [7:0] _250,
  output [7:0] _249,
  output [7:0] _248,
  output [7:0] _247,
  output [7:0] _246,
  output [7:0] _245,
  output [7:0] _244,
  output [7:0] _243,
  output [7:0] _242,
  output [7:0] _241,
  output [7:0] _240
);

  wire cpu_decoder_4x16_1_l, cpu_decoder_4x16_1_m, cpu_decoder_4x16_1_out_3, cpu_decoder_4x16_1_out_4,
       cpu_decoder_4x16_1_out_5, cpu_decoder_4x16_1_out_6, cpu_decoder_4x16_1_out_7,
       cpu_decoder_4x16_1_out_8, cpu_decoder_4x16_1_out_9, cpu_decoder_4x16_1_out_10,
       cpu_decoder_4x16_1_out_11, cpu_decoder_4x16_1_out_12, cpu_decoder_4x16_1_out_13,
       cpu_decoder_4x16_1_out_14, cpu_decoder_4x16_1_out_15, cpu_decoder_4x16_1_out_16, cpu_decoder_4x16_2_l,
       cpu_decoder_4x16_2_m, cpu_decoder_4x16_2_out_3, cpu_decoder_4x16_2_out_4, cpu_decoder_4x16_2_out_5,
       cpu_decoder_4x16_2_out_6, cpu_decoder_4x16_2_out_7, cpu_decoder_4x16_2_out_8,
       cpu_decoder_4x16_2_out_9, cpu_decoder_4x16_2_out_10, cpu_decoder_4x16_2_out_11,
       cpu_decoder_4x16_2_out_12, cpu_decoder_4x16_2_out_13, cpu_decoder_4x16_2_out_14,
       cpu_decoder_4x16_2_out_15, cpu_decoder_4x16_2_out_16;
  wire [7:0] cpu_mem_16_1_p4, cpu_reg_byte_1_o;

  // CPU_MEM_16 cpu_mem_16_1: pin names not known; wires that end beside it: address, r, sa, cpu_mem_16_1_p4
  CPU_DECODER_4x16 cpu_decoder_4x16_1 (
    .out_13(cpu_decoder_4x16_1_out_13), .out_14(cpu_decoder_4x16_1_out_14),
    .out_15(cpu_decoder_4x16_1_out_15), .out_16(cpu_decoder_4x16_1_out_16), .M(cpu_decoder_4x16_1_m),
    .L(cpu_decoder_4x16_1_l), .out_3(cpu_decoder_4x16_1_out_3), .out_4(cpu_decoder_4x16_1_out_4),
    .out_5(cpu_decoder_4x16_1_out_5), .out_6(cpu_decoder_4x16_1_out_6), .out_7(cpu_decoder_4x16_1_out_7),
    .out_8(cpu_decoder_4x16_1_out_8), .out_9(cpu_decoder_4x16_1_out_9), .out_10(cpu_decoder_4x16_1_out_10),
    .out_11(cpu_decoder_4x16_1_out_11), .out_12(cpu_decoder_4x16_1_out_12), .in_1(cpu_mem_16_1_p4[7:4]));
  assign o = e ? cpu_reg_byte_1_o : 8'bz;  // Controlled_Buffer controlled_buffer_1
  CPU_REG_BYTE cpu_reg_byte_1 (
    .op(_15), .o(cpu_reg_byte_1_o), .h(cpu_decoder_4x16_1_l), .v(cpu_decoder_4x16_2_m), .r(r), .s(s), .e(e),
    .i(i));
  CPU_REG_BYTE cpu_reg_byte_2 (
    .op(_31), .o(cpu_reg_byte_1_o), .h(cpu_decoder_4x16_1_out_3), .v(cpu_decoder_4x16_2_m), .r(r), .s(s),
    .e(e), .i(i));
  CPU_REG_BYTE cpu_reg_byte_3 (
    .op(_47), .o(cpu_reg_byte_1_o), .h(cpu_decoder_4x16_1_out_4), .v(cpu_decoder_4x16_2_m), .r(r), .s(s),
    .e(e), .i(i));
  CPU_REG_BYTE cpu_reg_byte_4 (
    .op(_14), .o(cpu_reg_byte_1_o), .h(cpu_decoder_4x16_1_l), .v(cpu_decoder_4x16_2_out_16), .r(r), .s(s),
    .e(e), .i(i));
  CPU_REG_BYTE cpu_reg_byte_5 (
    .op(_30), .o(cpu_reg_byte_1_o), .h(cpu_decoder_4x16_1_out_3), .v(cpu_decoder_4x16_2_out_16), .r(r),
    .s(s), .e(e), .i(i));
  CPU_REG_BYTE cpu_reg_byte_6 (
    .op(_46), .o(cpu_reg_byte_1_o), .h(cpu_decoder_4x16_1_out_4), .v(cpu_decoder_4x16_2_out_16), .r(r),
    .s(s), .e(e), .i(i));
  CPU_REG_BYTE cpu_reg_byte_7 (
    .op(_13), .o(cpu_reg_byte_1_o), .h(cpu_decoder_4x16_1_l), .v(cpu_decoder_4x16_2_out_15), .r(r), .s(s),
    .e(e), .i(i));
  CPU_REG_BYTE cpu_reg_byte_8 (
    .op(_29), .o(cpu_reg_byte_1_o), .h(cpu_decoder_4x16_1_out_3), .v(cpu_decoder_4x16_2_out_15), .r(r),
    .s(s), .e(e), .i(i));
  CPU_REG_BYTE cpu_reg_byte_9 (
    .op(_45), .o(cpu_reg_byte_1_o), .h(cpu_decoder_4x16_1_out_4), .v(cpu_decoder_4x16_2_out_15), .r(r),
    .s(s), .e(e), .i(i));
  CPU_REG_BYTE cpu_reg_byte_10 (
    .op(_12), .o(cpu_reg_byte_1_o), .h(cpu_decoder_4x16_1_l), .v(cpu_decoder_4x16_2_out_14), .r(r), .s(s),
    .e(e), .i(i));
  CPU_REG_BYTE cpu_reg_byte_11 (
    .op(_28), .o(cpu_reg_byte_1_o), .h(cpu_decoder_4x16_1_out_3), .v(cpu_decoder_4x16_2_out_14), .r(r),
    .s(s), .e(e), .i(i));
  CPU_REG_BYTE cpu_reg_byte_12 (
    .op(_44), .o(cpu_reg_byte_1_o), .h(cpu_decoder_4x16_1_out_4), .v(cpu_decoder_4x16_2_out_14), .r(r),
    .s(s), .e(e), .i(i));
  CPU_REG_BYTE cpu_reg_byte_13 (
    .op(_11), .o(cpu_reg_byte_1_o), .h(cpu_decoder_4x16_1_l), .v(cpu_decoder_4x16_2_out_13), .r(r), .s(s),
    .e(e), .i(i));
  CPU_REG_BYTE cpu_reg_byte_14 (
    .op(_27), .o(cpu_reg_byte_1_o), .h(cpu_decoder_4x16_1_out_3), .v(cpu_decoder_4x16_2_out_13), .r(r),
    .s(s), .e(e), .i(i));
  CPU_REG_BYTE cpu_reg_byte_15 (
    .op(_43), .o(cpu_reg_byte_1_o), .h(cpu_decoder_4x16_1_out_4), .v(cpu_decoder_4x16_2_out_13), .r(r),
    .s(s), .e(e), .i(i));
  CPU_REG_BYTE cpu_reg_byte_16 (
    .op(_10), .o(cpu_reg_byte_1_o), .h(cpu_decoder_4x16_1_l), .v(cpu_decoder_4x16_2_out_12), .r(r), .s(s),
    .e(e), .i(i));
  CPU_REG_BYTE cpu_reg_byte_17 (
    .op(_26), .o(cpu_reg_byte_1_o), .h(cpu_decoder_4x16_1_out_3), .v(cpu_decoder_4x16_2_out_12), .r(r),
    .s(s), .e(e), .i(i));
  CPU_REG_BYTE cpu_reg_byte_18 (
    .op(_42), .o(cpu_reg_byte_1_o), .h(cpu_decoder_4x16_1_out_4), .v(cpu_decoder_4x16_2_out_12), .r(r),
    .s(s), .e(e), .i(i));
  CPU_REG_BYTE cpu_reg_byte_19 (
    .op(_9), .o(cpu_reg_byte_1_o), .h(cpu_decoder_4x16_1_l), .v(cpu_decoder_4x16_2_out_11), .r(r), .s(s),
    .e(e), .i(i));
  CPU_REG_BYTE cpu_reg_byte_20 (
    .op(_25), .o(cpu_reg_byte_1_o), .h(cpu_decoder_4x16_1_out_3), .v(cpu_decoder_4x16_2_out_11), .r(r),
    .s(s), .e(e), .i(i));
  CPU_REG_BYTE cpu_reg_byte_21 (
    .op(_41), .o(cpu_reg_byte_1_o), .h(cpu_decoder_4x16_1_out_4), .v(cpu_decoder_4x16_2_out_11), .r(r),
    .s(s), .e(e), .i(i));
  CPU_REG_BYTE cpu_reg_byte_22 (
    .op(_8), .o(cpu_reg_byte_1_o), .h(cpu_decoder_4x16_1_l), .v(cpu_decoder_4x16_2_out_10), .r(r), .s(s),
    .e(e), .i(i));
  CPU_REG_BYTE cpu_reg_byte_23 (
    .op(_24), .o(cpu_reg_byte_1_o), .h(cpu_decoder_4x16_1_out_3), .v(cpu_decoder_4x16_2_out_10), .r(r),
    .s(s), .e(e), .i(i));
  CPU_REG_BYTE cpu_reg_byte_24 (
    .op(_40), .o(cpu_reg_byte_1_o), .h(cpu_decoder_4x16_1_out_4), .v(cpu_decoder_4x16_2_out_10), .r(r),
    .s(s), .e(e), .i(i));
  CPU_DECODER_4x16 cpu_decoder_4x16_2 (
    .out_13(cpu_decoder_4x16_2_out_13), .out_14(cpu_decoder_4x16_2_out_14),
    .out_15(cpu_decoder_4x16_2_out_15), .out_16(cpu_decoder_4x16_2_out_16), .M(cpu_decoder_4x16_2_m),
    .L(cpu_decoder_4x16_2_l), .out_3(cpu_decoder_4x16_2_out_3), .out_4(cpu_decoder_4x16_2_out_4),
    .out_5(cpu_decoder_4x16_2_out_5), .out_6(cpu_decoder_4x16_2_out_6), .out_7(cpu_decoder_4x16_2_out_7),
    .out_8(cpu_decoder_4x16_2_out_8), .out_9(cpu_decoder_4x16_2_out_9), .out_10(cpu_decoder_4x16_2_out_10),
    .out_11(cpu_decoder_4x16_2_out_11), .out_12(cpu_decoder_4x16_2_out_12), .in_1(cpu_mem_16_1_p4[3:0]));
  CPU_REG_BYTE cpu_reg_byte_25 (
    .op(_7), .o(cpu_reg_byte_1_o), .h(cpu_decoder_4x16_1_l), .v(cpu_decoder_4x16_2_out_9), .r(r), .s(s),
    .e(e), .i(i));
  CPU_REG_BYTE cpu_reg_byte_26 (
    .op(_23), .o(cpu_reg_byte_1_o), .h(cpu_decoder_4x16_1_out_3), .v(cpu_decoder_4x16_2_out_9), .r(r), .s(s),
    .e(e), .i(i));
  CPU_REG_BYTE cpu_reg_byte_27 (
    .op(_39), .o(cpu_reg_byte_1_o), .h(cpu_decoder_4x16_1_out_4), .v(cpu_decoder_4x16_2_out_9), .r(r), .s(s),
    .e(e), .i(i));
  CPU_REG_BYTE cpu_reg_byte_28 (
    .op(_6), .o(cpu_reg_byte_1_o), .h(cpu_decoder_4x16_1_l), .v(cpu_decoder_4x16_2_out_8), .r(r), .s(s),
    .e(e), .i(i));
  CPU_REG_BYTE cpu_reg_byte_29 (
    .op(_22), .o(cpu_reg_byte_1_o), .h(cpu_decoder_4x16_1_out_3), .v(cpu_decoder_4x16_2_out_8), .r(r), .s(s),
    .e(e), .i(i));
  CPU_REG_BYTE cpu_reg_byte_30 (
    .op(_38), .o(cpu_reg_byte_1_o), .h(cpu_decoder_4x16_1_out_4), .v(cpu_decoder_4x16_2_out_8), .r(r), .s(s),
    .e(e), .i(i));
  CPU_REG_BYTE cpu_reg_byte_31 (
    .op(_5), .o(cpu_reg_byte_1_o), .h(cpu_decoder_4x16_1_l), .v(cpu_decoder_4x16_2_out_7), .r(r), .s(s),
    .e(e), .i(i));
  CPU_REG_BYTE cpu_reg_byte_32 (
    .op(_21_2), .o(cpu_reg_byte_1_o), .h(cpu_decoder_4x16_1_out_3), .v(cpu_decoder_4x16_2_out_7), .r(r),
    .s(s), .e(e), .i(i));
  CPU_REG_BYTE cpu_reg_byte_33 (
    .op(_37), .o(cpu_reg_byte_1_o), .h(cpu_decoder_4x16_1_out_4), .v(cpu_decoder_4x16_2_out_7), .r(r), .s(s),
    .e(e), .i(i));
  CPU_REG_BYTE cpu_reg_byte_34 (
    .op(_4), .o(cpu_reg_byte_1_o), .h(cpu_decoder_4x16_1_l), .v(cpu_decoder_4x16_2_out_6), .r(r), .s(s),
    .e(e), .i(i));
  CPU_REG_BYTE cpu_reg_byte_35 (
    .op(_20), .o(cpu_reg_byte_1_o), .h(cpu_decoder_4x16_1_out_3), .v(cpu_decoder_4x16_2_out_6), .r(r), .s(s),
    .e(e), .i(i));
  CPU_REG_BYTE cpu_reg_byte_36 (
    .op(_36), .o(cpu_reg_byte_1_o), .h(cpu_decoder_4x16_1_out_4), .v(cpu_decoder_4x16_2_out_6), .r(r), .s(s),
    .e(e), .i(i));
  CPU_REG_BYTE cpu_reg_byte_37 (
    .op(_21), .o(cpu_reg_byte_1_o), .h(cpu_decoder_4x16_1_l), .v(cpu_decoder_4x16_2_out_5), .r(r), .s(s),
    .e(e), .i(i));
  CPU_REG_BYTE cpu_reg_byte_38 (
    .op(_19), .o(cpu_reg_byte_1_o), .h(cpu_decoder_4x16_1_out_3), .v(cpu_decoder_4x16_2_out_5), .r(r), .s(s),
    .e(e), .i(i));
  CPU_REG_BYTE cpu_reg_byte_39 (
    .op(_35), .o(cpu_reg_byte_1_o), .h(cpu_decoder_4x16_1_out_4), .v(cpu_decoder_4x16_2_out_5), .r(r), .s(s),
    .e(e), .i(i));
  CPU_REG_BYTE cpu_reg_byte_40 (
    .op(_2), .o(cpu_reg_byte_1_o), .h(cpu_decoder_4x16_1_l), .v(cpu_decoder_4x16_2_out_4), .r(r), .s(s),
    .e(e), .i(i));
  CPU_REG_BYTE cpu_reg_byte_41 (
    .op(_18), .o(cpu_reg_byte_1_o), .h(cpu_decoder_4x16_1_out_3), .v(cpu_decoder_4x16_2_out_4), .r(r), .s(s),
    .e(e), .i(i));
  CPU_REG_BYTE cpu_reg_byte_42 (
    .op(_34), .o(cpu_reg_byte_1_o), .h(cpu_decoder_4x16_1_out_4), .v(cpu_decoder_4x16_2_out_4), .r(r), .s(s),
    .e(e), .i(i));
  CPU_REG_BYTE cpu_reg_byte_43 (
    .op(_1), .o(cpu_reg_byte_1_o), .h(cpu_decoder_4x16_1_l), .v(cpu_decoder_4x16_2_out_3), .r(r), .s(s),
    .e(e), .i(i));
  CPU_REG_BYTE cpu_reg_byte_44 (
    .op(_17), .o(cpu_reg_byte_1_o), .h(cpu_decoder_4x16_1_out_3), .v(cpu_decoder_4x16_2_out_3), .r(r), .s(s),
    .e(e), .i(i));
  CPU_REG_BYTE cpu_reg_byte_45 (
    .op(_33), .o(cpu_reg_byte_1_o), .h(cpu_decoder_4x16_1_out_4), .v(cpu_decoder_4x16_2_out_3), .r(r), .s(s),
    .e(e), .i(i));
  CPU_REG_BYTE cpu_reg_byte_46 (
    .op(_0), .o(cpu_reg_byte_1_o), .h(cpu_decoder_4x16_1_l), .v(cpu_decoder_4x16_2_l), .r(r), .s(s), .e(e),
    .i(i));
  CPU_REG_BYTE cpu_reg_byte_47 (
    .op(_16), .o(cpu_reg_byte_1_o), .h(cpu_decoder_4x16_1_out_3), .v(cpu_decoder_4x16_2_l), .r(r), .s(s),
    .e(e), .i(i));
  CPU_REG_BYTE cpu_reg_byte_48 (
    .op(_32), .o(cpu_reg_byte_1_o), .h(cpu_decoder_4x16_1_out_4), .v(cpu_decoder_4x16_2_l), .r(r), .s(s),
    .e(e), .i(i));
  CPU_REG_BYTE cpu_reg_byte_49 (
    .op(_48), .o(cpu_reg_byte_1_o), .h(cpu_decoder_4x16_1_out_5), .v(cpu_decoder_4x16_2_l), .r(r), .s(s),
    .e(e), .i(i));
endmodule

module CPU_NOT (
  input  [15:0] i,
  output [15:0] out_2
);

  not not_1 (out_2[0], i[0]);
  not not_2 (out_2[1], i[1]);
  not not_3 (out_2[2], i[2]);
  not not_4 (out_2[3], i[3]);
  not not_5 (out_2[4], i[4]);
  not not_6 (out_2[5], i[5]);
  not not_7 (out_2[6], i[6]);
  not not_8 (out_2[7], i[7]);
  not not_9 (out_2[8], i[8]);
  not not_10 (out_2[9], i[9]);
  not not_11 (out_2[10], i[10]);
  not not_12 (out_2[11], i[11]);
  not not_13 (out_2[12], i[12]);
  not not_14 (out_2[13], i[13]);
  not not_15 (out_2[14], i[14]);
  not not_16 (out_2[15], i[15]);
endmodule

module CPU_AND (
  input  [15:0] a,
  input  [15:0] b,
  output [15:0] o
);

  and and_1 (o[0], a[0], b[0]);
  and and_2 (o[1], a[1], b[1]);
  and and_3 (o[2], a[2], b[2]);
  and and_4 (o[3], a[3], b[3]);
  and and_5 (o[4], a[4], b[4]);
  and and_6 (o[5], a[5], b[5]);
  and and_7 (o[6], a[6], b[6]);
  and and_8 (o[7], a[7], b[7]);
  and and_9 (o[8], a[8], b[8]);
  and and_10 (o[9], a[9], b[9]);
  and and_11 (o[10], a[10], b[10]);
  and and_12 (o[11], a[11], b[11]);
  and and_13 (o[12], a[12], b[12]);
  and and_14 (o[13], a[13], b[13]);
  and and_15 (o[14], a[14], b[14]);
  and and_16 (o[15], a[15], b[15]);
endmodule

module CPU_OR (
  input  [15:0] a,
  input  [15:0] b,
  output [15:0] _0
);

  or or_1 (_0[0], a[0], b[0]);
  or or_2 (_0[1], a[1], b[1]);
  or or_3 (_0[2], a[2], b[2]);
  or or_4 (_0[3], a[3], b[3]);
  or or_5 (_0[4], a[4], b[4]);
  or or_6 (_0[5], a[5], b[5]);
  or or_7 (_0[6], a[6], b[6]);
  or or_8 (_0[7], a[7], b[7]);
  or or_9 (_0[8], a[8], b[8]);
  or or_10 (_0[9], a[9], b[9]);
  or or_11 (_0[10], a[10], b[10]);
  or or_12 (_0[11], a[11], b[11]);
  or or_13 (_0[12], a[12], b[12]);
  or or_14 (_0[13], a[13], b[13]);
  or or_15 (_0[14], a[14], b[14]);
  or or_16 (_0[15], a[15], b[15]);
endmodule

module CPU_XOR_1 (
  input  a,
  input  b,
  output o
);

  wire nand_1_out, nand_2_out, not_1_out, not_2_out;

  not not_1 (not_1_out, a);
  not not_2 (not_2_out, b);
  nand nand_1 (nand_1_out, not_1_out, b);
  nand nand_2 (nand_2_out, a, not_2_out);
  nand nand_3 (o, nand_1_out, nand_2_out);
endmodule

module CPU_SHR (
  input  [15:0] i,
  input  r,
  input  shift_in,
  output shift_out,
  output [15:0] o
);

  wire [15:1] cpu_register_16_1__0;

  CPU_REGISTER_16 cpu_register_16_1 (
    ._0({cpu_register_16_1__0, shift_out}), .i(i), .r(r), .s(1'b1), .e(1'b1));  // open: REG
  CPU_REGISTER_16 cpu_register_16_2 (
    ._0(o), .i({shift_in, cpu_register_16_1__0}), .r(r), .s(1'b1), .e(1'b1));  // open: REG
endmodule

module CPU_SHL (
  input  shift_in,
  input  [15:0] i,
  input  r,
  input  [15:0] r1,
  output [15:0] o,
  output shift_out
);

  wire [14:0] cpu_register_16_1__0;

  CPU_REGISTER_16 cpu_register_16_1 (
    ._0({shift_out, cpu_register_16_1__0}), .i(i), .r(r), .s(1'b1), .e(1'b1));  // open: REG
  CPU_REGISTER_16 cpu_register_16_2 (
    ._0(o), .i({cpu_register_16_1__0, shift_in}), .r(r), .s(1'b1), .e(1'b1));  // open: REG
endmodule

module CPU_ADDER (
  input  a,
  input  b,
  input  carry_in,
  output sum,
  output carry_out
);

  wire and_1_out, and_2_out, cpu_xor_1_1_o;

  CPU_XOR_1 cpu_xor_1_1 (.o(cpu_xor_1_1_o), .a(a), .b(b));
  and and_1 (and_1_out, carry_in, cpu_xor_1_1_o);
  and and_2 (and_2_out, a, b);
  CPU_XOR_1 cpu_xor_1_2 (.o(sum), .a(cpu_xor_1_1_o), .b(carry_in));
  or or_1 (carry_out, and_1_out, and_2_out);
endmodule

module CPU_ADDER_8 (
  input  [15:0] a,
  input  [15:0] b,
  input  carry_in,
  output carry_out,
  output [15:0] out_5
);

  wire cpu_adder_2_carry_out, cpu_adder_3_carry_out, cpu_adder_4_carry_out, cpu_adder_5_carry_out,
       cpu_adder_6_carry_out, cpu_adder_7_carry_out, cpu_adder_8_carry_out, cpu_adder_9_carry_out,
       cpu_adder_10_carry_out, cpu_adder_11_carry_out, cpu_adder_12_carry_out, cpu_adder_13_carry_out,
       cpu_adder_14_carry_out, cpu_adder_15_carry_out, cpu_adder_16_carry_out;

  CPU_ADDER cpu_adder_1 (
    .sum(out_5[15]), .carry_out(carry_out), .carry_in(cpu_adder_2_carry_out), .a(a[15]), .b(b[15]));
  CPU_ADDER cpu_adder_2 (
    .sum(out_5[14]), .carry_out(cpu_adder_2_carry_out), .carry_in(cpu_adder_3_carry_out), .a(a[14]), .b(b[14]));
  CPU_ADDER cpu_adder_3 (
    .sum(out_5[13]), .carry_out(cpu_adder_3_carry_out), .carry_in(cpu_adder_4_carry_out), .a(a[13]), .b(b[13]));
  CPU_ADDER cpu_adder_4 (
    .sum(out_5[12]), .carry_out(cpu_adder_4_carry_out), .carry_in(cpu_adder_5_carry_out), .a(a[12]), .b(b[12]));
  CPU_ADDER cpu_adder_5 (
    .sum(out_5[11]), .carry_out(cpu_adder_5_carry_out), .carry_in(cpu_adder_6_carry_out), .a(a[11]), .b(b[11]));
  CPU_ADDER cpu_adder_6 (
    .sum(out_5[10]), .carry_out(cpu_adder_6_carry_out), .carry_in(cpu_adder_7_carry_out), .a(a[10]), .b(b[10]));
  CPU_ADDER cpu_adder_7 (
    .sum(out_5[9]), .carry_out(cpu_adder_7_carry_out), .carry_in(cpu_adder_8_carry_out), .a(a[9]), .b(b[9]));
  CPU_ADDER cpu_adder_8 (
    .sum(out_5[8]), .carry_out(cpu_adder_8_carry_out), .carry_in(cpu_adder_9_carry_out), .a(a[8]), .b(b[8]));
  CPU_ADDER cpu_adder_9 (
    .sum(out_5[7]), .carry_out(cpu_adder_9_carry_out), .carry_in(cpu_adder_10_carry_out), .a(a[7]), .b(b[7]));
  CPU_ADDER cpu_adder_10 (
    .sum(out_5[6]), .carry_out(cpu_adder_10_carry_out), .carry_in(cpu_adder_11_carry_out), .a(a[6]), .b(b[6]));
  CPU_ADDER cpu_adder_11 (
    .sum(out_5[5]), .carry_out(cpu_adder_11_carry_out), .carry_in(cpu_adder_12_carry_out), .a(a[5]), .b(b[5]));
  CPU_ADDER cpu_adder_12 (
    .sum(out_5[4]), .carry_out(cpu_adder_12_carry_out), .carry_in(cpu_adder_13_carry_out), .a(a[4]), .b(b[4]));
  CPU_ADDER cpu_adder_13 (
    .sum(out_5[3]), .carry_out(cpu_adder_13_carry_out), .carry_in(cpu_adder_14_carry_out), .a(a[3]), .b(b[3]));
  CPU_ADDER cpu_adder_14 (
    .sum(out_5[2]), .carry_out(cpu_adder_14_carry_out), .carry_in(cpu_adder_15_carry_out), .a(a[2]), .b(b[2]));
  CPU_ADDER cpu_adder_15 (
    .sum(out_5[1]), .carry_out(cpu_adder_15_carry_out), .carry_in(cpu_adder_16_carry_out), .a(a[1]), .b(b[1]));
  CPU_ADDER cpu_adder_16 (.sum(out_5[0]), .carry_out(cpu_adder_16_carry_out), .carry_in(carry_in), .a(a[0]), .b(b[0]));
endmodule

module CPU_XOR_LE_1 (
  input  above_equal,
  input  a_larger,
  input  a,
  input  b,
  output c,
  output equal,
  output a_large
);

  wire and_2_out, not_1_out;

  CPU_XOR_1 cpu_xor_1_1 (.o(c), .a(a), .b(b));
  not not_1 (not_1_out, c);
  and and_1 (equal, not_1_out, above_equal);
  and and_2 (and_2_out, above_equal, a, c);
  or or_1 (a_large, and_2_out, a_larger);
endmodule

module CPU_XOR_LE_16 (
  input  [15:0] a,
  input  [15:0] b,
  output [15:0] out_3,
  output larger,
  output equal
);

  wire cpu_xor_le_1_1_a_large, cpu_xor_le_1_1_equal, cpu_xor_le_1_2_a_large, cpu_xor_le_1_2_equal,
       cpu_xor_le_1_3_a_large, cpu_xor_le_1_3_equal, cpu_xor_le_1_4_a_large, cpu_xor_le_1_4_equal,
       cpu_xor_le_1_5_a_large, cpu_xor_le_1_5_equal, cpu_xor_le_1_6_a_large, cpu_xor_le_1_6_equal,
       cpu_xor_le_1_7_a_large, cpu_xor_le_1_7_equal, cpu_xor_le_1_8_a_large, cpu_xor_le_1_8_equal,
       cpu_xor_le_1_9_a_large, cpu_xor_le_1_9_equal, cpu_xor_le_1_10_a_large, cpu_xor_le_1_10_equal,
       cpu_xor_le_1_11_a_large, cpu_xor_le_1_11_equal, cpu_xor_le_1_12_a_large, cpu_xor_le_1_12_equal,
       cpu_xor_le_1_13_a_large, cpu_xor_le_1_13_equal, cpu_xor_le_1_14_a_large, cpu_xor_le_1_14_equal,
       cpu_xor_le_1_15_a_large, cpu_xor_le_1_15_equal;

  CPU_XOR_LE_1 cpu_xor_le_1_1 (
    .equal(cpu_xor_le_1_1_equal), .a_large(cpu_xor_le_1_1_a_large), .c(out_3[0]), .a(a[15]), .b(b[15]),
    .above_equal(1'b1), .a_larger(1'b0));
  CPU_XOR_LE_1 cpu_xor_le_1_2 (
    .equal(cpu_xor_le_1_2_equal), .a_large(cpu_xor_le_1_2_a_large), .c(out_3[1]), .a(a[14]), .b(b[14]),
    .above_equal(cpu_xor_le_1_1_equal), .a_larger(cpu_xor_le_1_1_a_large));
  CPU_XOR_LE_1 cpu_xor_le_1_3 (
    .equal(cpu_xor_le_1_3_equal), .a_large(cpu_xor_le_1_3_a_large), .c(out_3[2]), .a(a[13]), .b(b[13]),
    .above_equal(cpu_xor_le_1_2_equal), .a_larger(cpu_xor_le_1_2_a_large));
  CPU_XOR_LE_1 cpu_xor_le_1_4 (
    .equal(cpu_xor_le_1_4_equal), .a_large(cpu_xor_le_1_4_a_large), .c(out_3[3]), .a(a[12]), .b(b[12]),
    .above_equal(cpu_xor_le_1_3_equal), .a_larger(cpu_xor_le_1_3_a_large));
  CPU_XOR_LE_1 cpu_xor_le_1_5 (
    .equal(cpu_xor_le_1_5_equal), .a_large(cpu_xor_le_1_5_a_large), .c(out_3[4]), .a(a[11]), .b(b[11]),
    .above_equal(cpu_xor_le_1_4_equal), .a_larger(cpu_xor_le_1_4_a_large));
  CPU_XOR_LE_1 cpu_xor_le_1_6 (
    .equal(cpu_xor_le_1_6_equal), .a_large(cpu_xor_le_1_6_a_large), .c(out_3[5]), .a(a[10]), .b(b[10]),
    .above_equal(cpu_xor_le_1_5_equal), .a_larger(cpu_xor_le_1_5_a_large));
  CPU_XOR_LE_1 cpu_xor_le_1_7 (
    .equal(cpu_xor_le_1_7_equal), .a_large(cpu_xor_le_1_7_a_large), .c(out_3[6]), .a(a[9]), .b(b[9]),
    .above_equal(cpu_xor_le_1_6_equal), .a_larger(cpu_xor_le_1_6_a_large));
  CPU_XOR_LE_1 cpu_xor_le_1_8 (
    .equal(cpu_xor_le_1_8_equal), .a_large(cpu_xor_le_1_8_a_large), .c(out_3[7]), .a(a[8]), .b(b[8]),
    .above_equal(cpu_xor_le_1_7_equal), .a_larger(cpu_xor_le_1_7_a_large));
  CPU_XOR_LE_1 cpu_xor_le_1_9 (
    .equal(cpu_xor_le_1_9_equal), .a_large(cpu_xor_le_1_9_a_large), .c(out_3[8]), .a(a[7]), .b(b[7]),
    .above_equal(cpu_xor_le_1_8_equal), .a_larger(cpu_xor_le_1_8_a_large));
  CPU_XOR_LE_1 cpu_xor_le_1_10 (
    .equal(cpu_xor_le_1_10_equal), .a_large(cpu_xor_le_1_10_a_large), .c(out_3[9]), .a(a[6]), .b(b[6]),
    .above_equal(cpu_xor_le_1_9_equal), .a_larger(cpu_xor_le_1_9_a_large));
  CPU_XOR_LE_1 cpu_xor_le_1_11 (
    .equal(cpu_xor_le_1_11_equal), .a_large(cpu_xor_le_1_11_a_large), .c(out_3[10]), .a(a[5]), .b(b[5]),
    .above_equal(cpu_xor_le_1_10_equal), .a_larger(cpu_xor_le_1_10_a_large));
  CPU_XOR_LE_1 cpu_xor_le_1_12 (
    .equal(cpu_xor_le_1_12_equal), .a_large(cpu_xor_le_1_12_a_large), .c(out_3[11]), .a(a[4]), .b(b[4]),
    .above_equal(cpu_xor_le_1_11_equal), .a_larger(cpu_xor_le_1_11_a_large));
  CPU_XOR_LE_1 cpu_xor_le_1_13 (
    .equal(cpu_xor_le_1_13_equal), .a_large(cpu_xor_le_1_13_a_large), .c(out_3[12]), .a(a[3]), .b(b[3]),
    .above_equal(cpu_xor_le_1_12_equal), .a_larger(cpu_xor_le_1_12_a_large));
  CPU_XOR_LE_1 cpu_xor_le_1_14 (
    .equal(cpu_xor_le_1_14_equal), .a_large(cpu_xor_le_1_14_a_large), .c(out_3[13]), .a(a[2]), .b(b[2]),
    .above_equal(cpu_xor_le_1_13_equal), .a_larger(cpu_xor_le_1_13_a_large));
  CPU_XOR_LE_1 cpu_xor_le_1_15 (
    .equal(cpu_xor_le_1_15_equal), .a_large(cpu_xor_le_1_15_a_large), .c(out_3[14]), .a(a[1]), .b(b[1]),
    .above_equal(cpu_xor_le_1_14_equal), .a_larger(cpu_xor_le_1_14_a_large));
  CPU_XOR_LE_1 cpu_xor_le_1_16 (
    .equal(equal), .a_large(larger), .c(out_3[15]), .a(a[0]), .b(b[0]), .above_equal(cpu_xor_le_1_15_equal),
    .a_larger(cpu_xor_le_1_15_a_large));
endmodule

module CPU_Z (
  input  [15:0] i,
  output o
);

  wire or_1_out;

  or or_1 (or_1_out, i[0], i[1], i[2], i[3], i[4], i[5], i[6], i[7], i[8], i[9], i[10], i[11], i[12], i[13], i[14], i[15]);
  not not_1 (o, or_1_out);
endmodule

module CPU_DECODER_3x8 (
  input  c,
  input  b,
  input  a,
  output [7:0] o
);

  wire not_1_out, not_2_out, not_3_out;

  not not_1 (not_1_out, a);
  not not_2 (not_2_out, b);
  not not_3 (not_3_out, c);
  and and_1 (o[0], not_3_out, not_2_out, not_1_out);
  and and_2 (o[1], not_3_out, not_2_out, a);
  and and_3 (o[2], not_3_out, b, not_1_out);
  and and_4 (o[3], not_3_out, b, a);
  and and_5 (o[4], c, not_2_out, not_1_out);
  and and_6 (o[5], c, not_2_out, a);
  and and_7 (o[6], c, b, not_1_out);
  and and_8 (o[7], c, b, a);

  // Notes on the sheet:
  //   msb
  //   lsb
endmodule

module CPU_E (
  input  [15:0] in_1,
  input  in_2,
  output [15:0] out_3
);

  wire and_1_out, and_2_out, and_3_out, and_4_out, and_5_out, and_6_out, and_7_out, and_8_out, and_9_out,
       and_10_out, and_11_out, and_12_out, and_13_out, and_14_out, and_15_out, and_16_out;

  and and_1 (and_1_out, in_1[0], in_2);
  assign out_3[0] = in_2 ? and_1_out : 1'bz;  // Controlled_Buffer controlled_buffer_1
  and and_2 (and_2_out, in_1[1], in_2);
  assign out_3[1] = in_2 ? and_2_out : 1'bz;  // Controlled_Buffer controlled_buffer_2
  and and_3 (and_3_out, in_1[2], in_2);
  assign out_3[2] = in_2 ? and_3_out : 1'bz;  // Controlled_Buffer controlled_buffer_3
  and and_4 (and_4_out, in_1[3], in_2);
  assign out_3[3] = in_2 ? and_4_out : 1'bz;  // Controlled_Buffer controlled_buffer_4
  and and_5 (and_5_out, in_1[4], in_2);
  assign out_3[4] = in_2 ? and_5_out : 1'bz;  // Controlled_Buffer controlled_buffer_5
  and and_6 (and_6_out, in_1[5], in_2);
  assign out_3[5] = in_2 ? and_6_out : 1'bz;  // Controlled_Buffer controlled_buffer_6
  and and_7 (and_7_out, in_1[6], in_2);
  assign out_3[6] = in_2 ? and_7_out : 1'bz;  // Controlled_Buffer controlled_buffer_7
  and and_8 (and_8_out, in_1[7], in_2);
  assign out_3[7] = in_2 ? and_8_out : 1'bz;  // Controlled_Buffer controlled_buffer_8
  and and_9 (and_9_out, in_1[8], in_2);
  assign out_3[8] = in_2 ? and_9_out : 1'bz;  // Controlled_Buffer controlled_buffer_9
  and and_10 (and_10_out, in_1[9], in_2);
  assign out_3[9] = in_2 ? and_10_out : 1'bz;  // Controlled_Buffer controlled_buffer_10
  and and_11 (and_11_out, in_1[10], in_2);
  assign out_3[10] = in_2 ? and_11_out : 1'bz;  // Controlled_Buffer controlled_buffer_11
  and and_12 (and_12_out, in_1[11], in_2);
  assign out_3[11] = in_2 ? and_12_out : 1'bz;  // Controlled_Buffer controlled_buffer_12
  and and_13 (and_13_out, in_1[12], in_2);
  assign out_3[12] = in_2 ? and_13_out : 1'bz;  // Controlled_Buffer controlled_buffer_13
  and and_14 (and_14_out, in_1[13], in_2);
  assign out_3[13] = in_2 ? and_14_out : 1'bz;  // Controlled_Buffer controlled_buffer_14
  and and_15 (and_15_out, in_1[14], in_2);
  assign out_3[14] = in_2 ? and_15_out : 1'bz;  // Controlled_Buffer controlled_buffer_15
  and and_16 (and_16_out, in_1[15], in_2);
  assign out_3[15] = in_2 ? and_16_out : 1'bz;  // Controlled_Buffer controlled_buffer_16
endmodule

module CPU_ALU (
  input  [15:0] a,
  input  [15:0] b_tmp,
  input  carry_in,
  input  r,
  input  d,
  input  c,
  input  b,
  input  a_2,
  output a_larger,
  output equal,
  output zero,
  output [15:0] c_2,
  output n,
  output carry_out,
  output mc,
  output ul
);

  wire adder_2_cout, and_1_out, and_2_out, and_3_out, cpu_alu_decoder_1_l, cpu_alu_decoder_1_out_3,
       cpu_alu_decoder_1_out_4, cpu_alu_decoder_1_out_5, cpu_alu_decoder_1_out_6, cpu_alu_decoder_1_out_7,
       cpu_alu_decoder_1_out_8, cpu_alu_decoder_1_out_9, cpu_alu_decoder_1_out_10, cpu_alu_decoder_1_out_11,
       cpu_alu_decoder_1_out_12, cpu_alu_decoder_1_out_13, cpu_alu_decoder_1_out_15,
       cpu_alu_decoder_1_out_16, cpu_shift_1_carry, or_1_out, subtractor_1_bout;
  wire [15:0] adder_1_out, adder_2_out, cpu_and_1_o, cpu_and_2_o, cpu_not_1_out_2, cpu_or_1__0,
       cpu_shift_1_op, cpu_xor_le_16_1_out_3, divider_1_out, multiplier_1_out, subtractor_1_out,
       subtractor_2_out;

  CPU_AND cpu_and_1 (.o(cpu_and_1_o), .a({16{1'b0}}), .b(a));
  Subtractor #(.width(16)) subtractor_1 (
    .a(a), .b(b_tmp), .out(subtractor_1_out), .bin(1'b0), .bout(subtractor_1_bout));
  Comparator #(.width(16)) comparator_1 (.a(a), .b(b_tmp), .gt(a_larger), .eq(equal));  // open: lt
  Divider #(.width(16)) divider_1 (.a(a), .b(b_tmp), .out(divider_1_out));  // open: upper, rem
  Multiplier #(.width(16)) multiplier_1 (.a(a), .b(b_tmp), .out(multiplier_1_out));  // open: cin, cout
  Subtractor #(.width(16)) subtractor_2 (.a(a), .b(16'h1), .out(subtractor_2_out));  // open: bin, bout
  Adder #(.width(16)) adder_1 (.a(a), .b(16'h1), .out(adder_1_out));  // open: cin, cout
  CPU_XOR_LE_16 cpu_xor_le_16_1 (.out_3(cpu_xor_le_16_1_out_3), .b(b_tmp), .a(a));  // open: larger, equal
  CPU_OR cpu_or_1 (._0(cpu_or_1__0), .a(a), .b(b_tmp));
  CPU_AND cpu_and_2 (.o(cpu_and_2_o), .a(a), .b(b_tmp));
  CPU_NOT cpu_not_1 (.out_2(cpu_not_1_out_2), .i(a));
  Adder #(.width(16)) adder_2 (.a(a), .b(b_tmp), .out(adder_2_out), .cin(1'b0), .cout(adder_2_cout));
  CPU_SHIFT cpu_shift_1 (
    .op(cpu_shift_1_op), .carry(cpu_shift_1_carry), .carry_in(1'b0), .i(b_tmp), .LRcount(a),
    .R(cpu_alu_decoder_1_out_3), .L(cpu_alu_decoder_1_out_4));
  CPU_ALU_DECODER cpu_alu_decoder_1 (
    .out_13(cpu_alu_decoder_1_out_13), .out_14(ul), .out_15(cpu_alu_decoder_1_out_15),
    .out_16(cpu_alu_decoder_1_out_16), .M(mc), .L(cpu_alu_decoder_1_l), .out_3(cpu_alu_decoder_1_out_3),
    .out_4(cpu_alu_decoder_1_out_4), .out_5(cpu_alu_decoder_1_out_5), .out_6(cpu_alu_decoder_1_out_6),
    .out_7(cpu_alu_decoder_1_out_7), .out_8(cpu_alu_decoder_1_out_8), .out_9(cpu_alu_decoder_1_out_9),
    .out_10(cpu_alu_decoder_1_out_10), .out_11(cpu_alu_decoder_1_out_11), .out_12(cpu_alu_decoder_1_out_12),
    .in_1({d, c, b, a_2}));
  assign c_2 = cpu_alu_decoder_1_out_9 ? a : 16'bz;  // Controlled_Buffer controlled_buffer_1
  or or_1 (or_1_out, cpu_alu_decoder_1_out_4, cpu_alu_decoder_1_out_3);
  CPU_E cpu_e_1 (.out_3(c_2), .in_1(cpu_and_1_o), .in_2(cpu_alu_decoder_1_out_16));
  CPU_E cpu_e_2 (.out_3(c_2), .in_1(subtractor_1_out), .in_2(cpu_alu_decoder_1_out_15));
  CPU_E cpu_e_3 (.out_3(c_2), .in_1(divider_1_out), .in_2(cpu_alu_decoder_1_out_13));
  CPU_E cpu_e_4 (.out_3(c_2), .in_1(multiplier_1_out), .in_2(cpu_alu_decoder_1_out_12));
  CPU_E cpu_e_5 (.out_3(c_2), .in_1(subtractor_2_out), .in_2(cpu_alu_decoder_1_out_11));
  CPU_E cpu_e_6 (.out_3(c_2), .in_1(adder_1_out), .in_2(cpu_alu_decoder_1_out_10));
  CPU_E cpu_e_7 (.out_3(c_2), .in_1(cpu_xor_le_16_1_out_3), .in_2(cpu_alu_decoder_1_out_8));
  CPU_E cpu_e_8 (.out_3(c_2), .in_1(cpu_or_1__0), .in_2(cpu_alu_decoder_1_out_7));
  CPU_E cpu_e_9 (.out_3(c_2), .in_1(cpu_and_2_o), .in_2(cpu_alu_decoder_1_out_6));
  CPU_E cpu_e_10 (.out_3(c_2), .in_1(cpu_not_1_out_2), .in_2(cpu_alu_decoder_1_out_5));
  CPU_E cpu_e_11 (.out_3(c_2), .in_1(cpu_shift_1_op), .in_2(or_1_out));
  CPU_E cpu_e_12 (.out_3(c_2), .in_1(adder_2_out), .in_2(cpu_alu_decoder_1_l));
  and and_1 (and_1_out, subtractor_1_bout, cpu_alu_decoder_1_out_15);
  assign carry_out = cpu_alu_decoder_1_out_15 ? and_1_out : 1'bz;  // Controlled_Buffer controlled_buffer_2
  and and_2 (and_2_out, cpu_shift_1_carry, or_1_out);
  assign carry_out = or_1_out ? and_2_out : 1'bz;  // Controlled_Buffer controlled_buffer_3
  and and_3 (and_3_out, adder_2_cout, cpu_alu_decoder_1_l);
  assign carry_out = cpu_alu_decoder_1_l ? and_3_out : 1'bz;  // Controlled_Buffer controlled_buffer_4
  Pull_Resistor pull_resistor_1 (.node(carry_out));
  Pull_Resistor pull_resistor_2 (.node(c_2));
  CPU_Z cpu_z_1 (.o(zero), .i(c_2));

  assign n = c_2[15];

  // Notes on the sheet:
  //   dec
  //   inc
endmodule

module CPU_BUS_1 (
  input  [15:0] i,
  input  bus_1,
  output [15:0] o
);

  wire not_1_out;

  and and_1 (o[15], i[15], not_1_out);
  and and_2 (o[14], i[14], not_1_out);
  and and_3 (o[13], i[13], not_1_out);
  and and_4 (o[12], i[12], not_1_out);
  and and_5 (o[11], i[11], not_1_out);
  and and_6 (o[10], i[10], not_1_out);
  and and_7 (o[9], i[9], not_1_out);
  and and_8 (o[8], i[8], not_1_out);
  and and_9 (o[7], i[7], not_1_out);
  and and_10 (o[6], i[6], not_1_out);
  and and_11 (o[5], i[5], not_1_out);
  and and_12 (o[4], i[4], not_1_out);
  and and_13 (o[3], i[3], not_1_out);
  and and_14 (o[2], i[2], not_1_out);
  and and_15 (o[1], i[1], not_1_out);
  or or_1 (o[0], i[0], bus_1);
  not not_1 (not_1_out, bus_1);
endmodule

module CPU_ACCUMULATOR (
  input  [15:0] i,
  input  r,
  input  s,
  input  e,
  output [15:0] ACC,
  output [15:0] o
);

  CPU_REGISTER_16 cpu_register_16_1 (.REG(ACC), ._0(o), .i(i), .r(r), .s(s), .e(e));
endmodule

module CPU_R (
  input  [15:0] i,
  input  r,
  input  s,
  input  e,
  output [15:0] \reg ,
  output [15:0] o
);

  CPU_REGISTER_16 cpu_register_16_1 (.REG(\reg ), ._0(o), .i(i), .r(r), .s(s), .e(e));
endmodule

module CPU_TMP (
  input  [15:0] i,
  input  r,
  input  s,
  output [15:0] o
);

  wire [15:0] controlled_buffer_1_out;

  assign controlled_buffer_1_out = s ? i : 16'bz;  // Controlled_Buffer controlled_buffer_1
  CPU_MEM_16 cpu_mem_16_1 (.out_4(o), .in_1(controlled_buffer_1_out), .r(r), .s(s));
endmodule

module CPU_STEPPER (
  input  clks,
  input  reset,
  input  st,
  input  clk,
  output f_e,
  output [7:0] execute,
  output step_1,
  output step_1_2,
  output step_1_3,
  output step_2,
  output step_3,
  output step_4,
  output step_5,
  output step_6,
  output step_7,
  output step_8,
  output step_9,
  output step_10,
  output step_11,
  output step_12,
  output step_13,
  output step_14,
  output step_15,
  output step_17,
  output step_18
);

  wire cpu_step_mem_1_out_3, cpu_step_mem_2_out_3, cpu_step_mem_3_out_3, cpu_step_mem_4_out_3,
       cpu_step_mem_5_out_3, cpu_step_mem_6_out_3, cpu_step_mem_7_out_3, cpu_step_mem_8_out_3,
       cpu_step_mem_9_out_3, cpu_step_mem_10_out_3, cpu_step_mem_11_out_3, cpu_step_mem_12_out_3,
       cpu_step_mem_13_out_3, cpu_step_mem_14_out_3, cpu_step_mem_15_out_3, cpu_step_mem_16_out_3,
       cpu_step_mem_17_out_3, cpu_step_mem_18_out_3, cpu_step_mem_19_out_3, cpu_step_mem_20_out_3,
       cpu_step_mem_21_out_3, cpu_step_mem_22_out_3, cpu_step_mem_23_out_3, cpu_step_mem_24_out_3,
       cpu_step_mem_25_out_3, cpu_step_mem_26_out_3, cpu_step_mem_27_out_3, cpu_step_mem_28_out_3,
       cpu_step_mem_29_out_3, cpu_step_mem_30_out_3, cpu_step_mem_31_out_3, cpu_step_mem_32_out_3,
       cpu_step_mem_33_out_3, cpu_step_mem_34_out_3, cpu_step_mem_35_out_3, cpu_step_mem_36_out_3,
       cpu_step_mem_37_out_3, cpu_step_mem_38_out_3, nor_1_out, not_1_out, not_2_out, not_3_out, not_4_out,
       not_5_out, not_6_out, not_7_out, not_8_out, not_9_out, not_10_out, not_11_out, not_12_out, not_13_out,
       not_14_out, not_15_out, not_16_out, not_17_out, not_18_out, not_19_out, not_20_out, not_21_out,
       or_1_out, or_2_out, or_3_out;

  or or_1 (or_1_out, reset, st, cpu_step_mem_38_out_3);
  not not_1 (not_1_out, clk);
  Counter #(.max('hf), .trigger("falling"), .width(4)) counter_1 (
    .load(1'b0), .count(1'b1), .Q(execute[3:0]), .up(1'b1), .clk(clk), .clr(step_3));  // open: D, carry
  not not_2 (not_2_out, or_1_out);
  or or_2 (or_2_out, or_1_out, clk);
  or or_3 (or_3_out, or_1_out, not_1_out);
  or or_4 (step_1_3, or_1_out, not_3_out);
  CPU_STEP_MEM cpu_step_mem_1 (.out_3(cpu_step_mem_1_out_3), .in_1(not_2_out), .in_2(or_2_out));
  not not_3 (not_3_out, cpu_step_mem_2_out_3);
  CPU_STEP_MEM cpu_step_mem_2 (.out_3(cpu_step_mem_2_out_3), .in_1(cpu_step_mem_1_out_3), .in_2(or_3_out));
  and and_1 (step_2, cpu_step_mem_2_out_3, not_4_out);
  nor nor_1 (nor_1_out, step_1_3, step_2, step_3);
  not not_4 (not_4_out, cpu_step_mem_4_out_3);
  CPU_STEP_MEM cpu_step_mem_3 (.out_3(cpu_step_mem_3_out_3), .in_1(cpu_step_mem_2_out_3), .in_2(or_2_out));
  CPU_STEP_MEM cpu_step_mem_4 (.out_3(cpu_step_mem_4_out_3), .in_1(cpu_step_mem_3_out_3), .in_2(or_3_out));
  and and_2 (step_3, cpu_step_mem_4_out_3, not_5_out);
  CPU_STEP_MEM cpu_step_mem_5 (.out_3(cpu_step_mem_5_out_3), .in_1(cpu_step_mem_4_out_3), .in_2(or_2_out));
  not not_5 (not_5_out, cpu_step_mem_6_out_3);
  CPU_STEP_MEM cpu_step_mem_6 (.out_3(cpu_step_mem_6_out_3), .in_1(cpu_step_mem_5_out_3), .in_2(or_3_out));
  and and_3 (step_4, cpu_step_mem_6_out_3, not_6_out);
  CPU_MEM_1 cpu_mem_1_1 (.out_4(f_e), .in_1(nor_1_out), .in_2(clks), .r(reset));
  not not_6 (not_6_out, cpu_step_mem_8_out_3);
  CPU_STEP_MEM cpu_step_mem_7 (.out_3(cpu_step_mem_7_out_3), .in_1(cpu_step_mem_6_out_3), .in_2(or_2_out));
  and and_4 (step_5, cpu_step_mem_8_out_3, not_7_out);
  CPU_STEP_MEM cpu_step_mem_8 (.out_3(cpu_step_mem_8_out_3), .in_1(cpu_step_mem_7_out_3), .in_2(or_3_out));
  not not_7 (not_7_out, cpu_step_mem_10_out_3);
  CPU_STEP_MEM cpu_step_mem_9 (.out_3(cpu_step_mem_9_out_3), .in_1(cpu_step_mem_8_out_3), .in_2(or_2_out));
  CPU_STEP_MEM cpu_step_mem_10 (.out_3(cpu_step_mem_10_out_3), .in_1(cpu_step_mem_9_out_3), .in_2(or_3_out));
  and and_5 (step_6, cpu_step_mem_10_out_3, not_8_out);
  CPU_STEP_MEM cpu_step_mem_11 (.out_3(cpu_step_mem_11_out_3), .in_1(cpu_step_mem_10_out_3), .in_2(or_2_out));
  not not_8 (not_8_out, cpu_step_mem_12_out_3);
  CPU_STEP_MEM cpu_step_mem_12 (.out_3(cpu_step_mem_12_out_3), .in_1(cpu_step_mem_11_out_3), .in_2(or_3_out));
  and and_6 (step_7, cpu_step_mem_12_out_3, not_9_out);
  not not_9 (not_9_out, cpu_step_mem_14_out_3);
  CPU_STEP_MEM cpu_step_mem_13 (.out_3(cpu_step_mem_13_out_3), .in_1(cpu_step_mem_12_out_3), .in_2(or_2_out));
  CPU_STEP_MEM cpu_step_mem_14 (.out_3(cpu_step_mem_14_out_3), .in_1(cpu_step_mem_13_out_3), .in_2(or_3_out));
  and and_7 (step_8, cpu_step_mem_14_out_3, not_10_out);
  CPU_STEP_MEM cpu_step_mem_15 (.out_3(cpu_step_mem_15_out_3), .in_1(cpu_step_mem_14_out_3), .in_2(or_2_out));
  not not_10 (not_10_out, cpu_step_mem_16_out_3);
  CPU_STEP_MEM cpu_step_mem_16 (.out_3(cpu_step_mem_16_out_3), .in_1(cpu_step_mem_15_out_3), .in_2(or_3_out));
  and and_8 (step_9, cpu_step_mem_16_out_3, not_11_out);
  not not_11 (not_11_out, cpu_step_mem_18_out_3);
  CPU_STEP_MEM cpu_step_mem_17 (.out_3(cpu_step_mem_17_out_3), .in_1(cpu_step_mem_16_out_3), .in_2(or_2_out));
  and and_9 (step_10, cpu_step_mem_18_out_3, not_12_out);
  CPU_STEP_MEM cpu_step_mem_18 (.out_3(cpu_step_mem_18_out_3), .in_1(cpu_step_mem_17_out_3), .in_2(or_3_out));
  not not_12 (not_12_out, cpu_step_mem_20_out_3);
  CPU_STEP_MEM cpu_step_mem_19 (.out_3(cpu_step_mem_19_out_3), .in_1(cpu_step_mem_18_out_3), .in_2(or_2_out));
  CPU_STEP_MEM cpu_step_mem_20 (.out_3(cpu_step_mem_20_out_3), .in_1(cpu_step_mem_19_out_3), .in_2(or_3_out));
  and and_10 (step_11, cpu_step_mem_20_out_3, not_13_out);
  CPU_STEP_MEM cpu_step_mem_21 (.out_3(cpu_step_mem_21_out_3), .in_1(cpu_step_mem_20_out_3), .in_2(or_2_out));
  not not_13 (not_13_out, cpu_step_mem_22_out_3);
  CPU_STEP_MEM cpu_step_mem_22 (.out_3(cpu_step_mem_22_out_3), .in_1(cpu_step_mem_21_out_3), .in_2(or_3_out));
  and and_11 (step_12, cpu_step_mem_22_out_3, not_14_out);
  CPU_STEP_MEM cpu_step_mem_23 (.out_3(cpu_step_mem_23_out_3), .in_1(cpu_step_mem_22_out_3), .in_2(or_2_out));
  not not_14 (not_14_out, cpu_step_mem_24_out_3);
  CPU_STEP_MEM cpu_step_mem_24 (.out_3(cpu_step_mem_24_out_3), .in_1(cpu_step_mem_23_out_3), .in_2(or_3_out));
  and and_12 (step_13, cpu_step_mem_24_out_3, not_15_out);
  CPU_STEP_MEM cpu_step_mem_25 (.out_3(cpu_step_mem_25_out_3), .in_1(cpu_step_mem_24_out_3), .in_2(or_2_out));
  not not_15 (not_15_out, cpu_step_mem_26_out_3);
  CPU_STEP_MEM cpu_step_mem_26 (.out_3(cpu_step_mem_26_out_3), .in_1(cpu_step_mem_25_out_3), .in_2(or_3_out));
  and and_13 (step_14, cpu_step_mem_26_out_3, not_16_out);
  not not_16 (not_16_out, cpu_step_mem_28_out_3);
  CPU_STEP_MEM cpu_step_mem_27 (.out_3(cpu_step_mem_27_out_3), .in_1(cpu_step_mem_26_out_3), .in_2(or_2_out));
  and and_14 (step_15, cpu_step_mem_28_out_3, not_17_out);
  CPU_STEP_MEM cpu_step_mem_28 (.out_3(cpu_step_mem_28_out_3), .in_1(cpu_step_mem_27_out_3), .in_2(or_3_out));
  CPU_STEP_MEM cpu_step_mem_29 (.out_3(cpu_step_mem_29_out_3), .in_1(cpu_step_mem_28_out_3), .in_2(or_2_out));
  not not_17 (not_17_out, cpu_step_mem_30_out_3);
  CPU_STEP_MEM cpu_step_mem_30 (.out_3(cpu_step_mem_30_out_3), .in_1(cpu_step_mem_29_out_3), .in_2(or_3_out));
  and and_15 (step_1, cpu_step_mem_30_out_3, not_18_out);
  not not_18 (not_18_out, cpu_step_mem_32_out_3);
  CPU_STEP_MEM cpu_step_mem_31 (.out_3(cpu_step_mem_31_out_3), .in_1(cpu_step_mem_30_out_3), .in_2(or_2_out));
  CPU_STEP_MEM cpu_step_mem_32 (.out_3(cpu_step_mem_32_out_3), .in_1(cpu_step_mem_31_out_3), .in_2(or_3_out));
  and and_16 (step_17, cpu_step_mem_32_out_3, not_19_out);
  not not_19 (not_19_out, cpu_step_mem_34_out_3);
  CPU_STEP_MEM cpu_step_mem_33 (.out_3(cpu_step_mem_33_out_3), .in_1(cpu_step_mem_32_out_3), .in_2(or_2_out));
  and and_17 (step_18, cpu_step_mem_34_out_3, not_20_out);
  CPU_STEP_MEM cpu_step_mem_34 (.out_3(cpu_step_mem_34_out_3), .in_1(cpu_step_mem_33_out_3), .in_2(or_3_out));
  CPU_STEP_MEM cpu_step_mem_35 (.out_3(cpu_step_mem_35_out_3), .in_1(cpu_step_mem_34_out_3), .in_2(or_2_out));
  not not_20 (not_20_out, cpu_step_mem_36_out_3);
  CPU_STEP_MEM cpu_step_mem_36 (.out_3(cpu_step_mem_36_out_3), .in_1(cpu_step_mem_35_out_3), .in_2(or_3_out));
  and and_18 (step_1_2, cpu_step_mem_36_out_3, not_21_out);
  not not_21 (not_21_out, cpu_step_mem_38_out_3);
  CPU_STEP_MEM cpu_step_mem_37 (.out_3(cpu_step_mem_37_out_3), .in_1(cpu_step_mem_36_out_3), .in_2(or_2_out));
  CPU_STEP_MEM cpu_step_mem_38 (.out_3(cpu_step_mem_38_out_3), .in_1(cpu_step_mem_37_out_3), .in_2(or_3_out));

  assign execute[7:4] = 4'b0000;
endmodule

module CPU (
  input  clock,
  input  r,
  input  [15:0] DATA_BUS_IN,
  input  W,
  output [15:0] R0,
  output [15:0] R1,
  output [15:0] R2,
  output [15:0] R3,
  output [15:0] R4,
  output [15:0] R5,
  output [15:0] R6_TMP,
  output [15:0] SP,
  output [15:0] INDEX,
  output [15:0] FU,
  output clkl,
  output clke,
  output clks,
  output STOP,
  output mc,
  output mc_2,
  output END,
  output [1:0] CNTRL_BUS,
  output [15:0] out_23,
  output [15:0] out_24,
  output [15:0] ADDR_BUS,
  output [5:0] FLAGS,
  output [15:0] DATA_BUS_OUT
);

  wire and_1_out, B, C, cpu_alu_1_a_larger, cpu_alu_1_carry_out, cpu_alu_1_equal, cpu_alu_1_n,
       cpu_alu_1_zero, cpu_carry_temp_1_o, cpu_control_section_1_acc_e, cpu_control_section_1_acc_s,
       cpu_control_section_1_alu_0, cpu_control_section_1_alu_1, cpu_control_section_1_alu_2,
       cpu_control_section_1_alu_3, cpu_control_section_1_flag_e, cpu_control_section_1_flags_s,
       cpu_control_section_1_iar_e, cpu_control_section_1_iar_s, cpu_control_section_1_ir_e,
       cpu_control_section_1_ir_s, fue, fus, lre, lrs, MARS, not_1_out, r1e, r1s, r2e, r2s, r3e, r3s, r4e,
       r4s, r5e, r5s, r6tmpe, r6tmps, roe, ros, sp_e, sp_s, TS;
  wire [15:0] cpu_accumulator_1_acc, cpu_alu_1_c_2, cpu_bus_1_1_o, cpu_tmp_1_o;

  // Probe on cpu_accumulator_1_acc
  CPU_ACCUMULATOR cpu_accumulator_1 (
    .ACC(cpu_accumulator_1_acc), .o(DATA_BUS_IN), .i(cpu_alu_1_c_2), .r(r), .s(cpu_control_section_1_acc_s),
    .e(cpu_control_section_1_acc_e));
  CPU_TMP cpu_tmp_1 (.o(cpu_tmp_1_o), .i(DATA_BUS_IN), .r(r), .s(TS));
  CPU_BUS_1 cpu_bus_1_1 (.o(cpu_bus_1_1_o), .bus_1(B), .i(cpu_tmp_1_o));
  CPU_ALU cpu_alu_1 (
    .c_2(cpu_alu_1_c_2), .carry_out(cpu_alu_1_carry_out), .a_larger(cpu_alu_1_a_larger),
    .equal(cpu_alu_1_equal), .zero(cpu_alu_1_zero), .n(cpu_alu_1_n), .mc(mc_2), .ul(mc), .r(r),
    .a(DATA_BUS_IN), .b_tmp(cpu_bus_1_1_o), .carry_in(FLAGS[5]), .d(cpu_control_section_1_alu_3),
    .c(cpu_control_section_1_alu_2), .b(cpu_control_section_1_alu_1), .a_2(cpu_control_section_1_alu_0));
  CPU_R cpu_r_1 (.\reg (R0), .o(DATA_BUS_IN), .i(DATA_BUS_IN), .r(r), .s(ros), .e(roe));
  not not_1 (not_1_out, END);
  and and_1 (and_1_out, not_1_out, clock);
  and and_2 (FLAGS[5], C, cpu_carry_temp_1_o);
  CPU_CLK cpu_clk_1 (.clk(clkl), .clks(clks), .clke(clke), .clkin(and_1_out));
  CPU_CARRY_TEMP cpu_carry_temp_1 (.o(cpu_carry_temp_1_o), .c(FLAGS[3]), .r(r), .s(TS));
  CPU_R cpu_r_2 (.\reg (R1), .o(DATA_BUS_IN), .i(DATA_BUS_IN), .r(r), .s(r1s), .e(r1e));
  CPU_FLAGS cpu_flags_1 (
    .C_2(FLAGS[3]), .A_2(FLAGS[2]), .E_3(FLAGS[1]), .Z_2(FLAGS[0]), .N_2(FLAGS[4]), .op(DATA_BUS_IN),
    .C(cpu_alu_1_carry_out), .A(cpu_alu_1_a_larger), .E(cpu_alu_1_equal), .Z(cpu_alu_1_zero),
    .N(cpu_alu_1_n), .r(r), .s(cpu_control_section_1_flags_s), .e_2(cpu_control_section_1_flag_e));
  CPU_R cpu_r_3 (.\reg (R2), .o(DATA_BUS_IN), .i(DATA_BUS_IN), .r(r), .s(r2s), .e(r2e));
  CPU_CONTROL_SECTION cpu_control_section_1 (
    .R3_E(r3e), .R2_E(r2e), .R1_E(r1e), .R0_E(roe), .ALU_2(cpu_control_section_1_alu_2),
    .ALU_3(cpu_control_section_1_alu_3), .BUS_1(B), .ACC_E(cpu_control_section_1_acc_e),
    .IR_E(cpu_control_section_1_ir_e), .IAR_E(cpu_control_section_1_iar_e), .CNTRL_E(CNTRL_BUS[0]),
    .R6_TMP_E(r6tmpe), .FLAG_E(cpu_control_section_1_flag_e), .STACK_E(sp_e), .INDEX_E(lre), .FPU_E(fue),
    .R5_E(r5e), .R4_E(r4e), .STOP(STOP), .END(END), .R3_S(r3s), .R2_S(r2s), .R1_S(r1s), .R0_S(ros),
    .ALU_1(cpu_control_section_1_alu_1), .ALU_0(cpu_control_section_1_alu_0), .C_2(C), .MAR_S(MARS),
    .ACC_S(cpu_control_section_1_acc_s), .IR_S(cpu_control_section_1_ir_s),
    .IAR_S(cpu_control_section_1_iar_s), .CNTRL_S(CNTRL_BUS[1]), .TMP_S(TS), .R6_TMP_S(r6tmps),
    .FLAGS_S(cpu_control_section_1_flags_s), .STACK_S(sp_s), .INDEX_S(lrs), .FPU_S(fus), .R5_S(r5s),
    .R4_S(r4s), .clks(clks), .clke(clke), .C(FLAGS[3]), .A(FLAGS[2]), .E(FLAGS[1]), .Z(FLAGS[0]),
    .N(FLAGS[4]), .r(r), .clk(clkl), .IR_IN(out_23));
  CPU_R cpu_r_4 (.\reg (R3), .o(DATA_BUS_IN), .i(DATA_BUS_IN), .r(r), .s(r3s), .e(r3e));
  CPU_R cpu_r_5 (.\reg (R4), .o(DATA_BUS_IN), .i(DATA_BUS_IN), .r(r), .s(r4s), .e(r4e));
  CPU_R cpu_r_6 (.\reg (R5), .o(DATA_BUS_IN), .i(DATA_BUS_IN), .r(r), .s(r5s), .e(r5e));
  CPU_IAR cpu_iar_1 (
    .IAR(out_24), .o(DATA_BUS_IN), .i(DATA_BUS_IN), .W(W), .r(r), .s(cpu_control_section_1_iar_s),
    .e(cpu_control_section_1_iar_e));
  CPU_R cpu_r_7 (.\reg (R6_TMP), .o(DATA_BUS_IN), .i(DATA_BUS_IN), .r(r), .s(r6tmps), .e(r6tmpe));
  CPU_IR cpu_ir_1 (
    .o(out_23), .en_o(DATA_BUS_IN), .r(r), .i(DATA_BUS_IN), .s(cpu_control_section_1_ir_s),
    .e(cpu_control_section_1_ir_e));
  CPU_R cpu_r_8 (.\reg (SP), .o(DATA_BUS_IN), .i(DATA_BUS_IN), .r(r), .s(sp_s), .e(sp_e));
  CPU_REGISTER_16 cpu_register_16_1 (._0(ADDR_BUS), .i(DATA_BUS_IN), .r(r), .s(MARS), .e(1'b1));  // open: REG
  CPU_R cpu_r_9 (.\reg (INDEX), .o(DATA_BUS_IN), .i(DATA_BUS_IN), .r(r), .s(lrs), .e(lre));
  CPU_R cpu_r_10 (.\reg (FU), .o(DATA_BUS_IN), .i(DATA_BUS_IN), .r(r), .s(fus), .e(fue));

  assign DATA_BUS_OUT = DATA_BUS_IN;
endmodule

module CPU_IAR (
  input  [15:0] i,
  input  r,
  input  W,
  input  s,
  input  e,
  output [15:0] IAR,
  output [15:0] o
);

  wire not_1_out;
  wire [15:0] controlled_buffer_1_out;

  assign controlled_buffer_1_out = not_1_out ? i : 16'bz;  // Controlled_Buffer controlled_buffer_1
  not not_1 (not_1_out, W);
  CPU_REGISTER_16 cpu_register_16_1 (.REG(IAR), ._0(o), .i(controlled_buffer_1_out), .r(r), .s(s), .e(e));
endmodule

module CPU_IR (
  input  [15:0] i,
  input  r,
  input  s,
  input  e,
  output [15:0] o,
  output [15:0] en_o
);

  CPU_MEM_16 cpu_mem_16_1 (.out_4(o), .in_1(i), .r(r), .s(s));
  CPU_ENABLE_16 cpu_enable_16_1 (.out_3(en_o), .in_1(o), .in_2(e));
endmodule

module CPU_FLAGS (
  input  C,
  input  A,
  input  E,
  input  Z,
  input  N,
  input  r,
  input  s,
  input  e_2,
  output C_2,
  output A_2,
  output E_3,
  output Z_2,
  output N_2,
  output [15:0] op
);

  CPU_MEM_1 cpu_mem_1_1 (.out_4(C_2), .in_1(C), .in_2(s), .r(r));
  CPU_MEM_1 cpu_mem_1_2 (.out_4(A_2), .in_1(A), .in_2(s), .r(r));
  CPU_MEM_1 cpu_mem_1_3 (.out_4(E_3), .in_1(E), .in_2(s), .r(r));
  CPU_MEM_1 cpu_mem_1_4 (.out_4(Z_2), .in_1(Z), .in_2(s), .r(r));
  CPU_MEM_1 cpu_mem_1_5 (.out_4(N_2), .in_1(N), .in_2(s), .r(r));
  CPU_ENABLE_16 cpu_enable_16_1 (.out_3(op), .in_1({{11{1'b0}}, N_2, Z_2, E_3, A_2, C_2}), .in_2(e_2));
endmodule

module CPU_CONTROL_SECTION (
  input  clks,
  input  clke,
  input  r,
  input  clk,
  input  C,
  input  A,
  input  E,
  input  Z,
  input  N,
  input  [15:0] IR_IN,
  output ALU_2,
  output ALU_1,
  output ALU_3,
  output ALU_0,
  output C_2,
  output BUS_1,
  output MAR_S,
  output ACC_S,
  output ACC_E,
  output IR_S,
  output IR_E,
  output IAR_S,
  output IAR_E,
  output CNTRL_S,
  output CNTRL_E,
  output TMP_S,
  output R6_TMP_E,
  output R6_TMP_S,
  output FLAGS_S,
  output FLAG_E,
  output STACK_S,
  output STACK_E,
  output INDEX_S,
  output INDEX_E,
  output FPU_S,
  output FPU_E,
  output R5_E,
  output R5_S,
  output R4_E,
  output R4_S,
  output R3_E,
  output R3_S,
  output R2_E,
  output R2_S,
  output R1_E,
  output R1_S,
  output R0_E,
  output R0_S,
  output STOP,
  output END
);

  wire _3, Ae, and_18_out, As, Be, Bs, cpu_4x16_control_1_ch, cpu_stepper_1_step_1_3, cpu_stepper_1_step_2,
       cpu_stepper_1_step_3, cpu_ucode_rom_1_op_3, cpu_ucode_rom_1_op_4, cpu_ucode_rom_1_op_5,
       cpu_ucode_rom_1_op_6, cpu_ucode_rom_1_op_7, cpu_ucode_rom_1_op_8, cpu_ucode_rom_1_op_9,
       cpu_ucode_rom_1_op_10, cpu_ucode_rom_1_op_11, cpu_ucode_rom_1_op_12, cpu_ucode_rom_1_op_18,
       cpu_ucode_rom_1_op_19, cpu_ucode_rom_1_op_20, cpu_ucode_rom_1_op_21, cpu_ucode_rom_1_op_22,
       cpu_ucode_rom_1_op_23, cpu_ucode_rom_1_op_24, cpu_ucode_rom_1_op_25, cpu_ucode_rom_1_op_26,
       cpu_ucode_rom_1_op_27, cpu_ucode_rom_1_op_28, f_e, JI, not_1_out, not_2_out, not_3_out, or_1_out,
       or_2_out, or_3_out, or_4_out, or_5_out, or_6_out, or_7_out, or_8_out, or_9_out, or_10_out, or_11_out,
       or_12_out, or_13_out, or_14_out, or_15_out, or_16_out, or_17_out, or_18_out, or_19_out;
  wire [7:0] execute;
  wire [15:0] cpu_ucode_decoder_1_op, cpu_ucode_decoder_2_op, RA_RB_E, RA_RB_S;

  and and_1 (BUS_1, or_1_out, clke);
  and and_2 (ACC_E, or_2_out, clke);
  and and_3 (IR_E, or_3_out, clke);
  and and_4 (IAR_E, or_4_out, clke);
  and and_5 (CNTRL_E, or_5_out, clke);
  and and_6 (R6_TMP_E, cpu_ucode_rom_1_op_7, clke);
  and and_7 (FLAG_E, or_6_out, clke);
  and and_8 (STACK_E, or_7_out, clke);
  and and_9 (INDEX_E, or_8_out, clke);
  and and_10 (FPU_E, or_9_out, clke);
  and and_11 (R5_E, clke, RA_RB_E[5]);
  and and_12 (R4_E, clke, RA_RB_E[4]);
  and and_13 (R3_E, clke, RA_RB_E[3]);
  and and_14 (R2_E, clke, RA_RB_E[2]);
  and and_15 (R1_E, clke, RA_RB_E[1]);
  and and_16 (R0_E, clke, RA_RB_E[0]);
  or or_1 (or_1_out, cpu_stepper_1_step_1_3, cpu_ucode_rom_1_op_12);
  or or_2 (or_2_out, cpu_ucode_rom_1_op_11, cpu_stepper_1_step_3, RA_RB_E[14]);
  or or_3 (or_3_out, cpu_ucode_rom_1_op_10, RA_RB_E[13]);
  or or_4 (or_4_out, cpu_stepper_1_step_1_3, cpu_ucode_rom_1_op_9, RA_RB_E[12]);
  or or_5 (or_5_out, cpu_stepper_1_step_2, cpu_ucode_rom_1_op_8, RA_RB_E[11]);
  or or_6 (or_6_out, cpu_ucode_rom_1_op_6, RA_RB_E[9]);
  or or_7 (or_7_out, cpu_ucode_rom_1_op_5, RA_RB_E[8]);
  or or_8 (or_8_out, cpu_ucode_rom_1_op_4, RA_RB_E[7]);
  or or_9 (or_9_out, cpu_ucode_rom_1_op_3, RA_RB_E[6]);
  CPU_4x16_CONTROL cpu_4x16_control_1 (
    .Ch(cpu_4x16_control_1_ch), ._3(IR_IN[7]), ._2(IR_IN[6]), ._1(IR_IN[5]), ._0(IR_IN[4]), .C(C), .A(A),
    .E(E), .Z(Z), .N(N));
  and and_17 (JI, cpu_4x16_control_1_ch, and_18_out, _3);
  and and_18 (and_18_out, IR_IN[10], IR_IN[11], not_1_out, not_2_out, IR_IN[14], not_3_out);
  CPU_uCode_ROM cpu_ucode_rom_1 (
    .op(Ae), .op_2(Be), .op_3(cpu_ucode_rom_1_op_3), .op_4(cpu_ucode_rom_1_op_4),
    .op_5(cpu_ucode_rom_1_op_5), .op_6(cpu_ucode_rom_1_op_6), .op_7(cpu_ucode_rom_1_op_7),
    .op_8(cpu_ucode_rom_1_op_8), .op_9(cpu_ucode_rom_1_op_9), .op_10(cpu_ucode_rom_1_op_10),
    .op_11(cpu_ucode_rom_1_op_11), .op_12(cpu_ucode_rom_1_op_12), .op_13(ALU_3), .op_14(ALU_2),
    .op_15(ALU_1), .op_16(ALU_0), .op_17(C_2), .op_18(cpu_ucode_rom_1_op_18), .op_19(cpu_ucode_rom_1_op_19),
    .op_20(cpu_ucode_rom_1_op_20), .op_21(cpu_ucode_rom_1_op_21), .op_22(cpu_ucode_rom_1_op_22),
    .op_23(cpu_ucode_rom_1_op_23), .op_24(cpu_ucode_rom_1_op_24), .op_25(cpu_ucode_rom_1_op_25),
    .op_26(cpu_ucode_rom_1_op_26), .op_27(cpu_ucode_rom_1_op_27), .op_28(cpu_ucode_rom_1_op_28),
    .op_29(STOP), .op_30(END), .op_31(As), .op_32(Bs), .f_e(f_e), .am0(IR_IN[8]), .am1(IR_IN[9]),
    .opcode(IR_IN[15:10]), .execute(execute));
  not not_1 (not_1_out, IR_IN[12]);
  not not_2 (not_2_out, IR_IN[13]);
  not not_3 (not_3_out, IR_IN[15]);
  CPU_STEPPER cpu_stepper_1 (
    .step_1_3(cpu_stepper_1_step_1_3), .step_2(cpu_stepper_1_step_2), .step_3(cpu_stepper_1_step_3),
    .f_e(f_e), .step_6(_3), .execute(execute), .clks(clks), .st(STOP), .reset(r), .clk(clk));  // open: step_4, step_5, step_7, step_8, step_9, step_10, step_11, step_12, step_13, step_14, step_15, step_1, step_17, step_18, step_1_2
  CPU_uCODE_DECODER cpu_ucode_decoder_1 (
    .op(cpu_ucode_decoder_1_op), ._2(IR_IN[5]), ._1(IR_IN[4]), ._4(IR_IN[7]), ._3(IR_IN[6]));
  CPU_uCODE_DECODER cpu_ucode_decoder_2 (
    .op(cpu_ucode_decoder_2_op), ._2(IR_IN[1]), ._1(IR_IN[0]), ._4(IR_IN[3]), ._3(IR_IN[2]));
  Multiplexer #(.enable("false"), .select(2), .width(16)) multiplexer_1 (
    .in0({16{1'b0}}), .in1(cpu_ucode_decoder_2_op), .in2(cpu_ucode_decoder_1_op), .in3({16{1'b0}}),
    .out(RA_RB_E), .sel({Ae, Be}));
  Multiplexer #(.enable("false"), .select(2), .width(16)) multiplexer_2 (
    .in0({16{1'b0}}), .in1(cpu_ucode_decoder_1_op), .in2(cpu_ucode_decoder_2_op), .in3({16{1'b0}}),
    .out(RA_RB_S), .sel({Bs, As}));
  or or_10 (or_10_out, cpu_stepper_1_step_1_3, cpu_ucode_rom_1_op_18, RA_RB_S[15]);
  or or_11 (or_11_out, cpu_stepper_1_step_1_3, cpu_ucode_rom_1_op_19, RA_RB_S[14]);
  or or_12 (or_12_out, cpu_stepper_1_step_2, cpu_ucode_rom_1_op_20, RA_RB_S[13]);
  or or_13 (or_13_out, cpu_stepper_1_step_3, cpu_ucode_rom_1_op_21, RA_RB_S[12], JI);
  or or_14 (or_14_out, cpu_ucode_rom_1_op_22, RA_RB_S[11]);
  or or_15 (or_15_out, cpu_ucode_rom_1_op_23, RA_RB_S[10]);
  or or_16 (or_16_out, cpu_ucode_rom_1_op_25, RA_RB_S[9]);
  or or_17 (or_17_out, cpu_ucode_rom_1_op_26, RA_RB_S[8]);
  or or_18 (or_18_out, cpu_ucode_rom_1_op_27, RA_RB_S[7]);
  or or_19 (or_19_out, cpu_ucode_rom_1_op_28, RA_RB_S[6]);
  and and_19 (MAR_S, or_10_out, clks);
  and and_20 (ACC_S, or_11_out, clks);
  and and_21 (IR_S, or_12_out, clks);
  and and_22 (IAR_S, or_13_out, clks);
  and and_23 (CNTRL_S, or_14_out, clks);
  and and_24 (TMP_S, or_15_out, clks);
  and and_25 (R6_TMP_S, cpu_ucode_rom_1_op_24, clks);
  and and_26 (FLAGS_S, or_16_out, clks);
  and and_27 (STACK_S, or_17_out, clks);
  and and_28 (INDEX_S, or_18_out, clks);
  and and_29 (FPU_S, or_19_out, clks);
  and and_30 (R5_S, RA_RB_S[5], clks);
  and and_31 (R4_S, RA_RB_S[4], clks);
  and and_32 (R3_S, RA_RB_S[3], clks);
  and and_33 (R2_S, RA_RB_S[2], clks);
  and and_34 (R1_S, RA_RB_S[1], clks);
  and and_35 (R0_S, RA_RB_S[0], clks);
  // also tied to GND on the sheet: {RA_RB_E[10], RA_RB_E[15]}

  // Other names for the same wires on the sheet: ALU0 = ALU_0; ALU1 = ALU_1; ALU2 = ALU_2; ALU3 = ALU_3

  // Notes on the sheet:
  //   JUMPIF
  //   INSTRUCTION
endmodule

module CPU_CLK (
  input  clkin,
  output clk,
  output clks,
  output clke
);

  wire comparator_2_eq;
  wire [1:0] t_ff_1_q;

  T_Flip_Flop #(.trigger("falling")) t_ff_1 (.clk(clkin), .T(1'b1), .Q(t_ff_1_q[0]));  // open: Qn, preset, reset
  T_Flip_Flop t_ff_2 (.clk(clkin), .T(1'b1), .Q(t_ff_1_q[1]));  // open: Qn, preset, reset
  not not_1 (clk, t_ff_1_q[0]);
  Comparator #(.mode("unsigned"), .width(2)) comparator_1 (.a(t_ff_1_q), .b(2'b10), .eq(clks));  // open: gt, lt
  Comparator #(.mode("unsigned"), .width(2)) comparator_2 (
    .a(t_ff_1_q), .b(2'b01), .eq(comparator_2_eq));  // open: gt, lt
  not not_2 (clke, comparator_2_eq);
endmodule

module CPU_DECODER_2x4 (
  input  a,
  input  b,
  output _0,
  output _1,
  output _2,
  output _3
);

  wire not_1_out, not_2_out;

  not not_1 (not_1_out, b);
  not not_2 (not_2_out, a);
  and and_1 (_0, not_2_out, not_1_out);
  and and_2 (_1, a, not_1_out);
  and and_3 (_2, b, not_2_out);
  and and_4 (_3, b, a);
endmodule

module CPU_DECODER_2x4_WEST (
  input  a,
  input  b,
  output _0,
  output _1,
  output _2,
  output _3
);

  wire not_1_out, not_2_out;

  not not_1 (not_1_out, b);
  not not_2 (not_2_out, a);
  and and_1 (_0, not_2_out, not_1_out);
  and and_2 (_1, a, not_1_out);
  and and_3 (_2, b, not_2_out);
  and and_4 (_3, b, a);
endmodule

module CPU_DECODER_CNTRL_3x8 (
  input  a,
  input  b,
  input  c,
  output _0,
  output _1,
  output _2,
  output _3,
  output _4,
  output _5,
  output _6,
  output _7
);

  wire not_1_out, not_2_out, not_3_out;

  not not_1 (not_1_out, c);
  not not_2 (not_2_out, b);
  not not_3 (not_3_out, a);
  and and_1 (_0, not_3_out, not_2_out, not_1_out);
  and and_2 (_1, not_3_out, not_2_out, c);
  and and_3 (_2, not_3_out, b, not_1_out);
  and and_4 (_3, not_3_out, b, c);
  and and_5 (_4, a, not_2_out, not_1_out);
  and and_6 (_5, a, not_2_out, c);
  and and_7 (_6, a, b, not_1_out);
  and and_8 (_7, a, b, c);
endmodule

module CPU_MOTHERBOARD (
  input  CLK_IN,
  input  r,
  input  [7:0] IN1,
  input  [15:0] IN2,
  input  [15:0] IN3,
  input  W,
  output CLKL,
  output CLKE,
  output CLKS,
  output [15:0] R0,
  output [15:0] R1,
  output [15:0] R2,
  output [15:0] R3,
  output END,
  output [15:0] IR,
  output [15:0] IAR,
  output STOP,
  output [5:0] FLAGS,
  output [15:0] SP,
  output [7:0] OUT1,
  output [15:0] INDEX,
  output [15:0] FPU,
  output [15:0] OUT2,
  output [15:0] R4,
  output [15:0] OUT3,
  output [15:0] R5,
  output [7:0] OUT3_2,
  output [15:0] R6_TEMP,
  output [7:0] OUT3_3,
  output KYB_CLK,
  output DIS_CLK
);

  wire and_1_out, and_2_out, and_3_out, cpu_1_mc_2, cpu_address_decoder_1_ram, cpu_address_decoder_1_rom, EN,
       UL;
  wire [1:0] cpu_1_cntrl_bus;
  wire [3:0] cpu_1_addr_bus;
  wire [7:0] undriven;
  wire [11:0] cpu_1_addr_bus_2;
  wire [15:0] cpu_1_data_bus_out, cpu_input_device_1_bus_out, ram_1_dout, rom_1_data;
  wire [15:8] OUT1_t;

  CPU cpu_1 (
    .out_23(IR), .R6_TMP(R6_TEMP), .SP(SP), .INDEX(INDEX), .STOP(STOP), .CNTRL_BUS(cpu_1_cntrl_bus),
    .END(END), .ADDR_BUS({cpu_1_addr_bus_2, cpu_1_addr_bus}), .FU(FPU), .mc(UL), .mc_2(cpu_1_mc_2), .R0(R0),
    .clkl(CLKL), .R1(R1), .clke(CLKE), .FLAGS(FLAGS), .clks(CLKS), .R2(R2), .R3(R3),
    .DATA_BUS_OUT(cpu_1_data_bus_out), .R4(R4), .out_24(IAR), .R5(R5), .W(W), .clock(CLK_IN),
    .DATA_BUS_IN(cpu_input_device_1_bus_out), .r(r));
  and and_1 (and_1_out, CLKS, cpu_1_mc_2);
  CPU_ADDRESS_DECODER cpu_address_decoder_1 (
    .i_o(EN), .ram(cpu_address_decoder_1_ram), .rom(cpu_address_decoder_1_rom),
    .addr({cpu_1_addr_bus_2, cpu_1_addr_bus}), .mc(and_1_out));
  ROM #(.addrWidth(15), .dataWidth(16)) rom_1 (.addr({cpu_1_addr_bus_2[10:0], cpu_1_addr_bus}), .data(rom_1_data));
  CPU_INPUT_DEVICE cpu_input_device_1 (
    .bus_out(cpu_input_device_1_bus_out), .io_e(KYB_CLK), .clk_e(cpu_1_cntrl_bus[0]), .en(EN), .id(4'b0000),
    .in_addr(cpu_1_addr_bus), .r(r), .data_in({undriven, IN1}));  // open: reg_out
  CPU_OUTPUT_DEVICE cpu_output_device_1 (
    .data_out({OUT1_t, OUT1}), .io_s(DIS_CLK), .cntrl_s(cpu_1_cntrl_bus[1]), .en(EN), .id(4'b0011),
    .in_addr(cpu_1_addr_bus), .data_in(cpu_1_data_bus_out), .r(r));  // open: reg_out
  assign cpu_input_device_1_bus_out = and_2_out ? rom_1_data : 16'bz;  // Controlled_Buffer controlled_buffer_1
  and and_2 (and_2_out, cpu_address_decoder_1_rom, cpu_1_cntrl_bus[0]);
  CPU_INPUT_DEVICE cpu_input_device_2 (
    .bus_out(cpu_input_device_1_bus_out), .clk_e(cpu_1_cntrl_bus[0]), .en(EN), .id(4'b0001),
    .in_addr(cpu_1_addr_bus), .r(r), .data_in(IN2));  // open: reg_out, io_e
  // CPU_GRAPHICS_1 cpu_graphics_1_1: pin names not known; wires that end beside it: r, 4'b0100, cpu_1_addr_bus, {cpu_1_addr_bus_2, cpu_1_addr_bus}, EN, cpu_1_cntrl_bus[1], UL, OUT2, OUT3_2, OUT3_3
  RAM #(.addrWidth(15), .dataWidth(16)) ram_1 (
    .addr({cpu_1_addr_bus_2[10:0], cpu_1_addr_bus}), .we(cpu_address_decoder_1_ram),
    .clk(cpu_1_cntrl_bus[1]), .din(cpu_1_data_bus_out), .dout(ram_1_dout));
  CPU_GRAPHICS_2 cpu_graphics_2_1 (
    .rgb(OUT2), .Y(OUT3_3), .X(OUT3_2), .id(4'b0101), .in_addr(cpu_1_addr_bus), .r(r),
    .cntrl_s(cpu_1_cntrl_bus[1]), .data_in(cpu_1_data_bus_out), .en(EN), .ul(UL));
  assign cpu_input_device_1_bus_out = and_3_out ? ram_1_dout : 16'bz;  // Controlled_Buffer controlled_buffer_2
  and and_3 (and_3_out, cpu_address_decoder_1_ram, cpu_1_cntrl_bus[0]);
  // CPU_INPUT_DEVICE cpu_input_device_3: pin names not known; wires that end beside it: r, 4'b0010, cpu_1_addr_bus, EN, cpu_1_cntrl_bus[0], IN3, cpu_input_device_1_bus_out

  // Other names for the same wires on the sheet: OUT1_t[7:0] = OUT1; X1[7:0] = OUT3_2; Y1[7:0] = OUT3_3

  // Notes on the sheet:
  //   keyboard
  //   display
  //   contents of rom_1 (hex, n*v repeats v):
  //   108 fff0 c00 8000 4076*0 200 0 d000 200 0 d001 1800 d001 1800 d000 300 0 d000 4c20 1003 1600 d000
  //   d00 d001 2100 0 d000 1600 d000 d00 d001 6*0 200 0 d017 200 0 d018 1800 d018 1907 1900 1901 4170 4c40
  //   1020 c00 1024 4077 0 4c40 e7f0 4077 0 4c40 1034 4077 1 4c40 1036 6100 4807 4077 1 4c40 1036 c00 102c
  //   100 1 6110 800 d017 d00 d018 100 ffff 800 e7f0 d00 d018 4031*0 200 0 d002 200 0 d003 200 0 d004 200
  //   0 d005 200 0 d006 200 0 d007 200 0 d008 200 0 d009 200 0 d00a 200 0 d00b 200 0 d00c 200 0 d00d 200 0
  //   d00e 200 0 d00f 200 0 d010 200 0 d011 200 0 d012 200 0 d013 200 0 d014 200 0 d015 200 0 d016 101
  //   f800 100 8080 7110 fff5 1800 d016 1800 d015 1900 3100 2400 81 800 d010 1900 2400 80 800 d00f 1900
  //   3100 2400 81 800 d00e 1900 2400 80 800 d00d 1c00 d010 d014 1c00 d00f d013 1c00 d00e d012 1c00 d00d
  //   d011 5f00 d00f d011 5f00 d010 d012 1600 d011 1000 ff0 1800 d006 1600 d012 1000 ff0 1800 d007 4300
  //   d007 d006 4c70 209d 200 1 d00c 400 d00d 401 d00e 800 d00e 810 d00d 400 d00f 401 d010 800 d010 810
  //   d00f 400 d006 401 d007 800 d007 810 d006 4300 d00d d00f 4c70 20b2 400 d00d 401 d00f 800 d00f 810
  //   d00d 400 d00e 401 d010 800 d010 810 d00e 4300 d00e d010 4c60 20bc 200 1 d008 c00 20bf 200 ffff d008
  //   400 d007 401 d006 2c00 1 5d01 810 d009 1c00 d00e d00a 1c00 d00d d00b 300 1 d00c 4cb0 20e0 402 d00b
  //   2c22 8 403 d00a 3923 405 d015 7153 fff5 c00 20eb 402 d00a 2c22 8 403 d00b 3923 405 d015 7153 fff5
  //   300 0 d009 4cf0 20fb 402 d007 2c22 1 403 d009 2523 830 d009 c00 2110 402 d007 2c22 1 403 d009 2523
  //   402 d006 2c22 1 5d32 820 d009 402 d00a 403 d008 2523 830 d00a 407 d00f 404 d00d 4174 4c40 211b 4600
  //   d00d c00 20cb d00 d016 3811*0 400 fff0 b07 4407 4801 5400 4011 0 4c40 300c c00 3000 6800 0 0 0 770
  //   800 fff3 4407 4801 5400 4011 0 4c40 301c c00 3010 6800
  //   spare
  //   graphics 2
  //   spare
  //   graphics 1
endmodule

module CPU_CARRY_TEMP (
  input  c,
  input  r,
  input  s,
  output o
);

  CPU_MEM_1 cpu_mem_1_1 (.out_4(o), .in_1(c), .in_2(s), .r(r));
endmodule

module LOAD_256_COUNT (
  input  clk,
  input  LOAD,
  input  reset,
  output [7:0] count,
  output carry
);

  wire and_1_out;
  wire [7:0] undriven;

  Counter #(.trigger("falling")) counter_1 (
    .D(undriven), .count(1'b1), .Q(count), .carry(carry), .clk(and_1_out), .clr(reset));  // open: load
  and and_1 (and_1_out, LOAD, clk);
endmodule

module CPU_DELAY (
  input  [7:0] i,
  input  clk,
  output [7:0] o
);

  wire undriven;

  Counter #(.ongoal("stay"), .trigger("falling")) counter_1 (
    .load(1'b1), .D(i), .count(undriven), .Q(o), .clk(clk));  // open: carry, clr
endmodule

module CPU_TOP_TEMP (
  input  clock
);

  wire and_1_out, C, cpu_accumulator_1_p1, cpu_accumulator_1_p3, cpu_accumulator_1_p4, cpu_alu_1_p4,
       cpu_alu_1_p5, cpu_alu_1_p6, cpu_alu_1_p8, cpu_alu_1_p9, cpu_alu_1_p10, cpu_alu_1_p11,
       cpu_carry_temp_1_o, cpu_clk_1_p2, cpu_clk_1_p3, cpu_clk_1_p4, cpu_control_section_1_p13,
       cpu_control_section_1_p18, cpu_control_section_1_p19, cpu_control_section_1_p20,
       cpu_control_section_1_p21, cpu_control_section_1_p22, cpu_control_section_1_p23,
       cpu_control_section_1_p24, cpu_control_section_1_p25, cpu_control_section_1_p26,
       cpu_control_section_1_p27, cpu_control_section_1_p28, cpu_control_section_1_p29,
       cpu_control_section_1_p30, cpu_control_section_1_p31, cpu_control_section_1_p32, cpu_flags_1_p5,
       cpu_flags_1_p6, cpu_flags_1_p7, cpu_flags_1_p8, cpu_flags_1_p9, TMP;
  wire [7:0] cpu_ram_256_1__56, cpu_tmp_1_p1;
  wire [15:0] cpu_bus_1_1_o, cpu_tmp_1_p2;

  // CPU_TMP cpu_tmp_1: pin names not known; wires that end beside it: cpu_tmp_1_p1, cpu_tmp_1_p2, TMP
  // CPU_ACCUMULATOR cpu_accumulator_1: pin names not known; wires that end beside it: cpu_accumulator_1_p1, cpu_tmp_1_p1, cpu_accumulator_1_p3, cpu_accumulator_1_p4
  CPU_BUS_1 cpu_bus_1_1 (.o(cpu_bus_1_1_o), .bus_1(cpu_control_section_1_p13), .i(cpu_tmp_1_p2));
  and and_1 (and_1_out, cpu_carry_temp_1_o, C);
  // CPU_ALU cpu_alu_1: pin names not known; wires that end beside it: cpu_tmp_1_p1, cpu_accumulator_1_p1, cpu_bus_1_1_o, cpu_alu_1_p4, cpu_alu_1_p5, cpu_alu_1_p6, and_1_out, cpu_alu_1_p8, cpu_alu_1_p9, cpu_alu_1_p10, cpu_alu_1_p11
  // CPU_CLK cpu_clk_1: pin names not known; wires that end beside it: clock, cpu_clk_1_p2, cpu_clk_1_p3, cpu_clk_1_p4
  CPU_CARRY_TEMP cpu_carry_temp_1 (.o(cpu_carry_temp_1_o), .c(cpu_flags_1_p5), .s(TMP));  // open: r
  // CPU_FLAGS cpu_flags_1: pin names not known; wires that end beside it: cpu_alu_1_p8, cpu_alu_1_p9, cpu_alu_1_p10, cpu_alu_1_p11, cpu_flags_1_p5, cpu_flags_1_p6, cpu_flags_1_p7, cpu_flags_1_p8, cpu_flags_1_p9, cpu_flags_1_p9
  // CPU_CONTROL_SECTION cpu_control_section_1: pin names not known; wires that end beside it: cpu_flags_1_p9, cpu_alu_1_p4, cpu_alu_1_p5, cpu_alu_1_p6, cpu_clk_1_p2, cpu_clk_1_p3, cpu_clk_1_p4, cpu_flags_1_p5, cpu_flags_1_p6, cpu_flags_1_p7, cpu_flags_1_p8, cpu_flags_1_p9, cpu_control_section_1_p13, TMP, cpu_accumulator_1_p3, C, cpu_accumulator_1_p4, cpu_control_section_1_p18, cpu_control_section_1_p19, cpu_control_section_1_p20, cpu_control_section_1_p21, cpu_control_section_1_p22, cpu_control_section_1_p23, cpu_control_section_1_p24, cpu_control_section_1_p25, cpu_control_section_1_p26, cpu_control_section_1_p27, cpu_control_section_1_p28, cpu_control_section_1_p29, cpu_control_section_1_p30, cpu_control_section_1_p31, cpu_control_section_1_p32
  // CPU_R cpu_r_1: pin names not known; wires that end beside it: cpu_tmp_1_p1, cpu_control_section_1_p18, cpu_tmp_1_p1, cpu_control_section_1_p19
  // CPU_R cpu_r_2: pin names not known; wires that end beside it: cpu_tmp_1_p1, cpu_control_section_1_p22, cpu_tmp_1_p1, cpu_control_section_1_p23
  // CPU_IAR cpu_iar_1: pin names not known; wires that end beside it: cpu_control_section_1_p20, cpu_tmp_1_p1, cpu_control_section_1_p21, cpu_tmp_1_p1
  // CPU_R cpu_r_3: pin names not known; wires that end beside it: cpu_tmp_1_p1, cpu_control_section_1_p25, cpu_tmp_1_p1, cpu_control_section_1_p27
  // CPU_IR cpu_ir_1: pin names not known; wires that end beside it: cpu_control_section_1_p24, cpu_tmp_1_p1, cpu_control_section_1_p26
  // CPU_R cpu_r_4: pin names not known; wires that end beside it: cpu_tmp_1_p1, cpu_control_section_1_p28, cpu_tmp_1_p1, cpu_control_section_1_p29
  CPU_RAM_256 cpu_ram_256_1 (
    ._56(cpu_ram_256_1__56), ._55(cpu_ram_256_1__56), .o(cpu_tmp_1_p1), .address(cpu_tmp_1_p1),
    .i(cpu_tmp_1_p1), .s(cpu_control_section_1_p32), .e(cpu_control_section_1_p31),
    .sa(cpu_control_section_1_p30));  // open: _107, _123, _139, _155, _171, _187, _203, _219, _11, _235, _251, _27, _43, _59, _75, _91, _106, _122, _138, _154, _170, _186, _202, _218, _10, _234, _250, _26, _42, _58, _74, _90, _105, _121, _137, _153, _169, _185, _201, _217, _9, _233, _249, _25, _41, _57, _73, _89, _104, _120, _136, _152, _168, _184, _200, _216, _8, _232, _248, _24, _40, _72, _88, _103, _119, _135, _151, _167, _183, _199, _215, _7, _231, _247, _23, _39, _71, _87, _102, _118, _134, _150, _166, _182, _198, _214, _6, _230, _246, _22, _38, _54, _70, _86, _101, _117, _133, _149, _165, _181, _197, _213, _5, _229, _245, _21_2, _37, _53, _69, _85, _100, _116, _132, _148, _164, _180, _196, _212, _4, _228, _244, _20, _36, _52, _68, _84, _99, _115, _131, _147, _163, _179, _195, _211, _21, _227, _243, _19, _35, _51, _67, _83, _98, _114, _130, _146, _162, _178, _194, _210, _2, _226, _242, _18, _34, _50, _66, _82, _97, _113, _129, _145, _161, _177, _193, _209, _1, _225, _241, _17, _33, _49, _65, _81, _96, _112, _128, _144, _160, _176, _192, _208, _0, _224, _240, _16, _32, _48, _64, _80, _111, _127, _143, _159, _175, _191, _207, _223, _15, _239, _255, _31, _47, _63, _79, _95, _110, _126, _142, _158, _174, _190, _206, _222, _14, _238, _254, _30, _46, _62, _78, _94, _109, _125, _141, _157, _173, _189, _205, _221, _13, _237, _253, _29, _45, _61, _77, _93, _108, _124, _140, _156, _172, _188, _204, _220, _12, _236, _252, _28, _44, _60, _76, _92, r
endmodule

module temp (
  input  i1,
  input  i2,
  input  i3,
  output i0
);

  wire not_1_out, not_2_out, not_3_out;

  not not_1 (not_1_out, i1);
  not not_2 (not_2_out, i2);
  not not_3 (not_3_out, i3);
  and and_1 (i0, not_1_out, not_2_out, not_3_out);
endmodule

module CPU_INPUT_DEVICE (
  input  [15:0] data_in,
  input  r,
  input  clk_e,
  input  en,
  input  [3:0] id,
  input  [3:0] in_addr,
  output [15:0] reg_out,
  output [15:0] bus_out,
  output io_e
);

  wire and_1_out;
  wire [3:0] xnor_1_out;

  assign xnor_1_out = ~(id ^ in_addr);  // XNOR_Gate xnor_1, 4 bits wide
  and and_1 (and_1_out, xnor_1_out[0], xnor_1_out[1], xnor_1_out[2], xnor_1_out[3]);
  and and_2 (io_e, clk_e, en, and_1_out);
  CPU_REGISTER_16 cpu_register_16_1 (.REG(reg_out), ._0(bus_out), .i(data_in), .r(r), .s(1'b1), .e(io_e));
endmodule

module CPU_OUTPUT_DEVICE (
  input  [15:0] data_in,
  input  r,
  input  cntrl_s,
  input  en,
  input  [3:0] id,
  input  [3:0] in_addr,
  output [15:0] reg_out,
  output [15:0] data_out,
  output io_s
);

  wire and_1_out;
  wire [3:0] xnor_1_out;

  assign xnor_1_out = ~(id ^ in_addr);  // XNOR_Gate xnor_1, 4 bits wide
  and and_1 (and_1_out, xnor_1_out[0], xnor_1_out[1], xnor_1_out[2], xnor_1_out[3]);
  and and_2 (io_s, cntrl_s, en, and_1_out);
  CPU_REGISTER_16 cpu_register_16_1 (.REG(reg_out), ._0(data_out), .i(data_in), .r(r), .s(io_s), .e(1'b1));
endmodule

module CPU_STEP_MEM (
  input  in_1,
  input  in_2,
  output out_3
);

  wire nand_1_out, nand_2_out, nand_4_out;

  nand nand_1 (nand_1_out, in_1, in_2);
  nand nand_2 (nand_2_out, nand_1_out, in_2);
  nand nand_3 (out_3, nand_1_out, nand_4_out);
  nand nand_4 (nand_4_out, out_3, nand_2_out);
endmodule

module CPU_ADDRESS_DECODER (
  input  [15:0] addr,
  input  mc,
  output i_o,
  output ram,
  output rom
);

  wire and_1_out, and_2_out, not_1_out, not_2_out, not_3_out;

  and and_1 (and_1_out, addr[4], addr[5], addr[6], addr[7], addr[8], addr[9], addr[10], addr[11], addr[12], addr[13], addr[14], addr[15]);
  not not_1 (not_1_out, and_1_out);
  not not_2 (not_2_out, addr[15]);
  and and_2 (and_2_out, not_1_out, addr[15]);
  not not_3 (not_3_out, mc);
  and and_3 (i_o, and_1_out, not_3_out);
  and and_4 (ram, and_2_out, not_3_out);
  and and_5 (rom, not_2_out, not_3_out);
endmodule

module CPU_2x4_CONT (
  input  a,
  input  b,
  output [3:0] op
);

  wire not_1_out, not_2_out;

  not not_1 (not_1_out, b);
  not not_2 (not_2_out, a);
  and and_1 (op[0], not_2_out, not_1_out);
  and and_2 (op[1], a, not_1_out);
  and and_3 (op[2], b, not_2_out);
  and and_4 (op[3], b, a);
endmodule

module CPU_uCode_ROM (
  input  f_e,
  input  am0,
  input  am1,
  input  [5:0] opcode,
  input  [7:0] execute,
  output op,
  output op_2,
  output op_3,
  output op_4,
  output op_5,
  output op_6,
  output op_7,
  output op_8,
  output op_9,
  output op_10,
  output op_11,
  output op_12,
  output op_13,
  output op_14,
  output op_15,
  output op_16,
  output op_17,
  output op_18,
  output op_19,
  output op_20,
  output op_21,
  output op_22,
  output op_23,
  output op_24,
  output op_25,
  output op_26,
  output op_27,
  output op_28,
  output op_29,
  output op_30,
  output op_31,
  output op_32
);

  wire comparator_1_eq, or_1_out;
  wire [7:0] adder_1_out;
  wire [9:0] adder_2_out, rom_1_data;
  wire [31:0] rom_2_data;

  ROM #(.dataWidth(10)) rom_1 (.addr(adder_1_out), .data(rom_1_data));
  Adder adder_1 (.a({opcode, am1, am0}), .b({8{1'b0}}), .out(adder_1_out));  // open: cin, cout
  ROM #(.addrWidth(10), .dataWidth(32)) rom_2 (.addr(adder_2_out), .data(rom_2_data));
  Adder #(.width(10)) adder_2 (.a(rom_1_data), .b({2'b00, execute}), .out(adder_2_out), .cin(1'b0));  // open: cout
  Comparator #(.width(32)) comparator_1 (.a(rom_2_data), .b(32'h4), .eq(comparator_1_eq));  // open: gt, lt
  or or_1 (or_1_out, comparator_1_eq, f_e);
  Multiplexer #(.enable("false"), .width(32)) multiplexer_1 (
    .in0({32{1'b0}}), .in1(rom_2_data),
    .out({op, op_2, op_3, op_4, op_5, op_6, op_7, op_8, op_9, op_10, op_11, op_12, op_13, op_14, op_15, op_16, op_17, op_18, op_19, op_20, op_21, op_22, op_23, op_24, op_25, op_26, op_27, op_28, op_29, op_30, op_31, op_32}),
    .sel(or_1_out));

  // Notes on the sheet:
  //   contents of rom_1 (hex, n*v repeats v):
  //   0 2 6 10 1d 23 28 30 33 39 3e 46 49 4c 51 55 57 5f 66 6d 72 7a 7e 88 93 9b 9f a7 b1 bc bf c1 c3 cb
  //   d6 d8 da e0 e4 ec f6 fd 101 10b 118 11f 123 12d 13a 141 144 148 151 157 15b 163 16d 173 177 17f 189
  //   18f 193 19b 1a5 1aa 1ad 1b4 1c3 1c6 1c8 1d1 1db 1de 1e2 1eb 1f5 1f9 1fb 1fe 204 214 216 218 21a 21c
  //   21e 220 222 224 226 228 22a 231 235 23d 24a 250 254 25c 266 26c 270 278 282 286 288 28a 28c 28f 291
  //   293 295 29b 2a9 2ab 2ad 2b5 2b7 2b9 2bb 2c3
  //   UCode Compress
  //   contents of rom_2 (hex, n*v repeats v):
  //   0 8 906000 1000001 200800 8 804000 1000100 906000 204000 1000020 10004000 2000400 902000 200800 8
  //   902000 204800 1000100 2004000 1000200 892000 204800 1058080 902000 200800 902000 200800 8 906000
  //   1000100 2004000 1000001 200800 8 80000200 10002000 204000 1000001 8 906000 1000100 2004000 1000100
  //   2004000 1000001 200800 8 80004000 1000001 8 906000 1000100 2004000 80000400 200800 8 40000200
  //   10002000 204000 80000400 8 906000 1000100 2004000 1000100 2004000 80000400 200800 8 40004000
  //   80000402 8 804000 1000800 8 804000 1000100 2004000 1000800 8 40004000 1000100 2000800 8 40000800 8
  //   8092000 200040 902000 8004000 200400 804000 1000800 8 8092000 204040 800400 40000a00 10002000 200001
  //   8 8092000 204040 800400 40004000 1000100 2000800 8 8092000 204040 800400 80000800 8 8092000 200040
  //   906000 1000100 8004000 2000400 200800 8 8092000 204040 40000400 8 8092000 200040 906000 1000100
  //   2004000 1000100 8004000 2000400 200800 8 8092000 200040 80004000 1000100 2004000 1000100 8004000
  //   2000400 80082000 200002 8 8086000 200040 1000100 906000 1000020 10004000 2000400 8 8086000 1000001
  //   200040 8 8086000 200040 1000100 40004000 1000020 10004000 2000400 8 8086000 200040 1000100 40004000
  //   1000020 10004000 2000400 40082000 200001 8 906000 1000100 2004000 1000100 204000 1000020 10004000
  //   2000400 902000 200800 8 80000100 2000001 8 0 8 0 8 8092000 204040 80000400 40000002 8086000 1000001
  //   200040 8 906000 1000100 200010 20106000 1000010 20004000 1000200 200800 20d2000 200400 8 0 8 0 8
  //   906000 200800 1000200 8000a080 200001 8 80000200 4000a080 200001 8 906000 200800 1000100 2004000
  //   1000200 8000a080 200001 8 80004000 1000100 2004000 1000200 4000a080 200001 80004000 1102000 200400 8
  //   906000 200800 1000100 80000200 201a080 200001 8 40000200 8001a080 200001 8 906000 200800 1000100
  //   40004000 1000020 10004000 1000200 201a080 200400 8 906000 200800 1000100 40004000 1000020 10004000
  //   1000200 201a080 200400 10102000 40004000 200400 8 906000 200800 1000100 80000200 202a080 200001 8
  //   40000200 8002a080 200001 8 906000 200800 1000100 40004000 1000020 10004000 1000200 202a080 200400 8
  //   906000 200800 1000100 40004000 1000020 10004000 1000200 202a080 200400 10102000 40004000 200400 8
  //   906000 200800 1000100 2004000 103a080 200400 8 8003a080 200001 8 8003a080 40004000 200400 8 8006a080
  //   40004000 1000100 2004000 80000400 40004000 1102000 200400 8 906000 200800 1000200 8004a080 200001 8
  //   80000200 4004a080 200001 8 906000 200800 1000100 2004000 1000200 8004a080 200001 8 80004000 1000100
  //   2004000 1000200 4004a080 200001 80004000 1102000 200400 8 906000 200800 1000200 8005a080 200001 8
  //   80000200 4005a080 200001 8 906000 200800 1000100 2004000 1000200 8005a080 200001 8 80004000 1000100
  //   2004000 1000200 4005a080 200001 80004000 1102000 200400 8 906000 200800 1000200 8006a080 200001 8
  //   80000200 4006a080 200001 8 906000 200800 1000100 2004000 1000200 8006a080 200001 8 80004000 1000100
  //   2004000 1000200 4006a080 200001 80004000 1102000 200400 8 906000 200800 1000200 40078080 8 40000200
  //   8007a080 8 906000 200800 1000100 2004000 1000200 8007a080 8 902000 204800 1000100 2004000 1000200
  //   892000 204800 1000100 2004000 1078080 902000 200800 902000 200800 8 4008a080 200001 8 0 8 804000
  //   1000100 2004000 108a080 2004000 200400 902000 200800 8 80004000 1000100 2004000 1000200 4008a080
  //   200001 80004000 1102000 200400 8 4009a080 200001 8 80000200 4009a080 200001 8 804000 1000100 2004000
  //   109a080 2004000 200400 902000 200800 8 80004000 1000100 2004000 1000200 4009a080 200001 80004000
  //   1102000 200400 8 906000 200800 1000000 8 40000800 8 40004800 1000800 8 40004800 1000800 40004000
  //   1102000 200400 8 15*0 8 0 8 0 8 0 8 100080 8 0 8 0 8 0 8 4 8 0 8 0 8 0 8 40000200 804000 10da080
  //   200001 906000 200800 8 40000200 800da080 200001 8 906000 200800 1000100 2004000 1000200 400da080
  //   200001 8 906000 1000100 2004000 1000100 200010 20106000 1000010 20004000 1000200 200800 20d2000
  //   200400 8 906000 200800 1000200 800aa080 200001 8 80000200 400aa080 200001 8 906000 200800 1000100
  //   2004000 1000200 800aa080 200001 8 80004000 1000100 2004000 1000200 400a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
  //   uCode ROM
  //   Outputs
endmodule

module CPU_INC_DEC (
  input  [15:0] in,
  input  r,
  input  S,
  input  E,
  input  ID,
  output [15:0] O
);

  wire not_1_out, xor_1_out;
  wire [15:0] adder_1_out, cpu_register_16_1__0, multiplexer_1_out, multiplexer_2_out, subtractor_1_out;

  Subtractor #(.width(16)) subtractor_1 (.a(in), .b(16'h1), .out(subtractor_1_out));  // open: bin, bout
  Adder #(.width(16)) adder_1 (.a(in), .b(16'h1), .out(adder_1_out));  // open: cin, cout
  xor xor_1 (xor_1_out, ID, not_1_out);
  Multiplexer #(.enable("false"), .width(16)) multiplexer_1 (
    .in0(subtractor_1_out), .in1(adder_1_out), .out(multiplexer_1_out), .sel(not_1_out));
  // Probe on multiplexer_2_out
  Multiplexer #(.enable("false"), .width(16)) multiplexer_2 (
    .in0(in), .in1(multiplexer_1_out), .out(multiplexer_2_out), .sel(xor_1_out));
  not not_1 (not_1_out, ID);
  CPU_REGISTER_16 cpu_register_16_1 (
    ._0(cpu_register_16_1__0), .i(multiplexer_2_out), .r(r), .s(S), .e(E));  // open: REG
  assign O = E ? cpu_register_16_1__0 : 16'bz;  // Controlled_Buffer controlled_buffer_1
endmodule

module CPU_ALU_DECODER (
  input  [3:0] in_1,
  output L,
  output out_3,
  output out_4,
  output out_5,
  output out_6,
  output out_7,
  output out_8,
  output out_9,
  output out_10,
  output out_11,
  output out_12,
  output out_13,
  output out_14,
  output out_15,
  output out_16,
  output M
);

  wire not_1_out, not_2_out, not_3_out, not_4_out;

  not not_1 (not_1_out, in_1[0]);
  not not_2 (not_2_out, in_1[1]);
  not not_3 (not_3_out, in_1[2]);
  not not_4 (not_4_out, in_1[3]);
  and and_1 (L, not_4_out, not_3_out, not_2_out, not_1_out);
  and and_2 (out_3, not_4_out, not_3_out, not_2_out, in_1[0]);
  and and_3 (out_4, not_4_out, not_3_out, in_1[1], not_1_out);
  and and_4 (out_5, not_4_out, not_3_out, in_1[1], in_1[0]);
  and and_5 (out_6, not_4_out, in_1[2], not_2_out, not_1_out);
  and and_6 (out_7, not_4_out, in_1[2], not_2_out, in_1[0]);
  and and_7 (out_8, not_4_out, in_1[2], in_1[1], not_1_out);
  and and_8 (out_9, not_4_out, in_1[2], in_1[1], in_1[0]);
  and and_9 (out_10, in_1[3], not_3_out, not_2_out, not_1_out);
  and and_10 (out_11, in_1[3], not_3_out, not_2_out, in_1[0]);
  and and_11 (out_12, in_1[3], not_3_out, in_1[1], not_1_out);
  and and_12 (out_13, in_1[3], not_3_out, in_1[1], in_1[0]);
  and and_13 (out_14, in_1[3], in_1[2], not_2_out, not_1_out);
  and and_14 (out_15, in_1[3], in_1[2], not_2_out, in_1[0]);
  and and_15 (out_16, in_1[3], in_1[2], in_1[1], not_1_out);
  and and_16 (M, in_1[3], in_1[2], in_1[1], in_1[0]);
endmodule

module CPU_uCODE_DECODER (
  input  _4,
  input  _3,
  input  _2,
  input  _1,
  output [15:0] op
);

  wire not_1_out, not_2_out, not_3_out, not_4_out;

  not not_1 (not_1_out, _1);
  not not_2 (not_2_out, _2);
  not not_3 (not_3_out, _3);
  not not_4 (not_4_out, _4);
  and and_1 (op[0], not_4_out, not_3_out, not_2_out, not_1_out);
  and and_2 (op[1], not_4_out, not_3_out, not_2_out, _1);
  and and_3 (op[2], not_4_out, not_3_out, _2, not_1_out);
  and and_4 (op[3], not_4_out, not_3_out, _2, _1);
  and and_5 (op[4], not_4_out, _3, not_2_out, not_1_out);
  and and_6 (op[5], not_4_out, _3, not_2_out, _1);
  and and_7 (op[6], not_4_out, _3, _2, not_1_out);
  and and_8 (op[7], not_4_out, _3, _2, _1);
  and and_9 (op[8], _4, not_3_out, not_2_out, not_1_out);
  and and_10 (op[9], _4, not_3_out, not_2_out, _1);
  and and_11 (op[10], _4, not_3_out, _2, not_1_out);
  and and_12 (op[11], _4, not_3_out, _2, _1);
  and and_13 (op[12], _4, _3, not_2_out, not_1_out);
  and and_14 (op[13], _4, _3, not_2_out, _1);
  and and_15 (op[14], _4, _3, _2, not_1_out);
  and and_16 (op[15], _4, _3, _2, _1);
endmodule
module CPU_SHIFT (
  input  carry_in,
  input  [15:0] i,
  input  [15:0] LRcount,
  input  R,
  input  L,
  output [15:0] op,
  output carry
);

  wire not_1_out;
  wire [0:0] or_1_out;
  wire [15:0] multiplexer_1_out, multiplexer_2_out;
  wire [31:0] shifter_1_out, shifter_2_out;

  or or_1 (or_1_out[0], R, not_1_out);
  not not_1 (not_1_out, L);
  Multiplexer #(.enable("false"), .select(2), .width(16)) multiplexer_1 (
    .in0({16{1'b0}}), .in1({16{1'b0}}), .in2(16'h8000), .in3(16'h1), .out(multiplexer_1_out),
    .sel({carry_in, or_1_out[0]}));
  Shifter #(.shift("rl"), .width(32)) shifter_1 (
    .in({multiplexer_1_out, i}), .\dist (LRcount[4:0]), .out(shifter_1_out));
  Shifter #(.shift("rr"), .width(32)) shifter_2 (
    .in({multiplexer_1_out, i}), .\dist (LRcount[4:0]), .out(shifter_2_out));
  Multiplexer #(.enable("false"), .width(32)) multiplexer_2 (
    .in0(shifter_1_out), .in1(shifter_2_out), .out({multiplexer_2_out, op}), .sel(or_1_out[0]));
  or or_2 (carry, multiplexer_2_out[15], multiplexer_2_out[14], multiplexer_2_out[13], multiplexer_2_out[12], multiplexer_2_out[11], multiplexer_2_out[10], multiplexer_2_out[9], multiplexer_2_out[8], multiplexer_2_out[7], multiplexer_2_out[6], multiplexer_2_out[5], multiplexer_2_out[4], multiplexer_2_out[3], multiplexer_2_out[2], multiplexer_2_out[1], multiplexer_2_out[0]);

  // Notes on the sheet:
  //   Left = 0
endmodule

module CPU_4x16_CONTROL (
  input  _3,
  input  C,
  input  _2,
  input  A,
  input  _1,
  input  _0,
  input  E,
  input  Z,
  input  N,
  output Ch
);

  wire and_1_out, and_2_out, and_3_out, and_4_out, and_5_out, and_6_out, and_7_out, and_8_out, and_9_out,
       and_10_out, and_11_out, and_12_out, and_13_out, and_14_out, and_15_out, and_16_out, and_17_out,
       and_18_out, and_19_out, and_20_out, and_21_out, and_22_out, and_23_out, and_24_out, and_25_out,
       and_26_out, and_27_out, and_28_out, and_29_out, and_30_out, and_31_out, ANG, NC, NE, not_6_out,
       not_7_out, not_8_out, not_9_out, NZ, or_2_out, or_3_out, P;

  not not_1 (NC, C);
  not not_2 (ANG, A);
  not not_3 (NE, E);
  not not_4 (NZ, Z);
  not not_5 (P, N);
  not not_6 (not_6_out, _0);
  not not_7 (not_7_out, _1);
  not not_8 (not_8_out, _2);
  not not_9 (not_9_out, _3);
  and and_1 (and_1_out, not_9_out, not_8_out, not_7_out, not_6_out);
  and and_2 (and_2_out, not_9_out, not_8_out, not_7_out, _0);
  and and_3 (and_3_out, not_9_out, not_8_out, _1, not_6_out);
  and and_4 (and_4_out, not_9_out, not_8_out, _1, _0);
  and and_5 (and_5_out, not_9_out, _2, not_7_out, not_6_out);
  and and_6 (and_6_out, not_9_out, _2, not_7_out, _0);
  and and_7 (and_7_out, not_9_out, _2, _1, not_6_out);
  and and_8 (and_8_out, not_9_out, _2, _1, _0);
  and and_9 (and_9_out, _3, not_8_out, not_7_out, not_6_out);
  and and_10 (and_10_out, _3, not_8_out, not_7_out, _0);
  and and_11 (and_11_out, _3, not_8_out, _1, not_6_out);
  and and_12 (and_12_out, _3, not_8_out, _1, _0);
  and and_13 (and_13_out, _3, _2, not_7_out, not_6_out);
  and and_14 (and_14_out, _3, _2, not_7_out, _0);
  and and_15 (and_15_out, _3, _2, _1, not_6_out);
  and and_16 (and_16_out, _3, _2, _1, _0);
  and and_17 (and_17_out, and_2_out, C);
  and and_18 (and_18_out, and_3_out, A);
  and and_19 (and_19_out, and_4_out, C, A);
  and and_20 (and_20_out, and_5_out, E);
  or or_1 (Ch, and_17_out, and_18_out, and_19_out, and_20_out, and_21_out, and_22_out, and_23_out, and_24_out, and_25_out, and_26_out, and_27_out, and_28_out, and_29_out, and_30_out, and_31_out);
  and and_21 (and_21_out, and_6_out, C, E);
  and and_22 (and_22_out, and_7_out, or_2_out);
  or or_2 (or_2_out, A, E);
  and and_23 (and_23_out, and_8_out, or_3_out);
  or or_3 (or_3_out, E, ANG);
  and and_24 (and_24_out, and_9_out, Z);
  and and_25 (and_25_out, and_10_out, NZ, N);
  and and_26 (and_26_out, and_11_out, E, Z);
  and and_27 (and_27_out, and_12_out, NE);
  and and_28 (and_28_out, and_13_out, NZ, P);
  and and_29 (and_29_out, and_14_out, NC);
  and and_30 (and_30_out, and_15_out, NZ);
  and and_31 (and_31_out, and_16_out, NE, ANG);

  // Notes on the sheet:
  //   N/A
  //   JC
  //   JAGT
  //   JCA - spare
  //   JE
  //   JCE - spare
  //   JAGE
  //   JALE
  //   JZ
  //   JMIN
  //   JEZ - spare
  //   JNE
  //   JPOS
  //   JNC
  //   JNZ
  //   JALT
  //   Jump if A = B
  //   not used
  //   Jump if A is Greater or Equal
  //   Jump if A is Less or Equal
  //   Jump if Zero
  //   Jump if MInuS
  //   not used
  //   Jump if Not Equal
  //   Jump if POSitive
  //   Jump if Not Carry
  //   Jump if Not Zero
  //   Jump if A is Less Than
endmodule

module CPU_GRAPHICS_1 (
  input  r,
  input  mc,
  input  clk_s,
  input  en,
  input  [3:0] id,
  input  [3:0] in_addr,
  input  ul,
  output [7:0] X1,
  output [7:0] Y1,
  output [15:0] rgb1
);

  wire and_1_out, and_2_out, and_3_out, and_4_out, clk, comparator_1_eq, counter_1_carry, counter_2_carry,
       d_ff_1_q, not_1_out, not_2_out;
  wire [3:0] xnor_1_out;
  wire [7:0] counter_1_q, counter_2_q;
  wire [15:0] counter_3_q, rom_1_data;

  Clock u_CLK (.out(clk));
  Counter counter_1 (.Q(counter_1_q), .carry(counter_1_carry), .clk(and_1_out), .clr(r));  // open: load, D, count
  and and_1 (and_1_out, clk, d_ff_1_q, not_1_out);
  not not_1 (not_1_out, and_2_out);
  and and_2 (and_2_out, counter_1_carry, counter_2_carry);
  assign xnor_1_out = ~(id ^ in_addr);  // XNOR_Gate xnor_1, 4 bits wide
  Comparator #(.mode("unsigned")) comparator_1 (.a(counter_1_q), .b({8{1'b0}}), .eq(comparator_1_eq));  // open: gt, lt
  Counter #(.ongoal("stay")) counter_2 (
    .Q(counter_2_q), .carry(counter_2_carry), .clk(comparator_1_eq));  // open: load, D, count, clr
  Counter #(.max('hffff), .width(16)) counter_3 (
    .Q(counter_3_q), .clk(and_1_out), .clr(r));  // open: load, D, count, carry
  and and_3 (and_3_out, xnor_1_out[0], xnor_1_out[1], xnor_1_out[2], xnor_1_out[3]);
  and and_4 (and_4_out, clk_s, en, and_3_out);
  ROM #(.addrWidth(16), .dataWidth(16)) rom_1 (.addr(counter_3_q), .data(rom_1_data));
  not not_2 (not_2_out, ul);
  assign X1 = d_ff_1_q ? counter_1_q : 8'bz;  // Controlled_Buffer controlled_buffer_1
  assign Y1 = d_ff_1_q ? counter_2_q : 8'bz;  // Controlled_Buffer controlled_buffer_2
  assign rgb1 = d_ff_1_q ? rom_1_data : 16'bz;  // Controlled_Buffer controlled_buffer_3
  D_Flip_Flop #(.trigger("falling")) d_ff_1 (
    .clk(and_4_out), .D(not_2_out), .Q(d_ff_1_q), .reset(ul));  // open: Qn, preset

  // Notes on the sheet:
  //   contents of rom_1 (hex, n*v repeats v):
  //   compressed eJzkfUm26zqObZ+jUFstq6CK4ViSNf8hfKIiAJLyOfe+F5GZ67+Iy6PKsizujYogGKdt7+/0X/e+
  //   1kjNEfclNQc019od143NFs5l2LpzmaCJe3d+UnMt+zs1x7ube9yOPeyFBf4cuHcd3d5fn/RnGNPf
  //   ++hSc5omXXQPZxiG/rMOZzdM6e90dqm5pIncwLkb/s7p73qF1Hw6bnZu0rfcK/yd09/j06Xmxiak
  //   T8AWNnQCmp0buGEnd4Wt9D2zPMrAjTw/NQF/FjYz/m56H+dn3btx73UHmjBu9BrkdeErWeT1x0jv
  //   NvXBgn0QqA+u3AcffP25Dz7YB/s7bPRF6f3hnSO9+plePRz9yN8bD+OLhzcODW516/Or5/cf6P2P
  //   /P5jL6/LvvrdvfmQ33z3+OZzPxYv27/nLr/nYN/zw8sed33PofWetTvl1570G2f6dfzTdv1pdnea
  //   8FcG/SWRfva4e8DB1kWXhPvWn60vxb2ZKd3mvhJK4TmxWfAAAhp2N9pd6VuWPqM2KH7pBWwF9L6/
  //   kiivpKR/gl5A6FnmT8z8pYW6IKh7fWX83BvUhS+oU8IbwAXti61n/tZ0Tg/WAuFML7HxiZAFQKcC
  //   gBqDkukMT9JAUUrvmYEqaNX+oS5ZtJMCHsF72J5qCgl8Ze/LdlJDPlAn8X3haxbhzXHkJu8mXmG3
  //   2bOX/z3chJUfr/Gj16Kvg2wdIGSOTsXNZ0knQJag0Bl7fq2N7mdGIgysvAk/ynuh1cKsMh3ucHKv
  //   tsPDU68XHR6yML2OZh8LB/XiX/Rs+hqR/GvuWSf0s+JF2GgfznX32v4Mpj8tP7UHN+q82FPP5a6i
  //   /lplK33QCk5g79hm75119qBSNRS9ubP2ZgEGvThxb46OvihHpUu3msN45W5v9EBkUGSuS9tsvkS3
  //   P3F4XKV/L+7f6fWtf1eWsdy/35X6WvVvg7LaxcHsOrZ2m1f+jpW2g6mBY/l1EAb2vtKTfNR2ubzT
  //   eLKtdnsEvBwCpEvwsJJ6zX1GrPwEg4pXU9CzjLfW3Q1IuUUM7IwUUqmMGZIFs+rPTvR+jYxgkWGl
  //   ewEKkrTjXCreZCw8gSJ4UHQPoAAhbkBR4CGb2GznBdvVtcYtZG7uvJ8M7VLwDnND5g7LD7z0Zrbl
  //   JUreBi9bFuAzJece7GF+8fSywxc2TvLiRYWGlp3DL35/29cdxKye+0qEGq0nqi8Yq9s0rd5wXVKK
  //   0BZjUpc0ewPpgKajEoCbwMe+eUOVRRQLQWp1wFNfmW6Chu43xp56KP4oL5NV4HuoVIV0/xsfAR7G
  //   a5XKTiTTOYC9Xjgl8K4GNreH2FuBge8h/Wbzq/xPQ3CgEEAEwk9bfvHTWBVUP40hh5ofZQKcSDhe
  //   d32T9sV+lA5gdOIuNZdu5SdHHZ/sryOgETYTAtn1ArLja4xnxU5vHAPS0p/0di5xfxh8YGCndwwS
  //   m2SxSOVdXm9vhDRsDSt9xMDwftqC6xb6olVUQnqEzWzzg3ETHHzhZzW1/wEYzi+J3u1OQCMpQwiv
  //   xQ/2FeF64s5ftfNr91M7/yhxHVC8I5rW6Z3e5PjaumnYYuL9/JJmeYVhWwbcombp6cCQ/m5DN77e
  //   Q+qT9GdMp8bXOYbUTMki/aTmlZq5x+21H/fXlL5hhEPpz5w+Ng3zHKZhmTvT7EukJl22b7D9hmaL
  //   0M24s8gJuTIdgI+ueMNk+47UBNxKj7WnL13oAVJDT/oZ4ZnSA3fDlhp8dNwaNvwt6U/6mfAbubG7
  //   idXDa8P3Yl8OXpQecUnNuXbbuQ6kkUhS+c5UhTKO2Jlh+hqzWZeiM4NR3aSr0w236XN3cVz2bn6f
  //   Zze+tzOM45w8grc2S2rGxe2mJtAuXJykEh/2nxy5qW45mubNzXsGSPKBEQ7kJu+m74FtuOz1DuPw
  //   Scdts3fFsWH/7GHYTzhx5mNpV45BsCBvpyt7PvvmZuYDY8/HNnNig0+4o9rsvTk6ycXLlriQGvzm
  //   CX9X+iXd9E50mofP2u3zPj6DIItzcqHHF9P6q/tmkeBiJoqE9LFtnl5dfKdHXucrhu0ekjOzoOzc
  //   PqCmPodvLmoC7sZ0EXg/n/SNsd+X9GdfB2n4wJJ8XWg6aT7SHJ9iN/Ax+rorbe3YwO5+4TOll7B9
  //   kvSHpqNmmXIz+K2khbeYdAo2SaNCc/EuHevxAJwKvIXNAZpHt21zVVdKc9TXFcf2Q67TreQs8S42
  //   q2/kROzhQFhjTAegGeAI7kzYvOnwzEevCW6rp4Y3b12D201bYZ3vnU5s8FUb/rD5Tvg8YhKwSTgk
  //   WZFwvJ/X1LVBehi1Q95B4hQemb/6oPsiNhWKK29OffYM0uGF4ios55q0BPT6At0Dv+eGBmI9122a
  //   JFPWzwDvLaHgAFDkJmJzwu6JW8Eeyyc+efczURPoGDVwKzoRj7wLDdrW9KXx5gYfdYv4vNgc0CTz
  //   E5qOmohbqzS4G9NWkkGpZ/fU9ckO4yb6Bo7hRdD9aS+Y47lJeIlDknvXAAe4CbK1dYQC2Eo3mZOl
  //   t5w3HoWta0souXg3qXU4kq5bzoPOprvjNhza13Ro34Jszys0caEtvM2GTwVb87ROYXi/wFe7k32R
  //   lANgrWtgLbRMHMLa2rNPBK9g+OZm7V4/ZjvHAu5gwL2TflzOmEyAD4SG4w6va987bg4gDWxRb1K/
  //   7nwdHTt8h1++Od503eygLE0+yh8Nuhv7AlC4lXdD+USm2aWJa4aJNMuVXgI3g2mwJ28+sPJ2Rohr
  //   1rD1ebvLKGEMdXDyguMHnlzDMsMWNmdu5j03K6Am+SR8HZ1Y9ITbStclsvCR6Jt0LJ5pK+GUDkxw
  //   Uz0/wXlqkqV4pssTPAGtxxrmY0+m4hhfoKi6fUv+wQlYXQxWvylvi9WQoGiwOv5SOHqHbNiyy3WI
  //   BkfhqFg9HEyjAIBAFRBgSTK9QUdykySlPwAyLKAgS/d828YDtQDn1nugGprQVmAAWigKCnUrSbHl
  //   iozHhCEEY4G3WUBHWyBP7NaVL75YhtHZ3h+VRm4793wtg9cCtrO73FgQG5imLQCbQhZhvGZUE26z
  //   fNRj6wKEg6NRwCxXIIRXgnCGK+E4SeaVMBunOya7eQf/6/xI87kTOcZkf92vAroUmagGiRpiNlro
  //   Ts9iFiMkLGa9O5m9V4oFC3RZzCLWspgFXXZ48XrtLOoQv6kBVQuQTLrXNjtoemz4bLJyYlbK+Xay
  //   Baw4KrFsZf3uZee+O3WwchN7kaNOmPYiRC0214ethCfodjxwoF6tYJ1xlgQogKGQmbsF495nSRoc
  //   yFaztXqcraGSobVInXsAY4A/kxwHRqCFgDidxnsk9O3vTwAEdsN7tA1hcWuI0SpQV4nR2WJxfhaj
  //   GYvBY7ErsXiyI8RiFMy25fIIcAI1qFRdUfNSg2NwCyBpAfsTmiTIwAZEQ5DEKdjlaDcu64lejViO
  //   tEUWa5bD8bYNwDZ4M6JW7qrhVaIiMmlrM7uA0eAVPsMNbEFqWPGno+En/HITGscUthAXzrg1yj2C
  //   wciQxe14tnCZVX6vUhGAmLaTbUp6PqEyqEaP54BqPeGTNEe6NHk3U8Lh8AoJnx3jM4GAmxKpgZD6
  //   VqnZRmoopCaJzsHAlTAbfyU/3YhrJT8Fsyw/4wWYlW4H+amAvXArw/SCjj9Ax6ZjBFfcgk8knux0
  //   TDCdAIeKnxB/vzuL08mANRjssjWhZ/XEEcQ3srYrG7CHAXVQ4YpNRmwhZAnAMYvYVSTmzSLUysws
  //   GOEo4TCe0iwGfYzO1aKTTxzlsaCqHoEYAWzS6DEAZVyKY50eW/q8nfRAhnJXbUVzTIA+8CVozqqR
  //   wvbrOiQhfN4O6TE3FvOBMP8RI9dgfr2cpSDBKYP5nA8wvBTzFBOYvwxCeMyHIsugwvwbMD+NgN+E  +aiOS/TNupE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
endmodule

module CPU_GRAPHICS_2 (
  input  r,
  input  [15:0] data_in,
  input  cntrl_s,
  input  en,
  input  [3:0] id,
  input  [3:0] in_addr,
  input  ul,
  output [15:0] rgb,
  output [7:0] Y,
  output [7:0] X
);

  wire and_1_out, and_2_out, and_3_out, and_4_out, and_5_out, and_6_out, and_7_out, and_8_out, j_k_ff_1_q,
       j_k_ff_1_qn, not_1_out, not_2_out;
  wire [3:0] xnor_1_out;
  wire [15:0] cpu_register_16_1_reg, cpu_register_16_2__0, cpu_register_16_2_reg, divider_1_out,
       divider_1_rem;

  assign xnor_1_out = ~(id ^ in_addr);  // XNOR_Gate xnor_1, 4 bits wide
  and and_1 (and_1_out, xnor_1_out[0], xnor_1_out[1], xnor_1_out[2], xnor_1_out[3]);
  and and_2 (and_2_out, cntrl_s, en, and_1_out);
  and and_3 (and_3_out, cntrl_s, and_2_out);
  not not_1 (not_1_out, and_3_out);
  J_K_Flip_Flop j_k_ff_1 (
    .J(1'b1), .clk(not_1_out), .K(1'b1), .Q(j_k_ff_1_q), .Qn(j_k_ff_1_qn), .preset(1'b0), .reset(1'b0));
  // Probe on cpu_register_16_1_reg
  and and_4 (and_4_out, and_3_out, j_k_ff_1_q);
  and and_5 (and_5_out, j_k_ff_1_qn, and_3_out);
  and and_6 (and_6_out, and_2_out, and_5_out);
  not not_2 (not_2_out, and_2_out);
  CPU_REGISTER_16 cpu_register_16_1 (.REG(cpu_register_16_1_reg), ._0(rgb), .i(data_in), .r(r), .s(and_6_out), .e(ul));
  and and_7 (and_7_out, and_4_out, and_2_out);
  // Probe on cpu_register_16_2_reg
  CPU_REGISTER_16 cpu_register_16_2 (
    .REG(cpu_register_16_2_reg), ._0(cpu_register_16_2__0), .i(data_in), .r(r), .s(and_7_out), .e(and_8_out));
  and and_8 (and_8_out, not_2_out, ul);
  Divider #(.mode("unsigned"), .width(16)) divider_1 (
    .a(cpu_register_16_2__0), .b(16'h100), .out(divider_1_out), .rem(divider_1_rem));  // open: upper
  Bit_Extender #(.in_width(16), .out_width(8), .\type ("zero")) bit_extender_1 (.in(divider_1_out), .out(Y));
  Bit_Extender #(.in_width(16), .out_width(8), .\type ("zero")) bit_extender_2 (.in(divider_1_rem), .out(X));

  // Notes on the sheet:
  //   Colour
  //   x , y
endmodule
